// Digital circuit System.dig as structural Verilog
module System (
  input  clk,
  input  clk_2,
  input  [7:0] in_3
);

  wire and_1_out, and_2_out, and_3_out, and_4_out, and_5_out, and_6_out, and_7_out, and_9_out, and_10_out, B,
       comparator_2_eq, comparator_3_eq, comparator_4_eq, comparator_5_eq, comparator_6_eq, comparator_7_eq,
       counter_1_ovf, d_ff_1_q, d_ff_2_nq, d_ff_3_q, E_out, H, multiplexer_1_out, multiplexer_2_out,
       nand_1_out, nor_1_out, or_1_out, processor_core_1_dm_w, processor_core_1_io_r, processor_core_1_io_w,
       \processor_core_1_σ , Q_out, t_ff_1_q, t_ff_2_q, W_out, \Φ ;
  wire [3:0] processor_core_1_st;
  wire [4:0] \processor_core_1_π ;
  wire [7:0] counter_3_out, multiplexer_3_out, not_1_out, processor_core_1_io_a, register_6_q, telnet_1_out;
  wire [11:0] div_1_q;
  wire [15:0] counter_1_out, counter_2_out, counter_4_out, Dedotated_Wam_d1, Dedotated_Wam_d2, driver_1_out,
       processor_core_1_dm_a, processor_core_1_dm_o, processor_core_1_io_o, processor_core_1_pm_a,
       processor_core_1_r_89ab, processor_core_1_r_89ab_2, processor_core_1_r_89ab_3,
       processor_core_1_r_89ab_4, processor_core_1_r_0123, processor_core_1_r_0123_2,
       processor_core_1_r_0123_3, processor_core_1_r_0123_4, processor_core_1_r_4567,
       processor_core_1_r_4567_2, processor_core_1_r_4567_3, processor_core_1_r_4567_4,
       processor_core_1_r_cdef, processor_core_1_r_cdef_2, processor_core_1_r_cdef_3,
       processor_core_1_r_cdef_4, processor_core_1_rf, register_1_q, register_2_q, register_3_q,
       register_4_q, register_5_q;
  wire [23:12] div_1_q_2;
  wire [35:0] processor_core_1_w;

  Counter #(.Bits(16)) counter_1 (.en(1'b1), .C(\Φ ), .clr(1'b0), .out(counter_1_out), .ovf(counter_1_ovf));
  Counter #(.Bits(16)) counter_2 (.en(nor_1_out), .C(\Φ ), .clr(counter_1_ovf), .out(counter_2_out));  // open: ovf
  // Probe on processor_core_1_r_0123
  // Probe on processor_core_1_r_0123_2
  // Probe on processor_core_1_r_0123_3
  // Probe on processor_core_1_r_0123_4
  // Probe on processor_core_1_r_4567
  // Probe on processor_core_1_r_4567_2
  // Probe on processor_core_1_r_4567_3
  // Probe on processor_core_1_r_4567_4
  // Probe on processor_core_1_r_89ab
  // Probe on processor_core_1_r_89ab_2
  // Probe on processor_core_1_r_89ab_3
  // Probe on processor_core_1_r_89ab_4
  // Probe on processor_core_1_r_cdef
  // Probe on processor_core_1_r_cdef_2
  // Probe on processor_core_1_r_cdef_3
  // Probe on processor_core_1_r_cdef_4
  // Probe on processor_core_1_rf
  // Probe on processor_core_1_st
  Comparator #(.Bits(16)) comparator_1 (.a({16{1'b1}}), .b(counter_1_out), .eq(B));  // open: gt, lt
  Div #(.Bits(24)) div_1 (
    .a({counter_1_out, {8{1'b0}}}), .b({{8{1'b0}}, counter_2_out}), .q({div_1_q_2, div_1_q}));  // open: r
  nor nor_1 (nor_1_out, \processor_core_1_σ , comparator_2_eq);
  RAMDualAccess #(.AddrBits(16), .isProgramMemory("true"), .Bits(16)) Dedotated_Wam (
    .str(processor_core_1_dm_w), .C(\Φ ), .ld(1'b1), .A1(processor_core_1_dm_a),
    .Din1(processor_core_1_dm_o), .A2(processor_core_1_pm_a), .D1(Dedotated_Wam_d1), .D2(Dedotated_Wam_d2));
  // Probe on processor_core_1_pm_a
  Processor_Core processor_core_1 (
    .IO_r(processor_core_1_io_r), .IO_w(processor_core_1_io_w), .DM_a(processor_core_1_dm_a),
    .DM_i(Dedotated_Wam_d1), .DM_w(processor_core_1_dm_w), .IO_i(driver_1_out), .IO_o(processor_core_1_io_o),
    .IO_a(processor_core_1_io_a), .DM_o(processor_core_1_dm_o), .PM_i(Dedotated_Wam_d2),
    .PM_a(processor_core_1_pm_a), .\Φ (\Φ ),
    .R_0123({processor_core_1_r_0123_4, processor_core_1_r_0123_3, processor_core_1_r_0123_2, processor_core_1_r_0123}),
    .R_4567({processor_core_1_r_4567_4, processor_core_1_r_4567_3, processor_core_1_r_4567_2, processor_core_1_r_4567}),
    .R_89AB({processor_core_1_r_89ab_4, processor_core_1_r_89ab_3, processor_core_1_r_89ab_2, processor_core_1_r_89ab}),
    .R_CDEF({processor_core_1_r_cdef_4, processor_core_1_r_cdef_3, processor_core_1_r_cdef_2, processor_core_1_r_cdef}),
    .RF(processor_core_1_rf), .ST(processor_core_1_st), .\Σ (\processor_core_1_σ ), .W(processor_core_1_w),
    .\Π (\processor_core_1_π ), .H(H));
  Comparator #(.Bits(36)) comparator_2 (.a(processor_core_1_w), .b({36{1'b0}}), .eq(comparator_2_eq));  // open: gt, lt
  // Probe on \processor_core_1_π 
  // Probe on div_1_q
  Button Q (.out(Q_out));
  Button W (.out(W_out));
  Button E (.out(E_out));
  Comparator #(.Bits(8)) comparator_3 (.a({8{1'b1}}), .b(processor_core_1_io_a), .eq(comparator_3_eq));  // open: gt, lt
  assign not_1_out = ~in_3;  // Not not_1, 8 bits wide
  Counter #(.Bits(8)) counter_3 (.en(1'b1), .C(clk_2), .clr(comparator_6_eq), .out(counter_3_out));  // open: ovf
  Multiplexer multiplexer_1 (.sel(and_6_out), .in_0(W_out), .in_1(t_ff_1_q), .out(multiplexer_1_out));
  D_FF d_ff_1 (.D(clk), .C(\Φ ), .Q(d_ff_1_q));  // open: nQ
  Comparator #(.Bits(16)) comparator_4 (
    .a({16{1'b0}}), .b(processor_core_1_io_o), .eq(comparator_4_eq));  // open: gt, lt
  Register #(.Bits(16)) register_1 (.D(processor_core_1_io_o), .C(\Φ ), .en(and_1_out), .Q(register_1_q));
  and and_1 (and_1_out, comparator_3_eq, processor_core_1_io_w);
  and and_2 (and_2_out, comparator_3_eq, processor_core_1_io_r);
  Comparator #(.Bits(8)) comparator_5 (.a(8'hfe), .b(processor_core_1_io_a), .eq(comparator_5_eq));  // open: gt, lt
  Comparator #(.Bits(8)) comparator_6 (.a(not_1_out), .b(counter_3_out), .eq(comparator_6_eq));  // open: gt, lt
  T_FF t_ff_1 (.T(1'b1), .C(multiplexer_1_out), .Q(t_ff_1_q));  // open: nQ
  D_FF d_ff_2 (.D(d_ff_1_q), .C(\Φ ), .nQ(d_ff_2_nq));  // open: Q
  and and_3 (and_3_out, and_1_out, comparator_4_eq);
  assign driver_1_out = and_2_out ? {16{1'b0}} : 16'bz;  // Driver driver_1
  and and_4 (and_4_out, comparator_5_eq, processor_core_1_io_w);
  and and_5 (and_5_out, comparator_5_eq, processor_core_1_io_r);
  Multiplexer multiplexer_2 (.sel(t_ff_1_q), .in_0(Q_out), .in_1(comparator_6_eq), .out(multiplexer_2_out));
  and and_6 (and_6_out, t_ff_2_q, B);
  and and_7 (and_7_out, d_ff_1_q, d_ff_2_nq);
  Register #(.Bits(16)) register_2 (.D(register_1_q), .C(\Φ ), .en(and_1_out), .Q(register_2_q));
  assign driver_1_out = and_5_out ? {telnet_1_out, {8{1'b1}}} : 16'bz;  // Driver driver_2
  and and_8 (\Φ , multiplexer_2_out, ~H);  // And
  T_FF t_ff_2 (.T(1'b1), .C(E_out), .Q(t_ff_2_q));  // open: nQ
  Counter #(.Bits(16)) counter_4 (.en(and_3_out), .C(\Φ ), .clr(and_7_out), .out(counter_4_out));  // open: ovf
  Register #(.Bits(16)) register_3 (.D(register_2_q), .C(\Φ ), .en(and_1_out), .Q(register_3_q));
  and and_9 (and_9_out, and_4_out, nand_1_out);
  Register #(.Bits(16)) register_4 (.D(counter_4_out), .C(and_7_out), .en(1'b1), .Q(register_4_q));
  D_FF d_ff_3 (.D(and_9_out), .C(\Φ ), .Q(d_ff_3_q));  // open: nQ
  Comparator #(.Bits(16)) comparator_7 (
    .a(processor_core_1_io_o), .b({16{1'b0}}), .eq(comparator_7_eq));  // open: gt, lt
  // Probe on register_4_q
  Register #(.Bits(16)) register_5 (.D(register_3_q), .C(\Φ ), .en(and_1_out), .Q(register_5_q));
  Register #(.Bits(8)) register_6 (.D(processor_core_1_io_o[7:0]), .C(\Φ ), .en(and_4_out), .Q(register_6_q));
  Multiplexer #(.Bits(8)) multiplexer_3 (
    .sel(and_4_out), .in_0(register_6_q), .in_1(processor_core_1_io_o[15:8]), .out(multiplexer_3_out));
  or or_1 (or_1_out, and_4_out, d_ff_3_q);
  nand nand_1 (nand_1_out, and_4_out, comparator_7_eq, d_ff_3_q);
  // Probe on {16{1'b0}}
  // Probe on {16{1'b0}}
  // Probe on {16{1'b0}}
  // Probe on {16{1'b0}}
  // Probe on register_5_q
  // Probe on register_3_q
  // Probe on register_2_q
  // Probe on register_1_q
  and and_10 (and_10_out, or_1_out, nand_1_out);
  Telnet telnet_1 (.in(multiplexer_3_out), .C(\Φ ), .wr(and_10_out), .rd(and_5_out), .out(telnet_1_out));  // open: av

  // Notes on the sheet:
  //   clk_2: Hz: 50000
  //   $zr
  //   $rp
  //   $v0
  //   $v1
  //   $v2
  //   $v3
  //   $a0
  //   $a1
  //   $a2
  //   $s0
  //   $s1
  //   $s2
  //   $s3
  //   $s4
  //   $fp
  //   $sp
  //   $rf
  //   $st
  //   Dynamic CPI Display
  //   Fibonaccis Per Second
endmodule
