// Digital circuit Branch Stage.dig as structural Verilog
module Branch_Stage (
  input  [15:0] W_a,
  input  [35:0] W_c,
  input  \Φ ,
  input  [3:0] S_d,
  input  S_e,
  input  [3:0] A_a,
  input  [3:0] A_b,
  input  [15:0] IM_X,
  input  [7:0] IM_LS,
  input  [15:0] D_a_2,
  input  [15:0] D_b_2,
  input  \Σ_e ,
  input  \Σ_i ,
  output [15:0] W_c_2,
  output [15:0] D_a,
  output [15:0] D_b,
  output [15:0] J_a,
  output J_e,
  output [3:0] ST,
  output [15:0] RF,
  output [3:0] A_a_2,
  output [3:0] A_b_2,
  output F_c,
  output [15:0] A_m,
  output \Σ_o ,
  output \Π_a ,
  output \Π_b 
);

  wire and_3_out, and_5_out, and_6_out, and_7_out, bitselector_1_out, bitselector_2_out, C_x,
       comparator_1_eq, comparator_2_eq, comparator_3_eq, comparator_4_eq, comparator_5_eq, F,
       multiplexer_6_out, multiplexer_8_out, multiplexer_13_out, multiplexer_19_out, multiplexer_22_out,
       nor_1_out, not_2_out, not_3_out, not_5_out, not_6_out, or_2_out, or_3_out, or_4_out, or_5_out, RF_bit,
       xor_1_out, xor_2_out, \Σ ;
  wire [0:0] multiplexer_10_out;
  wire [1:0] and_2_out, multiplexer_1_out, multiplexer_2_out;
  wire [3:0] multiplexer_7_out, multiplexer_16_out;
  wire [4:2] multiplexer_2_out_2;
  wire [15:0] add_2_s, add_4_s, bit_replace_mux_1_d_o, IM_LS_t, L_0, L_2, multiplexer_3_out,
       multiplexer_4_out, multiplexer_5_out, multiplexer_9_out, multiplexer_11_out, multiplexer_12_out,
       multiplexer_14_out, multiplexer_15_out, multiplexer_18_out, multiplexer_20_out, multiplexer_21_out,
       multiplexer_23_out, multiplexer_24_out, multiplexer_27_out, multiplexer_28_out, not_4_out;

  Comparator #(.Bits(4)) comparator_1 (.a(A_a), .b(4'b0000), .eq(comparator_1_eq));  // open: gt, lt
  Comparator #(.Bits(4)) comparator_2 (.a(A_b), .b(4'b0000), .eq(comparator_2_eq));  // open: gt, lt
  and and_1 (and_2_out[0], W_c[34], ~comparator_1_eq);  // And
  and and_2 (and_2_out[1], W_c[35], ~comparator_2_eq);  // And
  Comparator #(.Bits(6)) comparator_3 (.a(W_c[13:8]), .b(6'b011110), .eq(comparator_3_eq));  // open: gt, lt
  BitExtender bitextender_1 (.in(IM_LS), .out(IM_LS_t));
  and and_3 (and_3_out, comparator_3_eq, ~F);  // And
  Multiplexer #(.Bits(2)) multiplexer_1 (.sel(and_3_out), .in_0(and_2_out), .in_1(2'b00), .out(multiplexer_1_out));
  Multiplexer #(.Bits(5)) multiplexer_2 (
    .sel(W_c[13]), .in_0({5{1'b0}}), .in_1(W_c[12:8]), .out({multiplexer_2_out_2, multiplexer_2_out}));
  Bit_Replace_Mux bit_replace_mux_1 (.B_a(IM_LS[7:4]), .D_i(RF), .D_o(bit_replace_mux_1_d_o), .B_d(multiplexer_13_out));
  Multiplexer #(.Bits(16)) multiplexer_3 (
    .sel(multiplexer_2_out_2[3]), .in_0(D_b_2), .in_1(IM_X), .out(multiplexer_3_out));
  Multiplexer #(.Bits(16)) multiplexer_4 (
    .sel(\Σ_e ), .in_0({multiplexer_1_out, W_c[33:20]}), .in_1({16{1'b0}}), .out(multiplexer_4_out));
  or or_1 (\Σ_o , \Σ_e , \Σ_i );
  not not_1 (\Σ , \Σ_i );
  Multiplexer #(.Bits(16)) multiplexer_5 (
    .sel(multiplexer_2_out_2[2]), .in_0(bit_replace_mux_1_d_o), .in_1(multiplexer_3_out),
    .out(multiplexer_5_out));
  Register #(.Bits(4)) register_1 (.D(A_a), .C(\Φ ), .en(\Σ ), .Q(A_a_2));
  Register #(.Bits(4)) register_2 (.D(A_b), .C(\Φ ), .en(\Σ ), .Q(A_b_2));
  Register #(.Bits(16)) register_3 (.D(multiplexer_4_out), .C(\Φ ), .en(\Σ ), .Q(W_c_2));
  Register #(.Bits(16)) u_rf (.D(multiplexer_5_out), .C(\Φ ), .en(multiplexer_2_out_2[4]), .Q(RF));
  Multiplexer multiplexer_6 (.sel(W_c[19]), .in_0(bitselector_1_out), .in_1(RF_bit), .out(multiplexer_6_out));
  BitSelector #(.Selector_Bits(4)) bitselector_1 (.in(D_a_2), .sel(IM_LS[7:4]), .out(bitselector_1_out));
  and and_4 (C_x, not_3_out, W_c[19]);
  Multiplexer #(.Bits(4)) multiplexer_7 (.sel(S_e), .in_0({ST[3:1], F_c}), .in_1(S_d), .out(multiplexer_7_out));
  Multiplexer multiplexer_8 (.sel(multiplexer_2_out_2[2]), .in_0(F), .in_1(bitselector_2_out), .out(multiplexer_8_out));
  BitSelector #(.Selector_Bits(4)) bitselector_2 (.in(RF), .sel(IM_LS[3:0]), .out(bitselector_2_out));
  BitSelector #(.Selector_Bits(4)) bitselector_3 (.in(RF), .sel(IM_LS[7:4]), .out(RF_bit));
  and and_5 (and_5_out, multiplexer_8_out, RF_bit);
  or or_2 (or_2_out, multiplexer_8_out, RF_bit);
  not not_2 (not_2_out, multiplexer_8_out);
  Multiplexer #(.Bits(16)) multiplexer_9 (.sel(W_c[5]), .in_0(16'h1), .in_1({16{1'b1}}), .out(multiplexer_9_out));
  Add #(.Bits(16)) add_1 (.a(W_a), .b(16'h1), .c_i(W_c[7]), .s(L_2));  // open: c_o
  Multiplexer multiplexer_10 (
    .sel(not_3_out), .in_0(multiplexer_6_out), .in_1(multiplexer_7_out[0]), .out(multiplexer_10_out[0]));
  or or_3 (or_3_out, S_e, W_c[18]);
  not not_3 (not_3_out, W_c[18]);
  Multiplexer #(.Bits(16)) multiplexer_11 (.sel(W_c[2]), .in_0(IM_X), .in_1(IM_LS_t), .out(multiplexer_11_out));
  Multiplexer #(.Bits(16)) multiplexer_12 (
    .sel(W_c[6]), .in_0(multiplexer_9_out), .in_1({16{1'b0}}), .out(multiplexer_12_out));
  Multiplexer #(.Selector_Bits(2)) multiplexer_13 (
    .sel(multiplexer_2_out), .in_0(and_5_out), .in_1(or_2_out), .in_2(multiplexer_8_out), .in_3(not_2_out),
    .out(multiplexer_13_out));
  Multiplexer #(.Bits(16)) multiplexer_14 (
    .sel(W_c[3]), .in_0(multiplexer_11_out), .in_1({16{1'b0}}), .out(multiplexer_14_out));
  Multiplexer #(.Bits(16)) multiplexer_15 (.sel(W_c[4]), .in_0(L_0), .in_1({16{1'b0}}), .out(multiplexer_15_out));
  Add #(.Bits(16)) add_2 (.a(multiplexer_12_out), .b(D_b_2), .c_i(1'b0), .s(add_2_s));  // open: c_o
  Register #(.Bits(4)) u_st (
    .D({multiplexer_7_out[3:1], multiplexer_10_out[0]}), .C(\Φ ), .en(or_3_out), .Q({ST[3:1], F_c}));
  Add #(.Bits(16)) add_3 (.a(multiplexer_14_out), .b(multiplexer_15_out), .c_i(1'b0), .s(J_a));  // open: c_o
  and and_6 (and_6_out, W_c[5], W_c[6]);
  Comparator #(.Bits(16)) comparator_4 (.a(D_a_2), .b({16{1'b0}}), .eq(comparator_4_eq));  // open: gt, lt
  Comparator #(.Bits(16)) comparator_5 (.a(D_a_2), .b(RF), .eq(comparator_5_eq));  // open: gt, lt
  Multiplexer #(.Bits(4)) multiplexer_16 (
    .sel(or_3_out), .in_0({ST[3:1], F_c}), .in_1({multiplexer_7_out[3:1], multiplexer_10_out[0]}),
    .out(multiplexer_16_out));
  Multiplexer #(.Bits(16)) multiplexer_17 (.sel(and_6_out), .in_0(add_2_s), .in_1(W_a), .out(L_0));
  xor xor_1 (xor_1_out, multiplexer_16_out[3], multiplexer_16_out[2]);
  or or_4 (or_4_out, not_6_out, multiplexer_16_out[1]);
  or or_5 (or_5_out, multiplexer_16_out[1], xor_1_out);
  assign not_4_out = ~D_b_2;  // Not not_4, 16 bits wide
  Add #(.Bits(16)) add_4 (.a(not_4_out), .b({16{1'b0}}), .c_i(1'b1), .s(add_4_s));  // open: c_o
  Multiplexer #(.Bits(16)) multiplexer_18 (.sel(F), .in_0(D_a_2), .in_1(D_b_2), .out(multiplexer_18_out));
  Multiplexer #(.Selector_Bits(2)) multiplexer_19 (
    .sel(W_c[15:14]), .in_0(comparator_4_eq), .in_1(comparator_5_eq), .in_2(D_a_2[15]), .in_3(D_a_2[0]),
    .out(multiplexer_19_out));
  xor xor_2 (xor_2_out, multiplexer_19_out, W_c[16]);
  not not_5 (not_5_out, multiplexer_16_out[1]);
  not not_6 (not_6_out, multiplexer_16_out[0]);
  Multiplexer #(.Selector_Bits(3), .Bits(16)) multiplexer_20 (
    .sel(W_c[10:8]), .in_0(D_a_2), .in_1(D_a_2), .in_2(D_b_2), .in_3(J_a), .in_4(L_2),
    .in_5({D_b_2[7:0], D_b_2[15:8]}), .in_6(multiplexer_18_out), .in_7(add_4_s), .out(multiplexer_20_out));
  Multiplexer #(.Bits(16)) multiplexer_21 (.sel(F), .in_0(D_b_2), .in_1(D_a_2), .out(multiplexer_21_out));
  and and_7 (and_7_out, ~W_c[8], ~W_c[9], W_c[10]);  // And
  Multiplexer #(.Selector_Bits(3)) multiplexer_22 (
    .sel(W_c[16:14]), .in_0(multiplexer_16_out[0]), .in_1(multiplexer_16_out[2]),
    .in_2(multiplexer_16_out[1]), .in_3(not_5_out), .in_4(not_6_out), .in_5(or_4_out), .in_6(xor_1_out),
    .in_7(or_5_out), .out(multiplexer_22_out));
  Multiplexer #(.Bits(16)) multiplexer_23 (
    .sel(W_c[13]), .in_0(multiplexer_20_out), .in_1(RF), .out(multiplexer_23_out));
  nor nor_1 (nor_1_out, W_c[8], W_c[9], W_c[10]);
  Multiplexer #(.Selector_Bits(2), .Bits(16)) multiplexer_24 (
    .sel(W_c[12:11]), .in_0(D_a_2), .in_1(L_0), .in_2(J_a), .in_3(multiplexer_21_out),
    .out(multiplexer_24_out));
  Multiplexer multiplexer_25 (.sel(C_x), .in_0(and_7_out), .in_1(F), .out(J_e));
  Multiplexer multiplexer_26 (.sel(W_c[17]), .in_0(xor_2_out), .in_1(multiplexer_22_out), .out(F));
  Register #(.Bits(16)) register_4 (.D(J_a), .C(\Φ ), .en(\Σ ), .Q(A_m));
  Register #(.Bits(16)) register_5 (.D(multiplexer_23_out), .C(\Φ ), .en(\Σ ), .Q(D_a));
  Multiplexer #(.Bits(16)) multiplexer_27 (
    .sel(nor_1_out), .in_0(multiplexer_24_out), .in_1(D_b_2), .out(multiplexer_27_out));
  Multiplexer #(.Bits(16)) multiplexer_28 (
    .sel(W_c[13]), .in_0(multiplexer_27_out), .in_1({16{1'b0}}), .out(multiplexer_28_out));
  Register #(.Bits(16)) register_6 (.D(multiplexer_28_out), .C(\Φ ), .en(\Σ ), .Q(D_b));

  assign ST[0] = F_c;
  assign \Π_a  = W_c[0];
  assign \Π_b  = W_c[1];

  // Other names for the same wires on the sheet: D_a_t[15:0] = D_a_2; D_b_t[15:0] = D_b_2; L_1[15:0] = J_a;
  //   C_0[5:0] = W_c[7:2]; C_1[5:0] = W_c[13:8]; C_2[5:0] = W_c[19:14]

  // Notes on the sheet:
  //   W_a: Program Word Address
  //   W_c: Program Control Word
  //   Φ: Clock
  //   W_c_2: Program Control Word
  //   D_a: Port A Data
  //   D_b: Port B Data
  //   J_a: Jump Address
  //   J_e: Jump Enable
  //   S_d: Status Register Data
  //   S_e: Status Register Write Enable
  //   ST: Status Register
  //   RF: Reference Register
  //   A_a: Port A Address
  //   A_b: Port B Address
  //   A_a_2: Port A Address
  //   A_b_2: Port B Address
  //   F_c: Carry Flag
  //   IM_X: Extended Immediate
  //   IM_LS: Long/Short Immediate
  //   D_a_2: Port A Originating Data
  //   D_b_2: Port B Originating Data
  //   A_m: Memory Address
  //   Σ_e: Stall Enable
  //   Σ_i: Stall Backpropagate Input
  //   Σ_o: Stall Backpropagate Output
  //   Π_a: Forwarding Signals Lane A
  //   Π_b: Forwarding Signals Lane A
  //   C
  //   Z
  //   V
  //   S
endmodule
