// Digital circuit Execute Stage.dig as structural Verilog
module Execute_Stage (
  input  [15:0] W_c,
  input  [3:0] A_a,
  input  [15:0] D_a,
  input  [3:0] A_b,
  input  [15:0] D_b,
  input  \Φ ,
  input  F_c,
  input  [15:0] A_m_2,
  input  \Σ_e ,
  output [3:0] S_d,
  output S_e,
  output [3:0] A_a_2,
  output [15:0] D_a_2,
  output [3:0] A_b_2,
  output [15:0] D_b_2,
  output [5:0] W_c_2,
  output [15:0] A_m,
  output \Σ_o ,
  output [2:0] \Π_a ,
  output [2:0] \Π_b 
);

  wire add_1_c_o, add_2_c_o, and_2_out, and_3_out, comparator_2_eq, multiplexer_2_out, multiplexer_4_out,
       multiplexer_6_out, not_4_out, xor_2_out;
  wire [0:0] and_1_out;
  wire [5:0] multiplexer_13_out;
  wire [14:0] add_2_s, multiplexer_10_out;
  wire [15:0] barrel_shifter_1_d_o, multiplexer_1_out, multiplexer_3_out, multiplexer_5_out,
       multiplexer_7_out, multiplexer_8_out, multiplexer_9_out, multiplexer_14_out, multiplexer_15_out,
       multiplier_1_p_h, multiplier_1_p_l, not_1_out, not_2_out, not_3_out, or_1_out, xor_1_out;
  wire [15:15] add_1_s;

  assign not_1_out = ~D_b;  // Not not_1, 16 bits wide
  assign not_2_out = ~D_a;  // Not not_2, 16 bits wide
  Multiplexer #(.Bits(16)) multiplexer_1 (.sel(W_c[3]), .in_0(D_b), .in_1(not_1_out), .out(multiplexer_1_out));
  Multiplexer multiplexer_2 (.sel(W_c[4]), .in_0(F_c), .in_1(D_b[15]), .out(multiplexer_2_out));
  Comparator #(.Bits(12)) comparator_1 (.a(W_c[13:2]), .b({12{1'b0}}), .eq(\Π_a [1]));  // open: gt, lt
  Multiplexer #(.Bits(16)) multiplexer_3 (.sel(W_c[2]), .in_0(D_a), .in_1(not_2_out), .out(multiplexer_3_out));
  and and_1 (and_1_out[0], W_c[3], multiplexer_2_out);
  and and_2 (and_2_out, W_c[3], W_c[4], W_c[5]);
  Multiplexer multiplexer_4 (.sel(W_c[5]), .in_0(W_c[4]), .in_1(F_c), .out(multiplexer_4_out));
  assign or_1_out = multiplexer_3_out | multiplexer_1_out;  // Or or_1, 16 bits wide
  assign xor_1_out = multiplexer_3_out ^ multiplexer_1_out;  // XOr xor_1, 16 bits wide
  Add add_1 (.a(multiplexer_3_out[15]), .b(multiplexer_1_out[15]), .c_i(add_2_c_o), .s(add_1_s[15]), .c_o(add_1_c_o));
  Add #(.Bits(15)) add_2 (
    .a(multiplexer_3_out[14:0]), .b(multiplexer_1_out[14:0]), .c_i(multiplexer_4_out), .s(add_2_s),
    .c_o(add_2_c_o));
  Multiplexer #(.Bits(16)) multiplexer_5 (.sel(W_c[4]), .in_0(or_1_out), .in_1(xor_1_out), .out(multiplexer_5_out));
  Barrel_Shifter barrel_shifter_1 (.D_i(D_a), .S(D_b[3:0]), .D_o(barrel_shifter_1_d_o), .C(W_c[3:2]));
  Multiplier multiplier_1 (.P_L(multiplier_1_p_l), .D_B(D_b), .D_A(D_a), .P_H(multiplier_1_p_h), .C(W_c[2]));
  assign not_3_out = ~multiplexer_5_out;  // Not not_3, 16 bits wide
  Multiplexer multiplexer_6 (.sel(W_c[2]), .in_0(D_b[15]), .in_1(D_b[0]), .out(multiplexer_6_out));
  xor xor_2 (xor_2_out, add_1_c_o, add_2_c_o);
  Multiplexer #(.Bits(16)) multiplexer_7 (
    .sel(W_c[5]), .in_0(multiplexer_5_out), .in_1(not_3_out), .out(multiplexer_7_out));
  Multiplexer #(.Bits(16)) multiplexer_8 (
    .sel(W_c[2]), .in_0({D_b[14:0], and_1_out[0]}), .in_1({and_1_out[0], D_b[15:1]}), .out(multiplexer_8_out));
  Multiplexer #(.Bits(16)) multiplexer_9 (
    .sel(and_2_out), .in_0(barrel_shifter_1_d_o), .in_1(multiplier_1_p_l), .out(multiplexer_9_out));
  Comparator #(.Bits(16)) comparator_2 (.a(multiplier_1_p_h), .b({16{1'b0}}), .eq(comparator_2_eq));  // open: gt, lt
  Multiplexer #(.Selector_Bits(2), .Bits(16)) multiplexer_10 (
    .sel(W_c[7:6]), .in_0({add_1_s[15], add_2_s}), .in_1(multiplexer_7_out), .in_2(multiplexer_8_out),
    .in_3(multiplexer_9_out), .out({S_d[2], multiplexer_10_out}));
  not not_4 (not_4_out, comparator_2_eq);
  Comparator #(.Bits(16)) comparator_3 (.a({S_d[2], multiplexer_10_out}), .b({16{1'b0}}), .eq(S_d[1]));  // open: gt, lt
  and and_3 (and_3_out, W_c[6], W_c[7]);
  Multiplexer multiplexer_11 (.sel(W_c[7]), .in_0(add_1_c_o), .in_1(multiplexer_6_out), .out(S_d[0]));
  Multiplexer multiplexer_12 (.sel(and_3_out), .in_0(xor_2_out), .in_1(not_4_out), .out(S_d[3]));
  Multiplexer #(.Bits(6)) multiplexer_13 (.sel(\Σ_e ), .in_0(W_c[15:10]), .in_1({6{1'b0}}), .out(multiplexer_13_out));
  Multiplexer #(.Bits(16)) multiplexer_14 (
    .sel(W_c[8]), .in_0(D_a), .in_1({S_d[2], multiplexer_10_out}), .out(multiplexer_14_out));
  Multiplexer #(.Bits(16)) multiplexer_15 (.sel(W_c[9]), .in_0(D_b), .in_1(multiplier_1_p_h), .out(multiplexer_15_out));
  Register #(.Bits(4)) register_1 (.D(A_a), .C(\Φ ), .en(1'b1), .Q(A_a_2));
  Register #(.Bits(4)) register_2 (.D(A_b), .C(\Φ ), .en(1'b1), .Q(A_b_2));
  Register #(.Bits(16)) register_3 (.D(multiplexer_14_out), .C(\Φ ), .en(1'b1), .Q(D_a_2));
  Register #(.Bits(16)) register_4 (.D(multiplexer_15_out), .C(\Φ ), .en(1'b1), .Q(D_b_2));
  Register #(.Bits(16)) register_5 (.D(A_m_2), .C(\Φ ), .en(1'b1), .Q(A_m));
  Register #(.Bits(6)) register_6 (.D(multiplexer_13_out), .C(\Φ ), .en(1'b1), .Q(W_c_2));

  assign S_e = W_c[8];
  assign {\Π_a [2], \Π_a [0]} = {W_c[0], W_c[14]};
  assign \Π_b  = {W_c[1], \Π_a [1], W_c[15]};
  assign \Σ_o  = \Σ_e ;

  // Notes on the sheet:
  //   W_c: Program Control Word
  //   A_a: Port A Address
  //   D_a: Port A Data
  //   A_b: Port B Address
  //   D_b: Port B Data
  //   S_d: Status Register Data
  //   S_e: Status Register Write Enable
  //   A_a_2: Port A Address
  //   D_a_2: Port A Data
  //   A_b_2: Port B Address
  //   D_b_2: Port B Data
  //   W_c_2: Program Control Word
  //   Φ: Clock
  //   F_c: Carry Flag Return
  //   A_m: Memory Address
  //   A_m_2: Memory Address
  //   Σ_e: Stall Enable
  //   Σ_o: Stall Backpropagate Output
  //   Π_a: Forwarding Signals Lane A
  //   Π_b: Forwarding Signals Lane A
endmodule
