// Digital circuit Memory Stage New.dig as structural Verilog
module Memory_Stage_New (
  input  [15:0] D_a,
  input  [15:0] D_b,
  input  [15:0] IO_i,
  input  [5:0] W_c,
  input  \Φ ,
  input  [3:0] A_a_2,
  input  [3:0] A_b_2,
  input  [15:0] A_m,
  input  [15:0] DM_i,
  output [15:0] D_a_2,
  output [15:0] D_b_2,
  output IO_r,
  output IO_w,
  output [1:0] W_c_2,
  output [3:0] A_a,
  output [3:0] A_b,
  output [1:0] \Π_a ,
  output [1:0] \Π_b ,
  output DM_w,
  output [15:0] DM_a
);

  wire [15:0] multiplexer_1_out, multiplexer_2_out, multiplexer_3_out;

  Multiplexer #(.Bits(16)) multiplexer_1 (.sel(W_c[2]), .in_0(DM_i), .in_1(IO_i), .out(multiplexer_1_out));
  Multiplexer #(.Bits(16)) multiplexer_2 (.sel(W_c[3]), .in_0({16{1'b0}}), .in_1({16{1'b1}}), .out(multiplexer_2_out));
  Multiplexer #(.Bits(16)) multiplexer_3 (.sel(W_c[0]), .in_0(D_a), .in_1(multiplexer_1_out), .out(multiplexer_3_out));
  Comparator #(.Bits(4)) comparator_1 (.a(W_c[3:0]), .b(4'b0000), .eq(\Π_a [1]));  // open: gt, lt
  Add #(.Bits(16)) add_1 (.a(A_m), .b(multiplexer_2_out), .c_i(1'b0), .s(DM_a));  // open: c_o
  Register #(.Bits(16)) register_1 (.D(multiplexer_3_out), .C(\Φ ), .en(1'b1), .Q(D_a_2));
  Register #(.Bits(2)) register_2 (.D(W_c[5:4]), .C(\Φ ), .en(1'b1), .Q(W_c_2));
  and and_1 (IO_r, W_c[2], W_c[0]);
  and and_2 (IO_w, W_c[2], W_c[1]);
  and and_3 (DM_w, ~W_c[2], W_c[1]);  // And
  Register #(.Bits(4)) register_3 (.D(A_a_2), .C(\Φ ), .en(1'b1), .Q(A_a));
  Register #(.Bits(4)) register_4 (.D(A_b_2), .C(\Φ ), .en(1'b1), .Q(A_b));
  Register #(.Bits(16)) register_5 (.D(D_b), .C(\Φ ), .en(1'b1), .Q(D_b_2));

  assign \Π_a [0] = W_c[4];
  assign \Π_b  = {1'b1, W_c[5]};

  // Notes on the sheet:
  //   D_a: Port A Data
  //   D_b: Port B Data
  //   D_a_2: Port A Data
  //   D_b_2: Port B Data
  //   IO_i: IO Data In
  //   IO_r: IO Read
  //   IO_w: IO Write
  //   W_c: Program Control Word
  //   W_c_2: Program Control Word
  //   Φ: Clock
  //   A_a: Port A Address
  //   A_b: Port B Address
  //   A_a_2: Port A Address
  //   A_b_2: Port B Address
  //   A_m: Memory Address
  //   Π_a: Forwarding Signals Lane A
  //   Π_b: Forwarding Signals Lane A
  //   DM_w: Data Memory Write
  //   DM_a: Data Memory Address
  //   DM_i: Data Memory Data In
endmodule
