// Digital circuit Memory Stage.dig as structural Verilog
module Memory_Stage (
  input  [15:0] D_a,
  input  [15:0] D_b,
  input  [15:0] P_a,
  input  [15:0] IO_i,
  input  [5:0] W_c,
  input  \Φ ,
  input  [3:0] A_a_2,
  input  [3:0] A_b_2,
  input  [15:0] A_m,
  output [15:0] D_a_2,
  output [15:0] D_b_2,
  output [15:0] P_d,
  output [15:0] IO_o,
  output IO_r,
  output IO_w,
  output [7:0] IO_a,
  output [1:0] W_c_2,
  output [3:0] A_a,
  output [3:0] A_b,
  output [1:0] \Π_a ,
  output [1:0] \Π_b 
);

  wire and_1_out;
  wire [15:0] add_1_s, Dedotated_Wam_d1, multiplexer_1_out, multiplexer_2_out, multiplexer_3_out;

  Multiplexer #(.Bits(16)) multiplexer_1 (.sel(W_c[3]), .in_0({16{1'b0}}), .in_1({16{1'b1}}), .out(multiplexer_1_out));
  Multiplexer #(.Bits(16)) multiplexer_2 (.sel(W_c[2]), .in_0(Dedotated_Wam_d1), .in_1(IO_i), .out(multiplexer_2_out));
  Add #(.Bits(16)) add_1 (.a(A_m), .b(multiplexer_1_out), .c_i(1'b0), .s(add_1_s));  // open: c_o
  Multiplexer #(.Bits(16)) multiplexer_3 (.sel(W_c[0]), .in_0(D_a), .in_1(multiplexer_2_out), .out(multiplexer_3_out));
  and and_1 (and_1_out, W_c[1], ~W_c[2]);  // And
  Comparator #(.Bits(4)) comparator_1 (.a(W_c[3:0]), .b(4'b0000), .eq(\Π_a [1]));  // open: gt, lt
  RAMDualAccess #(.AddrBits(16), .isProgramMemory("true"), .Bits(16)) Dedotated_Wam (
    .str(and_1_out), .C(\Φ ), .ld(1'b1), .A1(add_1_s), .Din1(D_a), .A2(P_a), .D1(Dedotated_Wam_d1), .D2(P_d));
  Register #(.Bits(16)) register_1 (.D(multiplexer_3_out), .C(\Φ ), .en(1'b1), .Q(D_a_2));
  Register #(.Bits(4)) register_2 (.D(A_a_2), .C(\Φ ), .en(1'b1), .Q(A_a));
  Register #(.Bits(4)) register_3 (.D(A_b_2), .C(\Φ ), .en(1'b1), .Q(A_b));
  Register #(.Bits(2)) register_4 (.D(W_c[5:4]), .C(\Φ ), .en(1'b1), .Q(W_c_2));
  and and_2 (IO_r, W_c[2], W_c[0]);
  and and_3 (IO_w, W_c[2], W_c[1]);
  Register #(.Bits(16)) register_5 (.D(D_b), .C(\Φ ), .en(1'b1), .Q(D_b_2));

  assign IO_a = A_m[7:0];
  assign IO_o = D_a;
  assign \Π_a [0] = W_c[4];
  assign \Π_b  = {1'b1, W_c[5]};

  // Notes on the sheet:
  //   D_a: Port A Data
  //   D_b: Port B Data
  //   D_a_2: Port A Data
  //   D_b_2: Port B Data
  //   P_a: Program Address
  //   P_d: Program Data
  //   IO_o: IO Data Out
  //   IO_i: IO Data In
  //   IO_r: IO Read
  //   IO_w: IO Write
  //   IO_a: IO Address
  //   W_c: Program Control Word
  //   W_c_2: Program Control Word
  //   Φ: Clock
  //   A_a: Port A Address
  //   A_b: Port B Address
  //   A_a_2: Port A Address
  //   A_b_2: Port B Address
  //   A_m: Memory Address
  //   Π_a: Forwarding Signals Lane A
  //   Π_b: Forwarding Signals Lane A
endmodule
