// Digital circuit Register Stage.dig as structural Verilog
module Register_Stage (
  input  WE_b,
  input  [3:0] WA_b,
  input  [3:0] WA_a,
  input  WE_a,
  input  [3:0] RA_b,
  input  [3:0] RA_a,
  input  [15:0] WD_a,
  input  [15:0] WD_b,
  input  \Φ ,
  output [15:0] RD_b,
  output [15:0] RD_a,
  output [63:0] R_0123,
  output [63:0] R_4567,
  output [63:0] R_89AB,
  output [63:0] R_CDEF
);

  wire and_1_out, and_2_out, and_3_out, comparator_1_eq, comparator_2_eq, comparator_3_eq, comparator_4_eq,
       comparator_5_eq, comparator_6_eq, demultiplexer_1_out_1, demultiplexer_1_out_2, demultiplexer_1_out_3,
       demultiplexer_1_out_4, demultiplexer_1_out_5, demultiplexer_1_out_6, demultiplexer_1_out_7,
       demultiplexer_1_out_8, demultiplexer_1_out_9, demultiplexer_1_out_10, demultiplexer_1_out_11,
       demultiplexer_1_out_12, demultiplexer_1_out_13, demultiplexer_1_out_14, demultiplexer_1_out_15,
       demultiplexer_2_out_1, demultiplexer_2_out_2, demultiplexer_2_out_3, demultiplexer_2_out_4,
       demultiplexer_2_out_5, demultiplexer_2_out_6, demultiplexer_2_out_7, demultiplexer_2_out_8,
       demultiplexer_2_out_9, demultiplexer_2_out_10, demultiplexer_2_out_11, demultiplexer_2_out_12,
       demultiplexer_2_out_13, demultiplexer_2_out_14, demultiplexer_2_out_15, nor_1_out, or_1_out, or_2_out,
       or_3_out, or_4_out, or_5_out, or_6_out, or_7_out, or_8_out, or_9_out, or_10_out, or_11_out, or_12_out,
       or_13_out, or_14_out, or_15_out;
  wire [15:0] multiplexer_1_out, multiplexer_2_out, multiplexer_3_out, multiplexer_4_out, multiplexer_5_out,
       multiplexer_6_out, multiplexer_7_out, multiplexer_8_out, multiplexer_9_out, multiplexer_10_out,
       multiplexer_11_out, multiplexer_12_out, multiplexer_13_out, multiplexer_14_out, multiplexer_15_out,
       multiplexer_16_out, multiplexer_17_out, multiplexer_19_out;

  Demultiplexer #(.Selector_Bits(4)) demultiplexer_1 (
    .sel(WA_b), .in(WE_b), .out_1(demultiplexer_1_out_1), .out_2(demultiplexer_1_out_2),
    .out_3(demultiplexer_1_out_3), .out_4(demultiplexer_1_out_4), .out_5(demultiplexer_1_out_5),
    .out_6(demultiplexer_1_out_6), .out_7(demultiplexer_1_out_7), .out_8(demultiplexer_1_out_8),
    .out_9(demultiplexer_1_out_9), .out_10(demultiplexer_1_out_10), .out_11(demultiplexer_1_out_11),
    .out_12(demultiplexer_1_out_12), .out_13(demultiplexer_1_out_13), .out_14(demultiplexer_1_out_14),
    .out_15(demultiplexer_1_out_15));  // open: out_0
  Demultiplexer #(.Selector_Bits(4)) demultiplexer_2 (
    .sel(WA_a), .in(WE_a), .out_1(demultiplexer_2_out_1), .out_2(demultiplexer_2_out_2),
    .out_3(demultiplexer_2_out_3), .out_4(demultiplexer_2_out_4), .out_5(demultiplexer_2_out_5),
    .out_6(demultiplexer_2_out_6), .out_7(demultiplexer_2_out_7), .out_8(demultiplexer_2_out_8),
    .out_9(demultiplexer_2_out_9), .out_10(demultiplexer_2_out_10), .out_11(demultiplexer_2_out_11),
    .out_12(demultiplexer_2_out_12), .out_13(demultiplexer_2_out_13), .out_14(demultiplexer_2_out_14),
    .out_15(demultiplexer_2_out_15));  // open: out_0
  or or_1 (or_1_out, demultiplexer_1_out_1, demultiplexer_2_out_1);
  or or_2 (or_2_out, demultiplexer_1_out_2, demultiplexer_2_out_2);
  or or_3 (or_3_out, demultiplexer_1_out_3, demultiplexer_2_out_3);
  or or_4 (or_4_out, demultiplexer_1_out_4, demultiplexer_2_out_4);
  or or_5 (or_5_out, demultiplexer_1_out_5, demultiplexer_2_out_5);
  or or_6 (or_6_out, demultiplexer_1_out_6, demultiplexer_2_out_6);
  or or_7 (or_7_out, demultiplexer_1_out_7, demultiplexer_2_out_7);
  or or_8 (or_8_out, demultiplexer_1_out_8, demultiplexer_2_out_8);
  or or_9 (or_9_out, demultiplexer_1_out_9, demultiplexer_2_out_9);
  or or_10 (or_10_out, demultiplexer_1_out_10, demultiplexer_2_out_10);
  or or_11 (or_11_out, demultiplexer_1_out_11, demultiplexer_2_out_11);
  or or_12 (or_12_out, demultiplexer_1_out_12, demultiplexer_2_out_12);
  or or_13 (or_13_out, demultiplexer_1_out_13, demultiplexer_2_out_13);
  or or_14 (or_14_out, demultiplexer_1_out_14, demultiplexer_2_out_14);
  or or_15 (or_15_out, demultiplexer_1_out_15, demultiplexer_2_out_15);
  Multiplexer #(.Bits(16)) multiplexer_1 (
    .sel(demultiplexer_2_out_1), .in_0(WD_b), .in_1(WD_a), .out(multiplexer_1_out));
  Multiplexer #(.Bits(16)) multiplexer_2 (
    .sel(demultiplexer_2_out_2), .in_0(WD_b), .in_1(WD_a), .out(multiplexer_2_out));
  Multiplexer #(.Bits(16)) multiplexer_3 (
    .sel(demultiplexer_2_out_3), .in_0(WD_b), .in_1(WD_a), .out(multiplexer_3_out));
  Multiplexer #(.Bits(16)) multiplexer_4 (
    .sel(demultiplexer_2_out_4), .in_0(WD_b), .in_1(WD_a), .out(multiplexer_4_out));
  Multiplexer #(.Bits(16)) multiplexer_5 (
    .sel(demultiplexer_2_out_5), .in_0(WD_b), .in_1(WD_a), .out(multiplexer_5_out));
  Multiplexer #(.Bits(16)) multiplexer_6 (
    .sel(demultiplexer_2_out_6), .in_0(WD_b), .in_1(WD_a), .out(multiplexer_6_out));
  Multiplexer #(.Bits(16)) multiplexer_7 (
    .sel(demultiplexer_2_out_7), .in_0(WD_b), .in_1(WD_a), .out(multiplexer_7_out));
  Multiplexer #(.Bits(16)) multiplexer_8 (
    .sel(demultiplexer_2_out_8), .in_0(WD_b), .in_1(WD_a), .out(multiplexer_8_out));
  Multiplexer #(.Bits(16)) multiplexer_9 (
    .sel(demultiplexer_2_out_9), .in_0(WD_b), .in_1(WD_a), .out(multiplexer_9_out));
  Multiplexer #(.Bits(16)) multiplexer_10 (
    .sel(demultiplexer_2_out_10), .in_0(WD_b), .in_1(WD_a), .out(multiplexer_10_out));
  Multiplexer #(.Bits(16)) multiplexer_11 (
    .sel(demultiplexer_2_out_11), .in_0(WD_b), .in_1(WD_a), .out(multiplexer_11_out));
  Multiplexer #(.Bits(16)) multiplexer_12 (
    .sel(demultiplexer_2_out_12), .in_0(WD_b), .in_1(WD_a), .out(multiplexer_12_out));
  Multiplexer #(.Bits(16)) multiplexer_13 (
    .sel(demultiplexer_2_out_13), .in_0(WD_b), .in_1(WD_a), .out(multiplexer_13_out));
  Multiplexer #(.Bits(16)) multiplexer_14 (
    .sel(demultiplexer_2_out_14), .in_0(WD_b), .in_1(WD_a), .out(multiplexer_14_out));
  Multiplexer #(.Bits(16)) multiplexer_15 (
    .sel(demultiplexer_2_out_15), .in_0(WD_b), .in_1(WD_a), .out(multiplexer_15_out));
  Register #(.Bits(16)) register_1 (.D(multiplexer_1_out), .C(\Φ ), .en(or_1_out), .Q(R_0123[31:16]));
  Register #(.Bits(16)) register_2 (.D(multiplexer_2_out), .C(\Φ ), .en(or_2_out), .Q(R_0123[47:32]));
  Register #(.Bits(16)) register_3 (.D(multiplexer_3_out), .C(\Φ ), .en(or_3_out), .Q(R_0123[63:48]));
  Register #(.Bits(16)) register_4 (.D(multiplexer_4_out), .C(\Φ ), .en(or_4_out), .Q(R_4567[15:0]));
  Register #(.Bits(16)) register_5 (.D(multiplexer_5_out), .C(\Φ ), .en(or_5_out), .Q(R_4567[31:16]));
  Register #(.Bits(16)) register_6 (.D(multiplexer_6_out), .C(\Φ ), .en(or_6_out), .Q(R_4567[47:32]));
  Register #(.Bits(16)) register_7 (.D(multiplexer_7_out), .C(\Φ ), .en(or_7_out), .Q(R_4567[63:48]));
  Register #(.Bits(16)) register_8 (.D(multiplexer_8_out), .C(\Φ ), .en(or_8_out), .Q(R_89AB[15:0]));
  Register #(.Bits(16)) register_9 (.D(multiplexer_9_out), .C(\Φ ), .en(or_9_out), .Q(R_89AB[31:16]));
  Register #(.Bits(16)) register_10 (.D(multiplexer_10_out), .C(\Φ ), .en(or_10_out), .Q(R_89AB[47:32]));
  Register #(.Bits(16)) register_11 (.D(multiplexer_11_out), .C(\Φ ), .en(or_11_out), .Q(R_89AB[63:48]));
  Register #(.Bits(16)) register_12 (.D(multiplexer_12_out), .C(\Φ ), .en(or_12_out), .Q(R_CDEF[15:0]));
  Register #(.Bits(16)) register_13 (.D(multiplexer_13_out), .C(\Φ ), .en(or_13_out), .Q(R_CDEF[31:16]));
  Register #(.Bits(16)) register_14 (.D(multiplexer_14_out), .C(\Φ ), .en(or_14_out), .Q(R_CDEF[47:32]));
  Register #(.Bits(16)) register_15 (.D(multiplexer_15_out), .C(\Φ ), .en(or_15_out), .Q(R_CDEF[63:48]));
  Multiplexer #(.Selector_Bits(4), .Bits(16)) multiplexer_16 (
    .sel(RA_b), .in_0({16{1'b0}}), .in_1(R_0123[31:16]), .in_2(R_0123[47:32]), .in_3(R_0123[63:48]),
    .in_4(R_4567[15:0]), .in_5(R_4567[31:16]), .in_6(R_4567[47:32]), .in_7(R_4567[63:48]),
    .in_8(R_89AB[15:0]), .in_9(R_89AB[31:16]), .in_10(R_89AB[47:32]), .in_11(R_89AB[63:48]),
    .in_12(R_CDEF[15:0]), .in_13(R_CDEF[31:16]), .in_14(R_CDEF[47:32]), .in_15(R_CDEF[63:48]),
    .out(multiplexer_16_out));
  Multiplexer #(.Selector_Bits(4), .Bits(16)) multiplexer_17 (
    .sel(RA_a), .in_0({16{1'b0}}), .in_1(R_0123[31:16]), .in_2(R_0123[47:32]), .in_3(R_0123[63:48]),
    .in_4(R_4567[15:0]), .in_5(R_4567[31:16]), .in_6(R_4567[47:32]), .in_7(R_4567[63:48]),
    .in_8(R_89AB[15:0]), .in_9(R_89AB[31:16]), .in_10(R_89AB[47:32]), .in_11(R_89AB[63:48]),
    .in_12(R_CDEF[15:0]), .in_13(R_CDEF[31:16]), .in_14(R_CDEF[47:32]), .in_15(R_CDEF[63:48]),
    .out(multiplexer_17_out));
  Comparator #(.Bits(4)) comparator_1 (.a(RA_b), .b(4'b0000), .eq(comparator_1_eq));  // open: gt, lt
  Comparator #(.Bits(4)) comparator_2 (.a(RA_b), .b(WA_a), .eq(comparator_2_eq));  // open: gt, lt
  Comparator #(.Bits(4)) comparator_3 (.a(RA_b), .b(4'b0000), .eq(comparator_3_eq));  // open: gt, lt
  Comparator #(.Bits(4)) comparator_4 (.a(RA_b), .b(WA_b), .eq(comparator_4_eq));  // open: gt, lt
  Comparator #(.Bits(4)) comparator_5 (.a(RA_a), .b(4'b0000), .eq(comparator_5_eq));  // open: gt, lt
  Comparator #(.Bits(4)) comparator_6 (.a(RA_a), .b(WA_a), .eq(comparator_6_eq));  // open: gt, lt
  Multiplexer #(.Bits(16)) multiplexer_18 (.sel(and_3_out), .in_0(multiplexer_17_out), .in_1(WD_a), .out(RD_a));
  and and_1 (and_1_out, comparator_2_eq, ~comparator_1_eq, WE_a);  // And
  and and_2 (and_2_out, comparator_4_eq, ~comparator_3_eq, WE_b);  // And
  and and_3 (and_3_out, comparator_6_eq, ~comparator_5_eq, WE_a);  // And
  Multiplexer #(.Bits(16)) multiplexer_19 (.sel(and_1_out), .in_0(WD_b), .in_1(WD_a), .out(multiplexer_19_out));
  nor nor_1 (nor_1_out, and_1_out, and_2_out);
  Multiplexer #(.Bits(16)) multiplexer_20 (
    .sel(nor_1_out), .in_0(multiplexer_19_out), .in_1(multiplexer_16_out), .out(RD_b));

  assign R_0123[15:0] = {16{1'b0}};

  // Notes on the sheet:
  //   WE_b: Port B Write Enable
  //   WA_b: Port B Write Address
  //   WA_a: Port A Write Address
  //   WE_a: Port A Write Enable
  //   RA_b: Port B Read Address
  //   RA_a: Port A Read Address
  //   WD_a: Port A Write Data
  //   WD_b: Port B Write Data
  //   Φ: Clock
  //   RD_b: Port B Read Data
  //   RD_a: Port A Read Data
endmodule
