// Digital circuit Bit Replace Mux.dig as structural Verilog
module Bit_Replace_Mux (
  input  [3:0] B_a,
  input  [15:0] D_i,
  input  B_d,
  output [15:0] D_o
);

  wire decoder_1_out_0, decoder_1_out_1, decoder_1_out_2, decoder_1_out_3, decoder_1_out_4, decoder_1_out_5,
       decoder_1_out_6, decoder_1_out_7, decoder_1_out_8, decoder_1_out_9, decoder_1_out_10,
       decoder_1_out_11, decoder_1_out_12, decoder_1_out_13, decoder_1_out_14, decoder_1_out_15;

  Decoder #(.Selector_Bits(4)) decoder_1 (
    .sel(B_a), .out_0(decoder_1_out_0), .out_1(decoder_1_out_1), .out_2(decoder_1_out_2),
    .out_3(decoder_1_out_3), .out_4(decoder_1_out_4), .out_5(decoder_1_out_5), .out_6(decoder_1_out_6),
    .out_7(decoder_1_out_7), .out_8(decoder_1_out_8), .out_9(decoder_1_out_9), .out_10(decoder_1_out_10),
    .out_11(decoder_1_out_11), .out_12(decoder_1_out_12), .out_13(decoder_1_out_13),
    .out_14(decoder_1_out_14), .out_15(decoder_1_out_15));
  Multiplexer multiplexer_1 (.sel(decoder_1_out_0), .in_0(D_i[0]), .in_1(B_d), .out(D_o[0]));
  Multiplexer multiplexer_2 (.sel(decoder_1_out_1), .in_0(D_i[1]), .in_1(B_d), .out(D_o[1]));
  Multiplexer multiplexer_3 (.sel(decoder_1_out_2), .in_0(D_i[2]), .in_1(B_d), .out(D_o[2]));
  Multiplexer multiplexer_4 (.sel(decoder_1_out_3), .in_0(D_i[3]), .in_1(B_d), .out(D_o[3]));
  Multiplexer multiplexer_5 (.sel(decoder_1_out_4), .in_0(D_i[4]), .in_1(B_d), .out(D_o[4]));
  Multiplexer multiplexer_6 (.sel(decoder_1_out_5), .in_0(D_i[5]), .in_1(B_d), .out(D_o[5]));
  Multiplexer multiplexer_7 (.sel(decoder_1_out_6), .in_0(D_i[6]), .in_1(B_d), .out(D_o[6]));
  Multiplexer multiplexer_8 (.sel(decoder_1_out_7), .in_0(D_i[7]), .in_1(B_d), .out(D_o[7]));
  Multiplexer multiplexer_9 (.sel(decoder_1_out_8), .in_0(D_i[8]), .in_1(B_d), .out(D_o[8]));
  Multiplexer multiplexer_10 (.sel(decoder_1_out_9), .in_0(D_i[9]), .in_1(B_d), .out(D_o[9]));
  Multiplexer multiplexer_11 (.sel(decoder_1_out_10), .in_0(D_i[10]), .in_1(B_d), .out(D_o[10]));
  Multiplexer multiplexer_12 (.sel(decoder_1_out_11), .in_0(D_i[11]), .in_1(B_d), .out(D_o[11]));
  Multiplexer multiplexer_13 (.sel(decoder_1_out_12), .in_0(D_i[12]), .in_1(B_d), .out(D_o[12]));
  Multiplexer multiplexer_14 (.sel(decoder_1_out_13), .in_0(D_i[13]), .in_1(B_d), .out(D_o[13]));
  Multiplexer multiplexer_15 (.sel(decoder_1_out_14), .in_0(D_i[14]), .in_1(B_d), .out(D_o[14]));
  Multiplexer multiplexer_16 (.sel(decoder_1_out_15), .in_0(D_i[15]), .in_1(B_d), .out(D_o[15]));

  // Notes on the sheet:
  //   B_a: Bit Insert Position
  //   D_i: Data In
  //   D_o: Data Out
  //   B_d: Insert Bit
endmodule
