// Digital circuit VGA Test.dig as structural Verilog
module VGA_Test (
  input  [8:0] in_1,
  input  [7:0] in_2,
  input  clk
);

  wire [2:0] generator_stage_1_s;
  wire [7:0] generator_stage_1_p_y;
  wire [8:0] add_1_s, generator_stage_1_p_x, multiplexer_1_out;

  Generator_Stage generator_stage_1 (
    .P_Y(generator_stage_1_p_y), .S(generator_stage_1_s), .\Φ_PX (clk), .C_3(in_2), .C_2(in_1),
    .P_X(generator_stage_1_p_x));
  Add #(.Bits(9)) add_1 (
    .a(generator_stage_1_p_x), .b({1'b0, generator_stage_1_p_y}), .c_i(1'b0), .s(add_1_s));  // open: c_o
  Multiplexer #(.Bits(9)) multiplexer_1 (
    .sel(generator_stage_1_s[0]), .in_0({9{1'b0}}), .in_1(add_1_s), .out(multiplexer_1_out));
  VGA vga_1 (
    .R(multiplexer_1_out[0]), .G(multiplexer_1_out[1]), .B(multiplexer_1_out[2]), .H(generator_stage_1_s[1]),
    .V(generator_stage_1_s[2]), .C(clk));

  // Other names for the same wires on the sheet: Φ = clk

  // Notes on the sheet:
  //   clk: Hz: 2147483647
endmodule
