// Digital circuit VGA.dig as structural Verilog
module VGA (
  input  clk,
  input  in_2,
  input  [8:0] in_3,
  input  [15:0] in_4,
  input  in_5,
  input  [11:0] in_6,
  input  [15:0] in_7,
  input  [10:0] in_8,
  input  [8:0] in_9,
  input  [7:0] in_10,
  input  in_11,
  input  [7:0] in_12
);

  wire palette_stage_1_v_h, palette_stage_1_v_v;
  wire [2:0] access_stage_a_1_s_2, access_stage_b_1_s_2, generator_stage_1_s;
  wire [4:0] palette_stage_1_v_b, palette_stage_1_v_g, palette_stage_1_v_r;
  wire [7:0] access_stage_a_1_p_y_2, access_stage_b_1_p_y_2, counter_1_out, generator_stage_1_p_y;
  wire [8:0] access_stage_a_1_p_x_2, access_stage_b_1_p_x_2, generator_stage_1_p_x;
  wire [10:0] access_stage_a_1_c, access_stage_b_1_c_2;
  wire [15:0] access_stage_a_1_d_a, access_stage_b_1_d_a, access_stage_b_1_d_b;

  Generator_Stage generator_stage_1 (
    .P_Y(generator_stage_1_p_y), .S(generator_stage_1_s), .\Φ_PX (clk), .C_3(in_10), .C_2(in_9),
    .P_X(generator_stage_1_p_x));
  Counter #(.Bits(8)) counter_1 (.en(in_11), .C(clk), .clr(1'b0), .out(counter_1_out));  // open: ovf
  Access_Stage_A access_stage_a_1 (
    .S(generator_stage_1_s), .P_X(generator_stage_1_p_x), .P_Y(generator_stage_1_p_y), .\Φ_IO (clk),
    .M_I({in_12, counter_1_out}), .M_A({2'b00, counter_1_out[7:4], 2'b00, counter_1_out[3:0]}), .M_E(in_11),
    .S_2(access_stage_a_1_s_2), .\Φ_PX (clk), .C_1(in_8), .P_X_2(access_stage_a_1_p_x_2),
    .P_Y_2(access_stage_a_1_p_y_2), .C(access_stage_a_1_c), .D_A(access_stage_a_1_d_a));  // open: M_O
  Access_Stage_B access_stage_b_1 (
    .S(access_stage_a_1_s_2), .P_X(access_stage_a_1_p_x_2), .P_Y(access_stage_a_1_p_y_2), .\Φ_IO (clk),
    .S_2(access_stage_b_1_s_2), .\Φ_PX (clk), .C(access_stage_a_1_c), .P_X_2(access_stage_b_1_p_x_2),
    .P_Y_2(access_stage_b_1_p_y_2), .C_2(access_stage_b_1_c_2), .D_A(access_stage_b_1_d_a),
    .D_A_2(access_stage_a_1_d_a), .M_I(in_7), .M_A(in_6), .M_E(in_5), .D_B(access_stage_b_1_d_b));  // open: M_O
  Palette_Stage palette_stage_1 (
    .M_I(in_4), .M_A(in_3), .M_E(in_2), .\Φ_IO (clk), .\Φ_PX (clk), .V_R(palette_stage_1_v_r),
    .V_G(palette_stage_1_v_g), .V_B(palette_stage_1_v_b), .V_H(palette_stage_1_v_h),
    .V_V(palette_stage_1_v_v), .S(access_stage_b_1_s_2), .P_X(access_stage_b_1_p_x_2),
    .P_Y(access_stage_b_1_p_y_2), .C(access_stage_b_1_c_2), .D_A(access_stage_b_1_d_a),
    .D_B(access_stage_b_1_d_b));  // open: M_O
  VGA vga_1 (
    .R(palette_stage_1_v_r), .G(palette_stage_1_v_g), .B(palette_stage_1_v_b), .H(palette_stage_1_v_h),
    .V(palette_stage_1_v_v), .C(clk));

  // Other names for the same wires on the sheet: Φ = clk

  // Notes on the sheet:
  //   clk: Hz: 2147483647
endmodule
