// Digital circuit Access Stage A.dig as structural Verilog
module Access_Stage_A (
  input  [2:0] S,
  input  [8:0] P_X,
  input  [7:0] P_Y,
  input  \Φ_IO ,
  input  [15:0] M_I,
  input  [11:0] M_A,
  input  M_E,
  input  \Φ_PX ,
  input  [10:0] C_1,
  output [15:0] M_O,
  output [2:0] S_2,
  output [8:0] P_X_2,
  output [7:0] P_Y_2,
  output [10:0] C,
  output [15:0] D_A
);

  wire [11:0] multiplexer_1_out;
  wire [15:0] ramdualaccess_1_d1, ramdualaccess_1_d2;

  Multiplexer #(.Selector_Bits(2), .Bits(12)) multiplexer_1 (
    .sel(C_1[10:9]), .in_0({P_Y[6:0], P_X[8:4]}), .in_1({P_Y[6:1], P_X[8:3]}), .in_2({P_Y[7:2], P_X[8:3]}),
    .in_3({C_1[8], P_Y[7:3], P_X[8:3]}), .out(multiplexer_1_out));
  RAMDualAccess #(.AddrBits(12), .Bits(16)) ramdualaccess_1 (
    .str(M_E), .C(\Φ_IO ), .ld(1'b1), .A1(M_A), .Din1(M_I), .A2(multiplexer_1_out), .D1(ramdualaccess_1_d1),
    .D2(ramdualaccess_1_d2));
  Register #(.Bits(3)) register_1 (.D(S), .C(\Φ_PX ), .en(1'b1), .Q(S_2));
  Register #(.Bits(11)) register_2 (.D(C_1), .C(\Φ_PX ), .en(1'b1), .Q(C));
  Register #(.Bits(9)) register_3 (.D(P_X), .C(\Φ_PX ), .en(1'b1), .Q(P_X_2));
  Register #(.Bits(8)) register_4 (.D(P_Y), .C(\Φ_PX ), .en(1'b1), .Q(P_Y_2));
  Register #(.Bits(16)) register_5 (.D(ramdualaccess_1_d1), .C(\Φ_IO ), .en(1'b1), .Q(M_O));
  Register #(.Bits(16)) register_6 (.D(ramdualaccess_1_d2), .C(\Φ_PX ), .en(1'b1), .Q(D_A));

  // Other names for the same wires on the sheet: C_t[10:0] = C_1

  // Notes on the sheet:
  //   S: Sync Signals
  //   P_X: X Position
  //   P_Y: Y Posititon
  //   Φ_IO: IO Clock
  //   M_I: VRAM Data Input
  //   M_A: VRAM Address
  //   M_E: VRAM Write Enable
  //   M_O: VRAM Data Output
  //   S_2: Sync Signals
  //   Φ_PX: Pixel Clock
  //   C_1: Control Word 1
  //   P_X_2: X Position
  //   P_Y_2: Y Position
  //   C: Control Word
  //   D_A: Data Output Part A
  //   Mode Selection
  //   I/O
  //   VRAM Part A
endmodule
