// Digital circuit Generator Stage.dig as structural Verilog
module Generator_Stage (
  input  \Φ_PX ,
  input  [7:0] C_3,
  input  [8:0] C_2,
  output [7:0] P_Y,
  output [2:0] S,
  output [8:0] P_X
);

  wire and_1_out, comparator_2_eq, comparator_3_eq, comparator_4_eq, comparator_5_eq, comparator_6_eq,
       comparator_7_eq, comparator_8_eq, comparator_9_eq, comparator_10_eq, d_ff_1_nq, d_ff_1_q, d_ff_2_nq,
       d_ff_2_q, d_ff_3_q, d_ff_4_q, multiplexer_1_out, multiplexer_2_out, multiplexer_3_out,
       multiplexer_4_out, not_1_out, not_2_out, not_3_out, not_4_out, \Φ_PX_t ;
  wire [0:0] counter_1_out;
  wire [2:0] d_ff_3_nq;
  wire [7:0] counter_2_out_2, sub_2_s;
  wire [8:0] counter_1_out_2, sub_1_s;
  wire [9:0] counter_2_out;

  Counter #(.Bits(10)) counter_1 (
    .en(1'b1), .C(\Φ_PX ), .clr(\Φ_PX_t ), .out({counter_1_out_2, counter_1_out[0]}));  // open: ovf
  and and_1 (and_1_out, comparator_2_eq, \Φ_PX_t );
  Counter #(.Bits(10)) counter_2 (
    .en(\Φ_PX_t ), .C(\Φ_PX ), .clr(and_1_out), .out({counter_2_out[9], counter_2_out_2, counter_2_out[0]}));  // open: ovf
  Comparator #(.Bits(10)) comparator_1 (
    .a({counter_1_out_2, counter_1_out[0]}), .b(10'h31f), .eq(\Φ_PX_t ));  // open: gt, lt
  Comparator #(.Bits(10)) comparator_2 (
    .a({counter_2_out[9], counter_2_out_2, counter_2_out[0]}), .b(10'h20c), .eq(comparator_2_eq));  // open: gt, lt
  Comparator #(.Bits(10)) comparator_3 (
    .a({counter_1_out_2, counter_1_out[0]}), .b(10'h27f), .eq(comparator_3_eq));  // open: gt, lt
  Comparator #(.Bits(10)) comparator_4 (
    .a({counter_2_out[9], counter_2_out_2, counter_2_out[0]}), .b(10'h1df), .eq(comparator_4_eq));  // open: gt, lt
  Multiplexer multiplexer_1 (.sel(d_ff_1_q), .in_0(comparator_3_eq), .in_1(not_1_out), .out(multiplexer_1_out));
  Multiplexer multiplexer_2 (.sel(d_ff_2_q), .in_0(comparator_4_eq), .in_1(not_2_out), .out(multiplexer_2_out));
  Comparator #(.Bits(10)) comparator_5 (
    .a({counter_1_out_2, counter_1_out[0]}), .b(10'h31f), .eq(comparator_5_eq));  // open: gt, lt
  not not_1 (not_1_out, comparator_5_eq);
  Comparator #(.Bits(10)) comparator_6 (
    .a({counter_2_out[9], counter_2_out_2, counter_2_out[0]}), .b(10'h20c), .eq(comparator_6_eq));  // open: gt, lt
  not not_2 (not_2_out, comparator_6_eq);
  D_FF d_ff_1 (.D(multiplexer_1_out), .C(\Φ_PX ), .Q(d_ff_1_q), .nQ(d_ff_1_nq));
  D_FF d_ff_2 (.D(multiplexer_2_out), .C(\Φ_PX_t ), .Q(d_ff_2_q), .nQ(d_ff_2_nq));
  and and_2 (d_ff_3_nq[0], d_ff_1_nq, d_ff_2_nq);
  Comparator #(.Bits(10)) comparator_7 (
    .a({counter_1_out_2, counter_1_out[0]}), .b(10'h28f), .eq(comparator_7_eq));  // open: gt, lt
  Comparator #(.Bits(10)) comparator_8 (
    .a({counter_2_out[9], counter_2_out_2, counter_2_out[0]}), .b(10'h1e9), .eq(comparator_8_eq));  // open: gt, lt
  not not_3 (not_3_out, comparator_9_eq);
  Multiplexer multiplexer_3 (.sel(d_ff_3_q), .in_0(comparator_7_eq), .in_1(not_3_out), .out(multiplexer_3_out));
  not not_4 (not_4_out, comparator_10_eq);
  Multiplexer multiplexer_4 (.sel(d_ff_4_q), .in_0(comparator_8_eq), .in_1(not_4_out), .out(multiplexer_4_out));
  Comparator #(.Bits(10)) comparator_9 (
    .a({counter_1_out_2, counter_1_out[0]}), .b(10'h2ef), .eq(comparator_9_eq));  // open: gt, lt
  D_FF d_ff_3 (.D(multiplexer_3_out), .C(\Φ_PX ), .Q(d_ff_3_q), .nQ(d_ff_3_nq[1]));
  Comparator #(.Bits(10)) comparator_10 (
    .a({counter_2_out[9], counter_2_out_2, counter_2_out[0]}), .b(10'h1eb), .eq(comparator_10_eq));  // open: gt, lt
  D_FF d_ff_4 (.D(multiplexer_4_out), .C(\Φ_PX_t ), .Q(d_ff_4_q), .nQ(d_ff_3_nq[2]));
  Sub #(.Bits(9)) sub_1 (.a(counter_1_out_2), .b(C_2), .c_i(1'b0), .s(sub_1_s));  // open: c_o
  Sub #(.Bits(8)) sub_2 (.a(counter_2_out_2), .b(C_3), .c_i(1'b0), .s(sub_2_s));  // open: c_o
  Register #(.Bits(9)) register_1 (.D(sub_1_s), .C(\Φ_PX ), .en(1'b1), .Q(P_X));
  Register #(.Bits(3)) register_2 (.D(d_ff_3_nq), .C(\Φ_PX ), .en(1'b1), .Q(S));
  Register #(.Bits(8)) register_3 (.D(sub_2_s), .C(\Φ_PX ), .en(1'b1), .Q(P_Y));

  // Notes on the sheet:
  //   P_Y: Y Position
  //   S: Sync Signals
  //   Φ_PX: Pixel Clock
  //   C_3: Control Word 3
  //   C_2: Control Word 2
  //   P_X: X Position
  //   Vertical Counter
  //   Horizontal Counter
  //   Horizontal Visible Area
  //   Vertical Visible Area
  //   Horizontal Blank
  //   Vertical Blank
  //   X Scroll
  //   Y Scroll
endmodule
