// Digital circuit Palette Stage.dig as structural Verilog
module Palette_Stage (
  input  [15:0] M_I,
  input  [8:0] M_A,
  input  M_E,
  input  \Φ_IO ,
  input  \Φ_PX ,
  input  [2:0] S,
  input  [8:0] P_X,
  input  [7:0] P_Y,
  input  [10:0] C,
  input  [15:0] D_A,
  input  [15:0] D_B,
  output [4:0] V_R,
  output [4:0] V_G,
  output [4:0] V_B,
  output V_H,
  output V_V,
  output [15:0] M_O
);

  wire multiplexer_5_out;
  wire [0:0] bitselector_1_out;
  wire [3:0] multiplexer_1_out, multiplexer_3_out, sub_1_s;
  wire [7:0] multiplexer_2_out;
  wire [8:0] multiplexer_7_out;
  wire [15:0] multiplexer_4_out, multiplexer_6_out, ramdualaccess_1_d1, ramdualaccess_1_d2;

  RAMDualAccess #(.AddrBits(9), .Bits(16)) ramdualaccess_1 (
    .str(M_E), .C(\Φ_IO ), .ld(1'b1), .A1(M_A), .Din1(M_I), .A2(multiplexer_7_out), .D1(ramdualaccess_1_d1),
    .D2(ramdualaccess_1_d2));
  Sub #(.Bits(4)) sub_1 (.a(4'b1111), .b(P_X[3:0]), .c_i(1'b0), .s(sub_1_s));  // open: c_o
  BitSelector #(.Selector_Bits(4)) bitselector_1 (.in(multiplexer_4_out), .sel(sub_1_s), .out(bitselector_1_out[0]));
  Multiplexer #(.Selector_Bits(2), .Bits(4)) multiplexer_1 (
    .sel(P_X[2:1]), .in_0(multiplexer_4_out[15:12]), .in_1(multiplexer_4_out[11:8]),
    .in_2(multiplexer_4_out[7:4]), .in_3(multiplexer_4_out[3:0]), .out(multiplexer_1_out));
  Multiplexer #(.Bits(8)) multiplexer_2 (
    .sel(P_X[2]), .in_0(multiplexer_4_out[15:8]), .in_1(multiplexer_4_out[7:0]), .out(multiplexer_2_out));
  Multiplexer #(.Selector_Bits(2), .Bits(4)) multiplexer_3 (
    .sel(P_X[1:0]), .in_0(multiplexer_4_out[15:12]), .in_1(multiplexer_4_out[11:8]),
    .in_2(multiplexer_4_out[7:4]), .in_3(multiplexer_4_out[3:0]), .out(multiplexer_3_out));
  Register #(.Bits(16)) register_1 (.D(ramdualaccess_1_d1), .C(\Φ_IO ), .en(1'b1), .Q(M_O));
  Multiplexer #(.Bits(16)) multiplexer_4 (.sel(multiplexer_5_out), .in_0(D_A), .in_1(D_B), .out(multiplexer_4_out));
  Multiplexer #(.Selector_Bits(2)) multiplexer_5 (
    .sel(C[10:9]), .in_0(P_Y[7]), .in_1(P_Y[7]), .in_2(C[8]), .in_3(1'b1), .out(multiplexer_5_out));
  Multiplexer #(.Bits(16)) multiplexer_6 (
    .sel(S[0]), .in_0({16{1'b0}}), .in_1(ramdualaccess_1_d2), .out(multiplexer_6_out));
  Multiplexer #(.Selector_Bits(2), .Bits(9)) multiplexer_7 (
    .sel(C[10:9]), .in_0({C[7:0], bitselector_1_out[0]}), .in_1({C[7:3], multiplexer_1_out}),
    .in_2({C[7], multiplexer_2_out}), .in_3({D_A[12:8], multiplexer_3_out}), .out(multiplexer_7_out));
  Register register_2 (.D(S[2]), .C(\Φ_PX ), .en(1'b1), .Q(V_V));
  Register register_3 (.D(S[1]), .C(\Φ_PX ), .en(1'b1), .Q(V_H));
  Register #(.Bits(5)) register_4 (.D(multiplexer_6_out[4:0]), .C(\Φ_PX ), .en(1'b1), .Q(V_R));
  Register #(.Bits(5)) register_5 (.D(multiplexer_6_out[9:5]), .C(\Φ_PX ), .en(1'b1), .Q(V_G));
  Register #(.Bits(5)) register_6 (.D(multiplexer_6_out[14:10]), .C(\Φ_PX ), .en(1'b1), .Q(V_B));

  // Notes on the sheet:
  //   M_I: Color RAM Data Input
  //   M_A: Color RAM Address
  //   M_E: Color RAM Write Enable
  //   Φ_IO: IO Clock
  //   Φ_PX: Pixel Clock
  //   V_R: Video Red
  //   V_G: Video Green
  //   V_B: Video Blue
  //   V_H: Video Horizontal Sync
  //   V_V: Video Vertical Sync
  //   M_O: Color RAM Data Output
  //   S: Sync Signals
  //   P_X: X Position
  //   P_Y: Y Posititon
  //   C: Control Word
  //   D_A: Data Input Part A
  //   D_B: Data Input Part B
  //   Color Memory
  //   Pixel Data Merge
  //   VGA Interface
endmodule
