// Digital circuit Processor Core.dig as structural Verilog
module Processor_Core (
  input  [15:0] DM_i,
  input  [15:0] IO_i,
  input  [15:0] PM_i,
  input  \Φ ,
  output IO_r,
  output IO_w,
  output [15:0] DM_a,
  output DM_w,
  output [15:0] IO_o,
  output [7:0] IO_a,
  output [15:0] DM_o,
  output [15:0] PM_a,
  output [63:0] R_0123,
  output [63:0] R_4567,
  output [63:0] R_89AB,
  output [63:0] R_CDEF,
  output [15:0] RF,
  output [3:0] ST,
  output \Σ ,
  output [35:0] W,
  output [4:0] \Π ,
  output H
);

  wire branch_stage_1_f_c, branch_stage_1_j_e, \decode_stage_1_σ_o , execute_stage_1_s_e,
       \execute_stage_1_σ_o , \Π_Ba , \Π_Bb , \Π_Ra , \Π_Rb , \Σ_B , \Σ_X ;
  wire [1:0] \Π_Ma , \Π_Mb ;
  wire [2:0] \Π_Xa , \Π_Xb ;
  wire [3:0] A_Ba, A_Bb, A_Ma, A_Mb, A_Ra, A_Rb, A_Xa, A_Xb, decode_stage_1_ra_a, decode_stage_1_ra_b,
       execute_stage_1_s_d;
  wire [5:0] execute_stage_1_w_c_2;
  wire [7:0] decode_stage_1_im_ls;
  wire [15:0] branch_stage_1_a_m, branch_stage_1_j_a, branch_stage_1_w_c_2, D_Ba, D_Bb, D_Ma, D_Mb, D_Ra,
       D_Rb, D_Xa, D_Xb, decode_stage_1_im_x_2, decode_stage_1_w_a_2, F_Ba, F_Bb, F_Mb, F_Xa, F_Xb,
       fetch_stage_1_w_a, fetch_stage_1_w_d, register_stage_1_rd_a, register_stage_1_rd_b;
  wire [15:8] execute_stage_1_a_m;

  Fetch_Stage fetch_stage_1 (
    .P_d(PM_i), .P_a(PM_a), .J_e(branch_stage_1_j_e), .J_a(branch_stage_1_j_a), .\Δ (1'b0), .\Φ (\Φ ),
    .W_a(fetch_stage_1_w_a), .W_d(fetch_stage_1_w_d), .\Σ_i (\decode_stage_1_σ_o ));
  Decode_Stage decode_stage_1 (
    .W_a(fetch_stage_1_w_a), .W_d(fetch_stage_1_w_d), .IM_X(PM_i), .RD_a(register_stage_1_rd_a),
    .RD_b(register_stage_1_rd_b), .RA_a(decode_stage_1_ra_a), .RA_b(decode_stage_1_ra_b),
    .W_a_2(decode_stage_1_w_a_2), .W_c(W), .A_a(A_Ba), .A_b(A_Bb), .D_a(D_Ba), .D_b(D_Bb),
    .IM_X_2(decode_stage_1_im_x_2), .IM_LS(decode_stage_1_im_ls), .\Φ (\Φ ), .H(H), .\Σ_i (\Σ ),
    .\Σ_o (\decode_stage_1_σ_o ), .N(branch_stage_1_j_e));
  Register_Stage register_stage_1 (
    .WE_b(\Π_Rb ), .WA_b(A_Rb), .WA_a(A_Ra), .WE_a(\Π_Ra ), .RA_b(decode_stage_1_ra_b),
    .RA_a(decode_stage_1_ra_a), .WD_a(D_Ra), .WD_b(D_Rb), .\Φ (\Φ ), .RD_b(register_stage_1_rd_b),
    .RD_a(register_stage_1_rd_a), .R_0123(R_0123), .R_4567(R_4567), .R_89AB(R_89AB), .R_CDEF(R_CDEF));
  Branch_Stage branch_stage_1 (
    .W_a(decode_stage_1_w_a_2), .W_c(W), .\Φ (\Φ ), .W_c_2(branch_stage_1_w_c_2), .D_a(D_Xa), .D_b(D_Xb),
    .J_a(branch_stage_1_j_a), .J_e(branch_stage_1_j_e), .S_d(execute_stage_1_s_d), .S_e(execute_stage_1_s_e),
    .ST(ST), .RF(RF), .A_a(A_Ba), .A_b(A_Bb), .A_a_2(A_Xa), .A_b_2(A_Xb), .F_c(branch_stage_1_f_c),
    .IM_X(decode_stage_1_im_x_2), .IM_LS(decode_stage_1_im_ls), .D_a_2(F_Ba), .D_b_2(F_Bb),
    .A_m(branch_stage_1_a_m), .\Σ_e (\Σ_B ), .\Σ_i (\execute_stage_1_σ_o ), .\Σ_o (\Σ ), .\Π_a (\Π_Ba ),
    .\Π_b (\Π_Bb ));
  Execute_Stage execute_stage_1 (
    .W_c(branch_stage_1_w_c_2), .A_a(A_Xa), .D_a(F_Xa), .A_b(A_Xb), .D_b(F_Xb), .S_d(execute_stage_1_s_d),
    .S_e(execute_stage_1_s_e), .A_a_2(A_Ma), .D_a_2(D_Ma), .A_b_2(A_Mb), .D_b_2(D_Mb),
    .W_c_2(execute_stage_1_w_c_2), .\Φ (\Φ ), .F_c(branch_stage_1_f_c), .A_m({execute_stage_1_a_m, IO_a}),
    .A_m_2(branch_stage_1_a_m), .\Σ_e (\Σ_X ), .\Σ_o (\execute_stage_1_σ_o ), .\Π_a (\Π_Xa ), .\Π_b (\Π_Xb ));
  Memory_Stage_New memory_stage_new_1 (
    .D_a(DM_o), .D_b(F_Mb), .D_a_2(D_Ra), .D_b_2(D_Rb), .IO_i(IO_i), .IO_r(IO_r), .IO_w(IO_w),
    .W_c(execute_stage_1_w_c_2), .W_c_2({\Π_Rb , \Π_Ra }), .\Φ (\Φ ), .A_a(A_Ra), .A_b(A_Rb), .A_a_2(A_Ma),
    .A_b_2(A_Mb), .A_m({execute_stage_1_a_m, IO_a}), .\Π_a (\Π_Ma ), .\Π_b (\Π_Mb ), .DM_w(DM_w),
    .DM_a(DM_a), .DM_i(DM_i));
  Forwarding_Controller forwarding_controller_1 (
    .\Π_Ba (\Π_Ba ), .\Π_Bb (\Π_Bb ), .\Π_Xa (\Π_Xa ), .\Π_Xb (\Π_Xb ), .\Π_Ma (\Π_Ma ), .\Π_Mb (\Π_Mb ),
    .\Π_Ra (\Π_Ra ), .\Π_Rb (\Π_Rb ), .\Σ_B (\Σ_B ), .\Σ_X (\Σ_X ), .D_Ba(D_Ba), .D_Bb(D_Bb), .D_Xa(D_Xa),
    .D_Xb(D_Xb), .D_Ma(D_Ma), .D_Mb(D_Mb), .D_Ra(D_Ra), .D_Rb(D_Rb), .A_Ba(A_Ba), .A_Bb(A_Bb), .A_Xa(A_Xa),
    .A_Xb(A_Xb), .A_Ma(A_Ma), .A_Mb(A_Mb), .A_Ra(A_Ra), .A_Rb(A_Rb), .F_Ba(F_Ba), .F_Xb(F_Xb), .F_Ma(DM_o),
    .F_Mb(F_Mb), .F_Bb(F_Bb), .F_Xa(F_Xa), .E(1'b1), .S(\Π ));

  assign IO_o = DM_o;

  // Other names for the same wires on the sheet: F_Ma[15:0] = DM_o

  // Notes on the sheet:
  //   IO_r: IO Read
  //   IO_w: IO Write
  //   DM_a: Data Memory Address
  //   DM_i: Data Memory Data In
  //   DM_w: Data Memory Write
  //   IO_i: IO Data In
  //   IO_o: IO Data Out
  //   IO_a: IO Address
  //   DM_o: Data Memory Data Out
  //   PM_i: Program Memory Data In
  //   PM_a: Program Memory Address
  //   Φ: System Clock
  //   R_0123: Diagnostics: Register File 1
  //   R_4567: Diagnostics: Register File 2
  //   R_89AB: Diagnostics: Register File 3
  //   R_CDEF: Diagnostics: Register File 4
  //   RF: Diagnostics: Reference Register
  //   ST: Diagnostics: Status Register
  //   Σ: Diagnostics: Stall
  //   W: Diagnostics: Decoded Word
  //   Π: Diagnostics: Forwarding
  //   H: Halt
endmodule
