// Digital circuit Decode Stage.dig as structural Verilog
module Decode_Stage (
  input  [15:0] W_a,
  input  [15:0] W_d,
  input  [15:0] IM_X,
  input  [15:0] RD_a,
  input  [15:0] RD_b,
  input  \Φ ,
  input  \Σ_i ,
  input  N,
  output [3:0] RA_a,
  output [3:0] RA_b,
  output [15:0] W_a_2,
  output [35:0] W_c,
  output [3:0] A_a,
  output [3:0] A_b,
  output [15:0] D_a,
  output [15:0] D_b,
  output [15:0] IM_X_2,
  output [7:0] IM_LS,
  output H,
  output \Σ_o 
);

  wire or_1_out, \Σ ;
  wire [0:0] register_1_q;
  wire [7:0] LOGIC_d, multiplexer_3_out, multiplexer_4_out;
  wire [31:0] MEMBLK_d;

  ROM #(.AddrBits(8), .Bits(8)) LOGIC (.A(multiplexer_3_out), .sel(1'b1), .D(LOGIC_d));
  Register #(.Bits(5)) register_1 (.D(LOGIC_d[7:3]), .C(\Φ ), .en(\Σ ), .Q({W_c[21:20], W_c[1:0], register_1_q[0]}));
  or or_1 (or_1_out, register_1_q[0], N);
  Multiplexer #(.Bits(4)) multiplexer_1 (.sel(LOGIC_d[0]), .in_0(W_d[3:0]), .in_1(4'b0001), .out(RA_a));
  Multiplexer #(.Bits(4)) multiplexer_2 (.sel(LOGIC_d[1]), .in_0(W_d[7:4]), .in_1(4'b1110), .out(RA_b));
  Multiplexer #(.Bits(8)) multiplexer_3 (.sel(or_1_out), .in_0(W_d[15:8]), .in_1({8{1'b1}}), .out(multiplexer_3_out));
  Register #(.Bits(4)) register_2 (.D(RA_a), .C(\Φ ), .en(\Σ ), .Q(A_a));
  and and_1 (H, LOGIC_d[0], LOGIC_d[1], ~N);  // And
  Register #(.Bits(4)) register_3 (.D(RA_b), .C(\Φ ), .en(\Σ ), .Q(A_b));
  ROM #(.AddrBits(8), .Bits(32)) MEMBLK (.A(multiplexer_3_out), .sel(1'b1), .D(MEMBLK_d));
  Multiplexer #(.Bits(8)) multiplexer_4 (.sel(LOGIC_d[2]), .in_0(W_d[7:0]), .in_1(W_d[11:4]), .out(multiplexer_4_out));
  Register #(.Bits(32)) register_4 (.D(MEMBLK_d), .C(\Φ ), .en(\Σ ), .Q({W_c[35:22], W_c[19:2]}));
  Register #(.Bits(8)) register_5 (.D(multiplexer_4_out), .C(\Φ ), .en(\Σ ), .Q(IM_LS));
  not not_1 (\Σ , \Σ_i );
  Register #(.Bits(16)) register_6 (.D(W_a), .C(\Φ ), .en(\Σ ), .Q(W_a_2));
  Register #(.Bits(16)) register_7 (.D(IM_X), .C(\Φ ), .en(\Σ ), .Q(IM_X_2));
  Register #(.Bits(16)) register_8 (.D(RD_a), .C(\Φ ), .en(\Σ ), .Q(D_a));
  Register #(.Bits(16)) register_9 (.D(RD_b), .C(\Φ ), .en(\Σ ), .Q(D_b));

  assign \Σ_o  = \Σ_i ;

  // Notes on the sheet:
  //   W_a: Program Word Address
  //   W_d: Program Word Data
  //   IM_X: Extended Immediate
  //   RD_a: Port A Read Data
  //   RD_b: Port B Read Data
  //   RA_a: Port A Read Address
  //   RA_b: Port B Read Address
  //   W_a_2: Program Word Address
  //   W_c: Program Control Word
  //   A_a: Port A Originating Address
  //   A_b: Port B Originating Address
  //   D_a: Port A Originating Data
  //   D_b: Port B Originating Data
  //   IM_X_2: Extended Immediate
  //   IM_LS: Long/Short Immediate
  //   Φ: Clock
  //   H: Halt
  //   Σ_i: Stall Backpropagate Input
  //   Σ_o: Stall Backpropagate Output
  //   N: Nullify
  //   contents of LOGIC (hex, n*v repeats v):
  //   4*f0,a8,20,a8,20,f0,a8,f0,f0,f0,a0,20,10,4*f0,4*a8,5*a0,54,54,54
  //   ,4*a0,4*f0,4*a8,4*f8,32*a6,16*4,16*14,16*4,8*20,8*30,8*20,8*30
  //   ,8*28,8*38,8*0,20,30,20,3,20,28,1,9*0,8*10,8*0,8*10,4*0,20,8
  //   contents of MEMBLK (hex, n*v repeats v):
  //   41000000,41200000,41180000,41280000,410002d4,400000c2,411402d4
  //   ,400000ca,41f80000,41f802d4,c3f80000,c3fc0000,1180000,11802d4
  //   ,400001c0,10000,416c0000,41400000,41600000,41500000,416c02d4,414002d4
  //   ,416002d4,415002d4,41800000,41880000,41840000,418c0000,419c0000
  //   ,41cc0445,41c00445,41c40445,44000012,c400024a,e4000242,c4000242
  //   ,8000012,8800024a,a8000242,88000242,44000010,c4000248,e4000240
  //   ,c4000240,8000010,88000248,a8000240,88000240,16*44000011,16*8000011
  //   ,16*54000005,16*18000005,16*400000c5,40008780,40009780,4000a780
  //   ,4000b780,4000c780,4000d780,4000e780,4000f780,40000780,40001780
  //   ,40002780,40003780,40004780,40005780,40006780,40007780,28012,29012
  //   ,2a012,2b012,2c012,2d012,2e012,2f012,20012,21012,22012,23012,24012
  //   ,25012,26012,27012,28010,29010,2a010,2b010,2c010,2d010,2e010,2f010
  //   ,20010,21010,22010,23010,24010,25010,26010,27010,28019,29019,2a019
  //   ,2b019,2c019,2d019,2e019,2f019,40000080,c0000080,40000350,0,40000112
  //   ,40000130,40000131,119,8400,9400,a400,b400,c400,d400,e400,f400
  //   ,c00,1c00,2c00,3c00,4c00,5c00,6c00,7c00,8c40,9c40,ac40,bc40,cc40
  //   ,dc40,ec40,fc40,c40,1c40,2c40,3c40,4c40,5c40,6c40,7c40,d80,dc0
  //   ,d00,d40,d00,f00,40000800,30000
endmodule
