// Digital circuit Fetch Stage.dig as structural Verilog
module Fetch_Stage (
  input  [15:0] P_d,
  input  J_e,
  input  [15:0] J_a,
  input  \Δ ,
  input  \Φ ,
  input  \Σ_i ,
  output [15:0] P_a,
  output [15:0] W_a,
  output [15:0] W_d
);

  wire \Σ ;
  wire [15:0] add_1_s, multiplexer_1_out, multiplexer_2_out, multiplexer_3_out;

  Multiplexer #(.Bits(16)) multiplexer_1 (.sel(J_e), .in_0(multiplexer_3_out), .in_1(J_a), .out(multiplexer_1_out));
  not not_1 (\Σ , \Σ_i );
  Register #(.Bits(16)) ip (.D(multiplexer_1_out), .C(\Φ ), .en(\Σ ), .Q(P_a));
  Multiplexer #(.Bits(16)) multiplexer_2 (.sel(J_e), .in_0(P_d), .in_1(16'hff00), .out(multiplexer_2_out));
  Add #(.Bits(16)) add_1 (.a(P_a), .b({16{1'b0}}), .c_i(1'b1), .s(add_1_s));  // open: c_o
  Register #(.Bits(16)) register_1 (.D(P_a), .C(\Φ ), .en(\Σ ), .Q(W_a));
  Register #(.Bits(16)) register_2 (.D(multiplexer_2_out), .C(\Φ ), .en(\Σ ), .Q(W_d));
  Multiplexer #(.Bits(16)) multiplexer_3 (.sel(\Δ ), .in_0(add_1_s), .in_1({16{1'b0}}), .out(multiplexer_3_out));

  // Notes on the sheet:
  //   P_d: Program Data
  //   P_a: Program Address
  //   J_e: Jump Enable
  //   J_a: Jump Address
  //   Δ: Reset
  //   Φ: Clock
  //   W_a: Program Word Address
  //   W_d: Program Word Data
  //   Σ_i: Stall Backpropagate Input
endmodule
