// Digital circuit Forwarding Controller.dig as structural Verilog
module Forwarding_Controller (
  input  \Π_Ba ,
  input  \Π_Bb ,
  input  [2:0] \Π_Xa ,
  input  [2:0] \Π_Xb ,
  input  [1:0] \Π_Ma ,
  input  [1:0] \Π_Mb ,
  input  \Π_Ra ,
  input  \Π_Rb ,
  input  [15:0] D_Ba,
  input  [15:0] D_Bb,
  input  [15:0] D_Xa,
  input  [15:0] D_Xb,
  input  [15:0] D_Ma,
  input  [15:0] D_Mb,
  input  [15:0] D_Ra,
  input  [15:0] D_Rb,
  input  [3:0] A_Ba,
  input  [3:0] A_Bb,
  input  [3:0] A_Xa,
  input  [3:0] A_Xb,
  input  [3:0] A_Ma,
  input  [3:0] A_Mb,
  input  [3:0] A_Ra,
  input  [3:0] A_Rb,
  input  E,
  output \Σ_B ,
  output \Σ_X ,
  output [15:0] F_Ba,
  output [15:0] F_Xb,
  output [15:0] F_Ma,
  output [15:0] F_Mb,
  output [15:0] F_Bb,
  output [15:0] F_Xa,
  output [4:0] S
);

  wire and_1_out, and_2_out, and_3_out, and_4_out, and_5_out, and_6_out, and_7_out, and_8_out, and_9_out,
       and_10_out, and_11_out, and_12_out, and_13_out, and_14_out, and_15_out, and_16_out, and_17_out,
       and_18_out, and_19_out, and_20_out, and_21_out, and_22_out, and_28_out, and_29_out, and_30_out,
       and_31_out, comparator_1_eq, comparator_2_eq, comparator_3_eq, comparator_4_eq, comparator_5_eq,
       comparator_6_eq, comparator_7_eq, comparator_8_eq, comparator_9_eq, comparator_10_eq,
       comparator_11_eq, comparator_12_eq, comparator_13_eq, comparator_14_eq, comparator_15_eq,
       comparator_16_eq, comparator_17_eq, comparator_18_eq, comparator_19_eq, comparator_20_eq,
       comparator_21_eq, comparator_22_eq, multiplexer_1_out, multiplexer_3_out, multiplexer_5_out,
       multiplexer_7_out, priorityencoder_1_any, priorityencoder_2_any, priorityencoder_3_any,
       priorityencoder_4_any, priorityencoder_5_any, priorityencoder_5_num, U_Ma, U_Mb;
  wire [1:0] priorityencoder_1_num, priorityencoder_2_num, priorityencoder_3_num, priorityencoder_4_num;
  wire [2:2] priorityencoder_1_num_2, priorityencoder_2_num_2;
  wire [15:0] multiplexer_2_out, multiplexer_4_out, multiplexer_6_out, multiplexer_8_out, multiplexer_9_out;

  Comparator #(.Bits(4)) comparator_1 (.a(A_Rb), .b(A_Ba), .eq(comparator_1_eq));  // open: gt, lt
  Comparator #(.Bits(4)) comparator_2 (.a(A_Ra), .b(A_Ba), .eq(comparator_2_eq));  // open: gt, lt
  Comparator #(.Bits(4)) comparator_3 (.a(A_Mb), .b(A_Ba), .eq(comparator_3_eq));  // open: gt, lt
  Comparator #(.Bits(4)) comparator_4 (.a(A_Ma), .b(A_Ba), .eq(comparator_4_eq));  // open: gt, lt
  Comparator #(.Bits(4)) comparator_5 (.a(A_Xb), .b(A_Ba), .eq(comparator_5_eq));  // open: gt, lt
  Comparator #(.Bits(4)) comparator_6 (.a(A_Xa), .b(A_Ba), .eq(comparator_6_eq));  // open: gt, lt
  Comparator #(.Bits(4)) comparator_7 (.a(A_Rb), .b(A_Bb), .eq(comparator_7_eq));  // open: gt, lt
  Comparator #(.Bits(4)) comparator_8 (.a(A_Ra), .b(A_Bb), .eq(comparator_8_eq));  // open: gt, lt
  Comparator #(.Bits(4)) comparator_9 (.a(A_Mb), .b(A_Bb), .eq(comparator_9_eq));  // open: gt, lt
  Comparator #(.Bits(4)) comparator_10 (.a(A_Ma), .b(A_Bb), .eq(comparator_10_eq));  // open: gt, lt
  Comparator #(.Bits(4)) comparator_11 (.a(A_Xb), .b(A_Bb), .eq(comparator_11_eq));  // open: gt, lt
  Comparator #(.Bits(4)) comparator_12 (.a(A_Xa), .b(A_Bb), .eq(comparator_12_eq));  // open: gt, lt
  Comparator #(.Bits(4)) comparator_13 (.a(A_Rb), .b(A_Xa), .eq(comparator_13_eq));  // open: gt, lt
  Comparator #(.Bits(4)) comparator_14 (.a(A_Ra), .b(A_Xa), .eq(comparator_14_eq));  // open: gt, lt
  Comparator #(.Bits(4)) comparator_15 (.a(A_Mb), .b(A_Xa), .eq(comparator_15_eq));  // open: gt, lt
  Comparator #(.Bits(4)) comparator_16 (.a(A_Ma), .b(A_Xa), .eq(comparator_16_eq));  // open: gt, lt
  Comparator #(.Bits(4)) comparator_17 (.a(A_Rb), .b(A_Xb), .eq(comparator_17_eq));  // open: gt, lt
  Comparator #(.Bits(4)) comparator_18 (.a(A_Ra), .b(A_Xb), .eq(comparator_18_eq));  // open: gt, lt
  Comparator #(.Bits(4)) comparator_19 (.a(A_Mb), .b(A_Xb), .eq(comparator_19_eq));  // open: gt, lt
  Comparator #(.Bits(4)) comparator_20 (.a(A_Ma), .b(A_Xb), .eq(comparator_20_eq));  // open: gt, lt
  Comparator #(.Bits(4)) comparator_21 (.a(A_Rb), .b(A_Ma), .eq(comparator_21_eq));  // open: gt, lt
  Comparator #(.Bits(4)) comparator_22 (.a(A_Ra), .b(A_Ma), .eq(comparator_22_eq));  // open: gt, lt
  and and_1 (and_1_out, \Π_Rb , \Π_Ba , comparator_1_eq);
  and and_2 (and_2_out, \Π_Ra , \Π_Ba , comparator_2_eq);
  and and_3 (and_3_out, \Π_Mb [0], \Π_Ba , comparator_3_eq);
  and and_4 (and_4_out, \Π_Ma [0], \Π_Ba , comparator_4_eq);
  and and_5 (and_5_out, \Π_Xb [0], \Π_Ba , comparator_5_eq);
  and and_6 (and_6_out, \Π_Xa [0], \Π_Ba , comparator_6_eq);
  and and_7 (and_7_out, \Π_Rb , \Π_Bb , comparator_7_eq);
  and and_8 (and_8_out, \Π_Ra , \Π_Bb , comparator_8_eq);
  and and_9 (and_9_out, \Π_Mb [0], \Π_Bb , comparator_9_eq);
  and and_10 (and_10_out, \Π_Ma [0], \Π_Bb , comparator_10_eq);
  and and_11 (and_11_out, \Π_Xb [0], \Π_Bb , comparator_11_eq);
  and and_12 (and_12_out, \Π_Xa [0], \Π_Bb , comparator_12_eq);
  and and_13 (and_13_out, \Π_Rb , \Π_Xa [2], comparator_13_eq);
  and and_14 (and_14_out, \Π_Ra , \Π_Xa [2], comparator_14_eq);
  and and_15 (and_15_out, \Π_Mb [0], \Π_Xa [2], comparator_15_eq);
  and and_16 (and_16_out, \Π_Ma [0], \Π_Xa [2], comparator_16_eq);
  and and_17 (and_17_out, \Π_Rb , \Π_Xb [2], comparator_17_eq);
  and and_18 (and_18_out, \Π_Ra , \Π_Xb [2], comparator_18_eq);
  and and_19 (and_19_out, \Π_Mb [0], \Π_Xb [2], comparator_19_eq);
  and and_20 (and_20_out, \Π_Ma [0], \Π_Xb [2], comparator_20_eq);
  and and_21 (and_21_out, \Π_Rb , U_Ma, comparator_21_eq);
  and and_22 (and_22_out, \Π_Ra , U_Ma, comparator_22_eq);
  PriorityEncoder #(.Selector_Bits(3)) priorityencoder_1 (
    .in0(1'b0), .in1(1'b0), .in2(and_1_out), .in3(and_2_out), .in4(and_3_out), .in5(and_4_out),
    .in6(and_5_out), .in7(and_6_out), .num({priorityencoder_1_num_2[2], priorityencoder_1_num}),
    .any(priorityencoder_1_any));
  PriorityEncoder #(.Selector_Bits(3)) priorityencoder_2 (
    .in0(1'b0), .in1(1'b0), .in2(and_7_out), .in3(and_8_out), .in4(and_9_out), .in5(and_10_out),
    .in6(and_11_out), .in7(and_12_out), .num({priorityencoder_2_num_2[2], priorityencoder_2_num}),
    .any(priorityencoder_2_any));
  PriorityEncoder #(.Selector_Bits(2)) priorityencoder_3 (
    .in0(and_13_out), .in1(and_14_out), .in2(and_15_out), .in3(and_16_out), .num(priorityencoder_3_num),
    .any(priorityencoder_3_any));
  PriorityEncoder #(.Selector_Bits(2)) priorityencoder_4 (
    .in0(and_17_out), .in1(and_18_out), .in2(and_19_out), .in3(and_20_out), .num(priorityencoder_4_num),
    .any(priorityencoder_4_any));
  PriorityEncoder priorityencoder_5 (
    .in0(and_21_out), .in1(and_22_out), .num(priorityencoder_5_num), .any(priorityencoder_5_any));
  Multiplexer #(.Selector_Bits(2)) multiplexer_1 (
    .sel(priorityencoder_1_num), .in_0(\Π_Mb [1]), .in_1(\Π_Ma [1]), .in_2(\Π_Xb [1]), .in_3(\Π_Xa [1]),
    .out(multiplexer_1_out));
  and and_23 (S[0], E, priorityencoder_1_any);
  Multiplexer #(.Selector_Bits(3), .Bits(16)) multiplexer_2 (
    .sel({priorityencoder_1_num_2[2], priorityencoder_1_num}), .in_0({16{1'b0}}), .in_1({16{1'b0}}),
    .in_2(D_Rb), .in_3(D_Ra), .in_4(D_Mb), .in_5(D_Ma), .in_6(D_Xb), .in_7(D_Xa), .out(multiplexer_2_out));
  Multiplexer #(.Selector_Bits(2)) multiplexer_3 (
    .sel(priorityencoder_2_num), .in_0(\Π_Mb [1]), .in_1(\Π_Ma [1]), .in_2(\Π_Xb [1]), .in_3(\Π_Xa [1]),
    .out(multiplexer_3_out));
  and and_24 (S[1], E, priorityencoder_2_any);
  Multiplexer #(.Selector_Bits(3), .Bits(16)) multiplexer_4 (
    .sel({priorityencoder_2_num_2[2], priorityencoder_2_num}), .in_0({16{1'b0}}), .in_1({16{1'b0}}),
    .in_2(D_Rb), .in_3(D_Ra), .in_4(D_Mb), .in_5(D_Ma), .in_6(D_Xb), .in_7(D_Xa), .out(multiplexer_4_out));
  Multiplexer multiplexer_5 (
    .sel(priorityencoder_3_num[0]), .in_0(\Π_Mb [1]), .in_1(\Π_Ma [1]), .out(multiplexer_5_out));
  and and_25 (S[2], E, priorityencoder_3_any);
  Multiplexer #(.Selector_Bits(2), .Bits(16)) multiplexer_6 (
    .sel(priorityencoder_3_num), .in_0(D_Rb), .in_1(D_Ra), .in_2(D_Mb), .in_3(D_Ma), .out(multiplexer_6_out));
  Multiplexer multiplexer_7 (
    .sel(priorityencoder_4_num[0]), .in_0(\Π_Mb [1]), .in_1(\Π_Ma [1]), .out(multiplexer_7_out));
  and and_26 (S[3], E, priorityencoder_4_any);
  Multiplexer #(.Selector_Bits(2), .Bits(16)) multiplexer_8 (
    .sel(priorityencoder_4_num), .in_0(D_Rb), .in_1(D_Ra), .in_2(D_Mb), .in_3(D_Ma), .out(multiplexer_8_out));
  and and_27 (S[4], E, priorityencoder_5_any);
  Multiplexer #(.Bits(16)) multiplexer_9 (
    .sel(priorityencoder_5_num), .in_0(D_Rb), .in_1(D_Ra), .out(multiplexer_9_out));
  not not_1 (U_Ma, \Π_Ma [1]);
  not not_2 (U_Mb, \Π_Mb [1]);
  and and_28 (and_28_out, ~multiplexer_1_out, S[0], priorityencoder_1_num_2[2]);  // And
  Multiplexer #(.Bits(16)) multiplexer_10 (.sel(S[0]), .in_0(D_Ba), .in_1(multiplexer_2_out), .out(F_Ba));
  and and_29 (and_29_out, ~multiplexer_3_out, S[1], priorityencoder_2_num_2[2]);  // And
  Multiplexer #(.Bits(16)) multiplexer_11 (.sel(S[1]), .in_0(D_Bb), .in_1(multiplexer_4_out), .out(F_Bb));
  and and_30 (and_30_out, ~multiplexer_5_out, S[2], priorityencoder_3_num[1]);  // And
  Multiplexer #(.Bits(16)) multiplexer_12 (.sel(S[2]), .in_0(D_Xa), .in_1(multiplexer_6_out), .out(F_Xa));
  and and_31 (and_31_out, ~multiplexer_7_out, S[3], priorityencoder_4_num[1]);  // And
  Multiplexer #(.Bits(16)) multiplexer_13 (.sel(S[3]), .in_0(D_Xb), .in_1(multiplexer_8_out), .out(F_Xb));
  Multiplexer #(.Bits(16)) multiplexer_14 (.sel(S[4]), .in_0(D_Ma), .in_1(multiplexer_9_out), .out(F_Ma));
  or or_1 (\Σ_B , and_28_out, and_29_out);
  or or_2 (\Σ_X , and_30_out, and_31_out);

  assign F_Mb = D_Mb;

  // Other names for the same wires on the sheet: S_Ba = S[0]; S_Bb = S[1]; S_Ma = S[4]; S_Xa = S[2]; S_Xb = S[3];
  //   U_Ba = \Π_Ba ; U_Bb = \Π_Bb ; W_Ra = \Π_Ra ; W_Rb = \Π_Rb ; W_Ma = \Π_Ma [0]; R_Ma = \Π_Ma [1];
  //   W_Mb = \Π_Mb [0]; R_Mb = \Π_Mb [1]; W_Xa = \Π_Xa [0]; R_Xa = \Π_Xa [1]; U_Xa = \Π_Xa [2]; W_Xb = \Π_Xb [0];
  //   R_Xb = \Π_Xb [1]; U_Xb = \Π_Xb [2]

  // Notes on the sheet:
  //   Π_Ba: Branch Stage Forwarding Signals Lane A
  //   Π_Bb: Branch Stage Forwarding Signals Lane B
  //   Π_Xa: Execute Stage Forwarding Signals Lane A
  //   Π_Xb: Execute Stage Forwarding Signals Lane B
  //   Π_Ma: Memory Stage Forwarding Signals Lane A
  //   Π_Mb: Memory Stage Forwarding Signals Lane B
  //   Π_Ra: Writeback Stage Forwarding Signals Lane A
  //   Π_Rb: Writeback Stage Forwarding Signals Lane B
  //   Σ_B: Branch Stage Stall Enable
  //   Σ_X: Execute Stage Stall Enable
  //   D_Ba: Branch Stage Register Data Lane A
  //   D_Bb: Branch Stage Register Data Lane B
  //   D_Xa: Execute Stage Register Data Lane A
  //   D_Xb: Execute Stage Register Data Lane B
  //   D_Ma: Memory Stage Register Data Lane A
  //   D_Mb: Memory Stage Register Data Lane B
  //   D_Ra: Writeback Stage Register Data Lane A
  //   D_Rb: Writeback Stage Register Data Lane B
  //   A_Ba: Branch Stage Register Address Lane A
  //   A_Bb: Branch Stage Register Address Lane B
  //   A_Xa: Execute Stage Register Address Lane A
  //   A_Xb: Execute Stage Register Address Lane B
  //   A_Ma: Memory Stage Register Address Lane A
  //   A_Ra: Writeback Stage Register Address Lane A
  //   A_Rb: Writeback Stage Register Address Lane B
  //   F_Ba: Branch Stage Register Forward Data Lane A
  //   F_Xb: Execute Stage Register Forward Data Lane B
  //   F_Ma: Memory Stage Register Forward Data Lane A
  //   F_Mb: Memory Stage Register Forward Data Lane B
  //   F_Bb: Branch Stage Register Forward Data Lane B
  //   F_Xa: Execute Stage Register Forward Data Lane A
  //   E: Forward Enable
  //   S: Forwarding Status
endmodule
