// Digital circuit Barrel Shifter.dig as structural Verilog
module Barrel_Shifter (
  input  [15:0] D_i,
  input  [3:0] S,
  input  [1:0] C,
  output [15:0] D_o
);

  wire and_1_out, and_2_out, and_3_out, and_4_out, multiplexer_1_out, multiplexer_2_out, multiplexer_3_out,
       multiplexer_4_out, multiplexer_5_out, multiplexer_6_out, multiplexer_7_out, multiplexer_8_out,
       multiplexer_9_out, multiplexer_10_out, multiplexer_11_out, multiplexer_12_out, multiplexer_13_out,
       multiplexer_14_out, multiplexer_15_out, multiplexer_16_out, multiplexer_17_out, multiplexer_18_out,
       multiplexer_19_out, multiplexer_20_out, multiplexer_21_out, multiplexer_22_out, multiplexer_23_out,
       multiplexer_24_out, multiplexer_25_out, multiplexer_26_out, multiplexer_27_out, multiplexer_28_out,
       multiplexer_29_out, multiplexer_30_out, multiplexer_31_out, multiplexer_32_out, multiplexer_33_out,
       multiplexer_34_out, multiplexer_35_out, multiplexer_36_out, multiplexer_37_out, multiplexer_38_out,
       multiplexer_39_out, multiplexer_40_out, multiplexer_41_out, multiplexer_42_out, multiplexer_43_out,
       multiplexer_44_out, multiplexer_45_out, multiplexer_46_out, multiplexer_47_out, multiplexer_48_out,
       multiplexer_49_out, multiplexer_50_out, multiplexer_51_out, multiplexer_52_out, multiplexer_53_out,
       multiplexer_54_out, multiplexer_55_out, multiplexer_56_out, multiplexer_57_out, multiplexer_58_out,
       multiplexer_59_out, multiplexer_60_out, multiplexer_61_out, multiplexer_62_out, multiplexer_63_out,
       multiplexer_64_out, multiplexer_65_out, multiplexer_66_out, multiplexer_67_out, multiplexer_68_out,
       multiplexer_69_out, multiplexer_70_out, multiplexer_71_out, multiplexer_72_out, multiplexer_73_out,
       multiplexer_74_out, multiplexer_75_out, multiplexer_76_out, multiplexer_77_out, multiplexer_78_out,
       multiplexer_79_out, multiplexer_80_out, multiplexer_81_out, multiplexer_82_out, multiplexer_83_out,
       multiplexer_84_out, multiplexer_85_out, multiplexer_86_out, multiplexer_87_out, multiplexer_88_out,
       multiplexer_89_out, multiplexer_90_out, multiplexer_91_out, multiplexer_92_out, multiplexer_93_out,
       multiplexer_94_out, multiplexer_95_out, multiplexer_96_out, multiplexer_97_out, multiplexer_98_out,
       multiplexer_99_out, multiplexer_100_out, multiplexer_101_out, multiplexer_102_out,
       multiplexer_103_out, multiplexer_104_out, multiplexer_105_out, multiplexer_106_out,
       multiplexer_107_out, multiplexer_108_out, multiplexer_109_out, multiplexer_110_out,
       multiplexer_111_out, multiplexer_112_out;

  and and_1 (and_1_out, D_i[15], C[1]);
  Multiplexer multiplexer_1 (.sel(S[0]), .in_0(D_i[0]), .in_1(multiplexer_2_out), .out(multiplexer_1_out));
  Multiplexer multiplexer_2 (.sel(C[0]), .in_0(1'b0), .in_1(D_i[1]), .out(multiplexer_2_out));
  Multiplexer multiplexer_3 (.sel(S[0]), .in_0(D_i[1]), .in_1(multiplexer_4_out), .out(multiplexer_3_out));
  Multiplexer multiplexer_4 (.sel(C[0]), .in_0(D_i[0]), .in_1(D_i[2]), .out(multiplexer_4_out));
  Multiplexer multiplexer_5 (.sel(S[0]), .in_0(D_i[2]), .in_1(multiplexer_6_out), .out(multiplexer_5_out));
  Multiplexer multiplexer_6 (.sel(C[0]), .in_0(D_i[1]), .in_1(D_i[3]), .out(multiplexer_6_out));
  Multiplexer multiplexer_7 (.sel(S[0]), .in_0(D_i[3]), .in_1(multiplexer_8_out), .out(multiplexer_7_out));
  Multiplexer multiplexer_8 (.sel(C[0]), .in_0(D_i[2]), .in_1(D_i[4]), .out(multiplexer_8_out));
  Multiplexer multiplexer_9 (.sel(S[0]), .in_0(D_i[4]), .in_1(multiplexer_10_out), .out(multiplexer_9_out));
  Multiplexer multiplexer_10 (.sel(C[0]), .in_0(D_i[3]), .in_1(D_i[5]), .out(multiplexer_10_out));
  Multiplexer multiplexer_11 (.sel(S[0]), .in_0(D_i[5]), .in_1(multiplexer_12_out), .out(multiplexer_11_out));
  Multiplexer multiplexer_12 (.sel(C[0]), .in_0(D_i[4]), .in_1(D_i[6]), .out(multiplexer_12_out));
  Multiplexer multiplexer_13 (.sel(S[0]), .in_0(D_i[6]), .in_1(multiplexer_14_out), .out(multiplexer_13_out));
  Multiplexer multiplexer_14 (.sel(C[0]), .in_0(D_i[5]), .in_1(D_i[7]), .out(multiplexer_14_out));
  Multiplexer multiplexer_15 (.sel(S[0]), .in_0(D_i[7]), .in_1(multiplexer_16_out), .out(multiplexer_15_out));
  Multiplexer multiplexer_16 (.sel(C[0]), .in_0(D_i[6]), .in_1(D_i[8]), .out(multiplexer_16_out));
  Multiplexer multiplexer_17 (.sel(S[0]), .in_0(D_i[8]), .in_1(multiplexer_18_out), .out(multiplexer_17_out));
  Multiplexer multiplexer_18 (.sel(C[0]), .in_0(D_i[7]), .in_1(D_i[9]), .out(multiplexer_18_out));
  Multiplexer multiplexer_19 (.sel(S[0]), .in_0(D_i[9]), .in_1(multiplexer_20_out), .out(multiplexer_19_out));
  Multiplexer multiplexer_20 (.sel(C[0]), .in_0(D_i[8]), .in_1(D_i[10]), .out(multiplexer_20_out));
  Multiplexer multiplexer_21 (.sel(S[0]), .in_0(D_i[10]), .in_1(multiplexer_22_out), .out(multiplexer_21_out));
  Multiplexer multiplexer_22 (.sel(C[0]), .in_0(D_i[9]), .in_1(D_i[11]), .out(multiplexer_22_out));
  Multiplexer multiplexer_23 (.sel(S[0]), .in_0(D_i[11]), .in_1(multiplexer_24_out), .out(multiplexer_23_out));
  Multiplexer multiplexer_24 (.sel(C[0]), .in_0(D_i[10]), .in_1(D_i[12]), .out(multiplexer_24_out));
  Multiplexer multiplexer_25 (.sel(S[0]), .in_0(D_i[12]), .in_1(multiplexer_26_out), .out(multiplexer_25_out));
  Multiplexer multiplexer_26 (.sel(C[0]), .in_0(D_i[11]), .in_1(D_i[13]), .out(multiplexer_26_out));
  Multiplexer multiplexer_27 (.sel(S[0]), .in_0(D_i[13]), .in_1(multiplexer_28_out), .out(multiplexer_27_out));
  Multiplexer multiplexer_28 (.sel(C[0]), .in_0(D_i[12]), .in_1(D_i[14]), .out(multiplexer_28_out));
  Multiplexer multiplexer_29 (.sel(S[0]), .in_0(D_i[14]), .in_1(multiplexer_30_out), .out(multiplexer_29_out));
  Multiplexer multiplexer_30 (.sel(C[0]), .in_0(D_i[13]), .in_1(D_i[15]), .out(multiplexer_30_out));
  Multiplexer multiplexer_31 (.sel(S[0]), .in_0(D_i[15]), .in_1(multiplexer_32_out), .out(multiplexer_31_out));
  Multiplexer multiplexer_32 (.sel(C[0]), .in_0(D_i[14]), .in_1(and_1_out), .out(multiplexer_32_out));
  and and_2 (and_2_out, multiplexer_31_out, C[1]);
  Multiplexer multiplexer_33 (.sel(C[0]), .in_0(1'b0), .in_1(multiplexer_5_out), .out(multiplexer_33_out));
  Multiplexer multiplexer_34 (.sel(C[0]), .in_0(1'b0), .in_1(multiplexer_7_out), .out(multiplexer_34_out));
  Multiplexer multiplexer_35 (.sel(C[0]), .in_0(multiplexer_1_out), .in_1(multiplexer_9_out), .out(multiplexer_35_out));
  Multiplexer multiplexer_36 (
    .sel(C[0]), .in_0(multiplexer_3_out), .in_1(multiplexer_11_out), .out(multiplexer_36_out));
  Multiplexer multiplexer_37 (
    .sel(C[0]), .in_0(multiplexer_5_out), .in_1(multiplexer_13_out), .out(multiplexer_37_out));
  Multiplexer multiplexer_38 (
    .sel(C[0]), .in_0(multiplexer_7_out), .in_1(multiplexer_15_out), .out(multiplexer_38_out));
  Multiplexer multiplexer_39 (
    .sel(C[0]), .in_0(multiplexer_9_out), .in_1(multiplexer_17_out), .out(multiplexer_39_out));
  Multiplexer multiplexer_40 (
    .sel(C[0]), .in_0(multiplexer_11_out), .in_1(multiplexer_19_out), .out(multiplexer_40_out));
  Multiplexer multiplexer_41 (
    .sel(C[0]), .in_0(multiplexer_13_out), .in_1(multiplexer_21_out), .out(multiplexer_41_out));
  Multiplexer multiplexer_42 (
    .sel(C[0]), .in_0(multiplexer_15_out), .in_1(multiplexer_23_out), .out(multiplexer_42_out));
  Multiplexer multiplexer_43 (
    .sel(C[0]), .in_0(multiplexer_17_out), .in_1(multiplexer_25_out), .out(multiplexer_43_out));
  Multiplexer multiplexer_44 (
    .sel(C[0]), .in_0(multiplexer_19_out), .in_1(multiplexer_27_out), .out(multiplexer_44_out));
  Multiplexer multiplexer_45 (
    .sel(C[0]), .in_0(multiplexer_21_out), .in_1(multiplexer_29_out), .out(multiplexer_45_out));
  Multiplexer multiplexer_46 (
    .sel(C[0]), .in_0(multiplexer_23_out), .in_1(multiplexer_31_out), .out(multiplexer_46_out));
  Multiplexer multiplexer_47 (.sel(C[0]), .in_0(multiplexer_25_out), .in_1(and_2_out), .out(multiplexer_47_out));
  Multiplexer multiplexer_48 (.sel(C[0]), .in_0(multiplexer_27_out), .in_1(and_2_out), .out(multiplexer_48_out));
  Multiplexer multiplexer_49 (
    .sel(S[1]), .in_0(multiplexer_1_out), .in_1(multiplexer_33_out), .out(multiplexer_49_out));
  Multiplexer multiplexer_50 (
    .sel(S[1]), .in_0(multiplexer_3_out), .in_1(multiplexer_34_out), .out(multiplexer_50_out));
  Multiplexer multiplexer_51 (
    .sel(S[1]), .in_0(multiplexer_5_out), .in_1(multiplexer_35_out), .out(multiplexer_51_out));
  Multiplexer multiplexer_52 (
    .sel(S[1]), .in_0(multiplexer_7_out), .in_1(multiplexer_36_out), .out(multiplexer_52_out));
  Multiplexer multiplexer_53 (
    .sel(S[1]), .in_0(multiplexer_9_out), .in_1(multiplexer_37_out), .out(multiplexer_53_out));
  Multiplexer multiplexer_54 (
    .sel(S[1]), .in_0(multiplexer_11_out), .in_1(multiplexer_38_out), .out(multiplexer_54_out));
  Multiplexer multiplexer_55 (
    .sel(S[1]), .in_0(multiplexer_13_out), .in_1(multiplexer_39_out), .out(multiplexer_55_out));
  Multiplexer multiplexer_56 (
    .sel(S[1]), .in_0(multiplexer_15_out), .in_1(multiplexer_40_out), .out(multiplexer_56_out));
  Multiplexer multiplexer_57 (
    .sel(S[1]), .in_0(multiplexer_17_out), .in_1(multiplexer_41_out), .out(multiplexer_57_out));
  Multiplexer multiplexer_58 (
    .sel(S[1]), .in_0(multiplexer_19_out), .in_1(multiplexer_42_out), .out(multiplexer_58_out));
  Multiplexer multiplexer_59 (
    .sel(S[1]), .in_0(multiplexer_21_out), .in_1(multiplexer_43_out), .out(multiplexer_59_out));
  Multiplexer multiplexer_60 (
    .sel(S[1]), .in_0(multiplexer_23_out), .in_1(multiplexer_44_out), .out(multiplexer_60_out));
  Multiplexer multiplexer_61 (
    .sel(S[1]), .in_0(multiplexer_25_out), .in_1(multiplexer_45_out), .out(multiplexer_61_out));
  Multiplexer multiplexer_62 (
    .sel(S[1]), .in_0(multiplexer_27_out), .in_1(multiplexer_46_out), .out(multiplexer_62_out));
  Multiplexer multiplexer_63 (
    .sel(S[1]), .in_0(multiplexer_29_out), .in_1(multiplexer_47_out), .out(multiplexer_63_out));
  Multiplexer multiplexer_64 (
    .sel(S[1]), .in_0(multiplexer_31_out), .in_1(multiplexer_48_out), .out(multiplexer_64_out));
  and and_3 (and_3_out, multiplexer_64_out, C[1]);
  Multiplexer multiplexer_65 (.sel(C[0]), .in_0(1'b0), .in_1(multiplexer_53_out), .out(multiplexer_65_out));
  Multiplexer multiplexer_66 (.sel(C[0]), .in_0(1'b0), .in_1(multiplexer_54_out), .out(multiplexer_66_out));
  Multiplexer multiplexer_67 (.sel(C[0]), .in_0(1'b0), .in_1(multiplexer_55_out), .out(multiplexer_67_out));
  Multiplexer multiplexer_68 (.sel(C[0]), .in_0(1'b0), .in_1(multiplexer_56_out), .out(multiplexer_68_out));
  Multiplexer multiplexer_69 (
    .sel(C[0]), .in_0(multiplexer_49_out), .in_1(multiplexer_57_out), .out(multiplexer_69_out));
  Multiplexer multiplexer_70 (
    .sel(C[0]), .in_0(multiplexer_50_out), .in_1(multiplexer_58_out), .out(multiplexer_70_out));
  Multiplexer multiplexer_71 (
    .sel(C[0]), .in_0(multiplexer_51_out), .in_1(multiplexer_59_out), .out(multiplexer_71_out));
  Multiplexer multiplexer_72 (
    .sel(C[0]), .in_0(multiplexer_52_out), .in_1(multiplexer_60_out), .out(multiplexer_72_out));
  Multiplexer multiplexer_73 (
    .sel(C[0]), .in_0(multiplexer_53_out), .in_1(multiplexer_61_out), .out(multiplexer_73_out));
  Multiplexer multiplexer_74 (
    .sel(C[0]), .in_0(multiplexer_54_out), .in_1(multiplexer_62_out), .out(multiplexer_74_out));
  Multiplexer multiplexer_75 (
    .sel(C[0]), .in_0(multiplexer_55_out), .in_1(multiplexer_63_out), .out(multiplexer_75_out));
  Multiplexer multiplexer_76 (
    .sel(C[0]), .in_0(multiplexer_56_out), .in_1(multiplexer_64_out), .out(multiplexer_76_out));
  Multiplexer multiplexer_77 (.sel(C[0]), .in_0(multiplexer_57_out), .in_1(and_3_out), .out(multiplexer_77_out));
  Multiplexer multiplexer_78 (.sel(C[0]), .in_0(multiplexer_58_out), .in_1(and_3_out), .out(multiplexer_78_out));
  Multiplexer multiplexer_79 (.sel(C[0]), .in_0(multiplexer_59_out), .in_1(and_3_out), .out(multiplexer_79_out));
  Multiplexer multiplexer_80 (.sel(C[0]), .in_0(multiplexer_60_out), .in_1(and_3_out), .out(multiplexer_80_out));
  Multiplexer multiplexer_81 (
    .sel(S[2]), .in_0(multiplexer_49_out), .in_1(multiplexer_65_out), .out(multiplexer_81_out));
  Multiplexer multiplexer_82 (
    .sel(S[2]), .in_0(multiplexer_50_out), .in_1(multiplexer_66_out), .out(multiplexer_82_out));
  Multiplexer multiplexer_83 (
    .sel(S[2]), .in_0(multiplexer_51_out), .in_1(multiplexer_67_out), .out(multiplexer_83_out));
  Multiplexer multiplexer_84 (
    .sel(S[2]), .in_0(multiplexer_52_out), .in_1(multiplexer_68_out), .out(multiplexer_84_out));
  Multiplexer multiplexer_85 (
    .sel(S[2]), .in_0(multiplexer_53_out), .in_1(multiplexer_69_out), .out(multiplexer_85_out));
  Multiplexer multiplexer_86 (
    .sel(S[2]), .in_0(multiplexer_54_out), .in_1(multiplexer_70_out), .out(multiplexer_86_out));
  Multiplexer multiplexer_87 (
    .sel(S[2]), .in_0(multiplexer_55_out), .in_1(multiplexer_71_out), .out(multiplexer_87_out));
  Multiplexer multiplexer_88 (
    .sel(S[2]), .in_0(multiplexer_56_out), .in_1(multiplexer_72_out), .out(multiplexer_88_out));
  Multiplexer multiplexer_89 (
    .sel(S[2]), .in_0(multiplexer_57_out), .in_1(multiplexer_73_out), .out(multiplexer_89_out));
  Multiplexer multiplexer_90 (
    .sel(S[2]), .in_0(multiplexer_58_out), .in_1(multiplexer_74_out), .out(multiplexer_90_out));
  Multiplexer multiplexer_91 (
    .sel(S[2]), .in_0(multiplexer_59_out), .in_1(multiplexer_75_out), .out(multiplexer_91_out));
  Multiplexer multiplexer_92 (
    .sel(S[2]), .in_0(multiplexer_60_out), .in_1(multiplexer_76_out), .out(multiplexer_92_out));
  Multiplexer multiplexer_93 (
    .sel(S[2]), .in_0(multiplexer_61_out), .in_1(multiplexer_77_out), .out(multiplexer_93_out));
  Multiplexer multiplexer_94 (
    .sel(S[2]), .in_0(multiplexer_62_out), .in_1(multiplexer_78_out), .out(multiplexer_94_out));
  Multiplexer multiplexer_95 (
    .sel(S[2]), .in_0(multiplexer_63_out), .in_1(multiplexer_79_out), .out(multiplexer_95_out));
  Multiplexer multiplexer_96 (
    .sel(S[2]), .in_0(multiplexer_64_out), .in_1(multiplexer_80_out), .out(multiplexer_96_out));
  and and_4 (and_4_out, multiplexer_96_out, C[1]);
  Multiplexer multiplexer_97 (.sel(C[0]), .in_0(1'b0), .in_1(multiplexer_89_out), .out(multiplexer_97_out));
  Multiplexer multiplexer_98 (.sel(C[0]), .in_0(1'b0), .in_1(multiplexer_90_out), .out(multiplexer_98_out));
  Multiplexer multiplexer_99 (.sel(C[0]), .in_0(1'b0), .in_1(multiplexer_91_out), .out(multiplexer_99_out));
  Multiplexer multiplexer_100 (.sel(C[0]), .in_0(1'b0), .in_1(multiplexer_92_out), .out(multiplexer_100_out));
  Multiplexer multiplexer_101 (.sel(C[0]), .in_0(1'b0), .in_1(multiplexer_93_out), .out(multiplexer_101_out));
  Multiplexer multiplexer_102 (.sel(C[0]), .in_0(1'b0), .in_1(multiplexer_94_out), .out(multiplexer_102_out));
  Multiplexer multiplexer_103 (.sel(C[0]), .in_0(1'b0), .in_1(multiplexer_95_out), .out(multiplexer_103_out));
  Multiplexer multiplexer_104 (.sel(C[0]), .in_0(1'b0), .in_1(multiplexer_96_out), .out(multiplexer_104_out));
  Multiplexer multiplexer_105 (.sel(C[0]), .in_0(multiplexer_81_out), .in_1(and_4_out), .out(multiplexer_105_out));
  Multiplexer multiplexer_106 (.sel(C[0]), .in_0(multiplexer_82_out), .in_1(and_4_out), .out(multiplexer_106_out));
  Multiplexer multiplexer_107 (.sel(C[0]), .in_0(multiplexer_83_out), .in_1(and_4_out), .out(multiplexer_107_out));
  Multiplexer multiplexer_108 (.sel(C[0]), .in_0(multiplexer_84_out), .in_1(and_4_out), .out(multiplexer_108_out));
  Multiplexer multiplexer_109 (.sel(C[0]), .in_0(multiplexer_85_out), .in_1(and_4_out), .out(multiplexer_109_out));
  Multiplexer multiplexer_110 (.sel(C[0]), .in_0(multiplexer_86_out), .in_1(and_4_out), .out(multiplexer_110_out));
  Multiplexer multiplexer_111 (.sel(C[0]), .in_0(multiplexer_87_out), .in_1(and_4_out), .out(multiplexer_111_out));
  Multiplexer multiplexer_112 (.sel(C[0]), .in_0(multiplexer_88_out), .in_1(and_4_out), .out(multiplexer_112_out));
  Multiplexer multiplexer_113 (.sel(S[3]), .in_0(multiplexer_81_out), .in_1(multiplexer_97_out), .out(D_o[0]));
  Multiplexer multiplexer_114 (.sel(S[3]), .in_0(multiplexer_82_out), .in_1(multiplexer_98_out), .out(D_o[1]));
  Multiplexer multiplexer_115 (.sel(S[3]), .in_0(multiplexer_83_out), .in_1(multiplexer_99_out), .out(D_o[2]));
  Multiplexer multiplexer_116 (.sel(S[3]), .in_0(multiplexer_84_out), .in_1(multiplexer_100_out), .out(D_o[3]));
  Multiplexer multiplexer_117 (.sel(S[3]), .in_0(multiplexer_85_out), .in_1(multiplexer_101_out), .out(D_o[4]));
  Multiplexer multiplexer_118 (.sel(S[3]), .in_0(multiplexer_86_out), .in_1(multiplexer_102_out), .out(D_o[5]));
  Multiplexer multiplexer_119 (.sel(S[3]), .in_0(multiplexer_87_out), .in_1(multiplexer_103_out), .out(D_o[6]));
  Multiplexer multiplexer_120 (.sel(S[3]), .in_0(multiplexer_88_out), .in_1(multiplexer_104_out), .out(D_o[7]));
  Multiplexer multiplexer_121 (.sel(S[3]), .in_0(multiplexer_89_out), .in_1(multiplexer_105_out), .out(D_o[8]));
  Multiplexer multiplexer_122 (.sel(S[3]), .in_0(multiplexer_90_out), .in_1(multiplexer_106_out), .out(D_o[9]));
  Multiplexer multiplexer_123 (.sel(S[3]), .in_0(multiplexer_91_out), .in_1(multiplexer_107_out), .out(D_o[10]));
  Multiplexer multiplexer_124 (.sel(S[3]), .in_0(multiplexer_92_out), .in_1(multiplexer_108_out), .out(D_o[11]));
  Multiplexer multiplexer_125 (.sel(S[3]), .in_0(multiplexer_93_out), .in_1(multiplexer_109_out), .out(D_o[12]));
  Multiplexer multiplexer_126 (.sel(S[3]), .in_0(multiplexer_94_out), .in_1(multiplexer_110_out), .out(D_o[13]));
  Multiplexer multiplexer_127 (.sel(S[3]), .in_0(multiplexer_95_out), .in_1(multiplexer_111_out), .out(D_o[14]));
  Multiplexer multiplexer_128 (.sel(S[3]), .in_0(multiplexer_96_out), .in_1(multiplexer_112_out), .out(D_o[15]));

  // Notes on the sheet:
  //   D_i: Data Input
  //   S: Shift
  //   D_o: Data Output
  //   C: Control
endmodule
