// Digital circuit Multiplier.dig as structural Verilog
module Multiplier (
  input  [15:0] D_B,
  input  [15:0] D_A,
  input  C,
  output [15:0] P_L,
  output [15:0] P_H
);

  wire and_1_out, and_2_out, xor_1_out;
  wire [15:0] add_1_s, add_2_s, add_3_s, add_4_s, add_5_s, add_6_s, add_7_s, add_8_s, add_9_s, add_10_s,
       add_11_s, add_12_s, add_13_s, add_14_s, add_15_s, add_16_s, add_17_s, multiplexer_1_out,
       multiplexer_2_out, multiplexer_3_out, multiplexer_4_out, multiplexer_5_out, multiplexer_6_out,
       multiplexer_7_out, multiplexer_8_out, multiplexer_9_out, multiplexer_10_out, multiplexer_11_out,
       multiplexer_12_out, multiplexer_13_out, multiplexer_14_out, multiplexer_15_out, multiplexer_16_out,
       multiplexer_17_out, multiplexer_18_out, not_1_out, not_2_out;
  wire [15:15] add_3_c_o, add_4_c_o, add_5_c_o, add_6_c_o, add_7_c_o, add_8_c_o, add_9_c_o, add_10_c_o,
       add_11_c_o, add_12_c_o, add_13_c_o, add_14_c_o, add_15_c_o, add_16_c_o;
  wire [31:0] multiplexer_19_out, not_3_out;
  wire [31:31] add_17_c_o;

  Multiplexer #(.Bits(16)) multiplexer_1 (.sel(and_1_out), .in_0(D_A), .in_1(not_1_out), .out(multiplexer_1_out));
  assign not_1_out = ~D_A;  // Not not_1, 16 bits wide
  and and_1 (and_1_out, D_A[15], C);
  Multiplexer #(.Bits(16)) multiplexer_2 (.sel(and_2_out), .in_0(D_B), .in_1(not_2_out), .out(multiplexer_2_out));
  assign not_2_out = ~D_B;  // Not not_2, 16 bits wide
  and and_2 (and_2_out, D_B[15], C);
  Add #(.Bits(16)) add_1 (.a({16{1'b0}}), .b(multiplexer_1_out), .c_i(and_1_out), .s(add_1_s));  // open: c_o
  Add #(.Bits(16)) add_2 (.a({16{1'b0}}), .b(multiplexer_2_out), .c_i(and_2_out), .s(add_2_s));  // open: c_o
  xor xor_1 (xor_1_out, and_1_out, and_2_out);
  Multiplexer #(.Bits(16)) multiplexer_3 (.sel(add_1_s[0]), .in_0({16{1'b0}}), .in_1(add_2_s), .out(multiplexer_3_out));
  Multiplexer #(.Bits(16)) multiplexer_4 (.sel(add_1_s[1]), .in_0({16{1'b0}}), .in_1(add_2_s), .out(multiplexer_4_out));
  Add #(.Bits(16)) add_3 (
    .a({1'b0, multiplexer_3_out[15:1]}), .b(multiplexer_4_out), .c_i(1'b0), .s(add_3_s), .c_o(add_3_c_o[15]));
  Multiplexer #(.Bits(16)) multiplexer_5 (.sel(add_1_s[2]), .in_0({16{1'b0}}), .in_1(add_2_s), .out(multiplexer_5_out));
  Add #(.Bits(16)) add_4 (
    .a({add_3_c_o[15], add_3_s[15:1]}), .b(multiplexer_5_out), .c_i(1'b0), .s(add_4_s), .c_o(add_4_c_o[15]));
  Multiplexer #(.Bits(16)) multiplexer_6 (.sel(add_1_s[3]), .in_0({16{1'b0}}), .in_1(add_2_s), .out(multiplexer_6_out));
  Add #(.Bits(16)) add_5 (
    .a({add_4_c_o[15], add_4_s[15:1]}), .b(multiplexer_6_out), .c_i(1'b0), .s(add_5_s), .c_o(add_5_c_o[15]));
  Multiplexer #(.Bits(16)) multiplexer_7 (.sel(add_1_s[4]), .in_0({16{1'b0}}), .in_1(add_2_s), .out(multiplexer_7_out));
  Add #(.Bits(16)) add_6 (
    .a({add_5_c_o[15], add_5_s[15:1]}), .b(multiplexer_7_out), .c_i(1'b0), .s(add_6_s), .c_o(add_6_c_o[15]));
  Multiplexer #(.Bits(16)) multiplexer_8 (.sel(add_1_s[5]), .in_0({16{1'b0}}), .in_1(add_2_s), .out(multiplexer_8_out));
  Add #(.Bits(16)) add_7 (
    .a({add_6_c_o[15], add_6_s[15:1]}), .b(multiplexer_8_out), .c_i(1'b0), .s(add_7_s), .c_o(add_7_c_o[15]));
  Multiplexer #(.Bits(16)) multiplexer_9 (.sel(add_1_s[6]), .in_0({16{1'b0}}), .in_1(add_2_s), .out(multiplexer_9_out));
  Add #(.Bits(16)) add_8 (
    .a({add_7_c_o[15], add_7_s[15:1]}), .b(multiplexer_9_out), .c_i(1'b0), .s(add_8_s), .c_o(add_8_c_o[15]));
  Multiplexer #(.Bits(16)) multiplexer_10 (
    .sel(add_1_s[7]), .in_0({16{1'b0}}), .in_1(add_2_s), .out(multiplexer_10_out));
  Add #(.Bits(16)) add_9 (
    .a({add_8_c_o[15], add_8_s[15:1]}), .b(multiplexer_10_out), .c_i(1'b0), .s(add_9_s), .c_o(add_9_c_o[15]));
  Multiplexer #(.Bits(16)) multiplexer_11 (
    .sel(add_1_s[8]), .in_0({16{1'b0}}), .in_1(add_2_s), .out(multiplexer_11_out));
  Add #(.Bits(16)) add_10 (
    .a({add_9_c_o[15], add_9_s[15:1]}), .b(multiplexer_11_out), .c_i(1'b0), .s(add_10_s), .c_o(add_10_c_o[15]));
  Multiplexer #(.Bits(16)) multiplexer_12 (
    .sel(add_1_s[9]), .in_0({16{1'b0}}), .in_1(add_2_s), .out(multiplexer_12_out));
  Add #(.Bits(16)) add_11 (
    .a({add_10_c_o[15], add_10_s[15:1]}), .b(multiplexer_12_out), .c_i(1'b0), .s(add_11_s),
    .c_o(add_11_c_o[15]));
  Multiplexer #(.Bits(16)) multiplexer_13 (
    .sel(add_1_s[10]), .in_0({16{1'b0}}), .in_1(add_2_s), .out(multiplexer_13_out));
  Add #(.Bits(16)) add_12 (
    .a({add_11_c_o[15], add_11_s[15:1]}), .b(multiplexer_13_out), .c_i(1'b0), .s(add_12_s),
    .c_o(add_12_c_o[15]));
  Multiplexer #(.Bits(16)) multiplexer_14 (
    .sel(add_1_s[11]), .in_0({16{1'b0}}), .in_1(add_2_s), .out(multiplexer_14_out));
  Add #(.Bits(16)) add_13 (
    .a({add_12_c_o[15], add_12_s[15:1]}), .b(multiplexer_14_out), .c_i(1'b0), .s(add_13_s),
    .c_o(add_13_c_o[15]));
  Multiplexer #(.Bits(16)) multiplexer_15 (
    .sel(add_1_s[12]), .in_0({16{1'b0}}), .in_1(add_2_s), .out(multiplexer_15_out));
  Add #(.Bits(16)) add_14 (
    .a({add_13_c_o[15], add_13_s[15:1]}), .b(multiplexer_15_out), .c_i(1'b0), .s(add_14_s),
    .c_o(add_14_c_o[15]));
  Multiplexer #(.Bits(16)) multiplexer_16 (
    .sel(add_1_s[13]), .in_0({16{1'b0}}), .in_1(add_2_s), .out(multiplexer_16_out));
  Add #(.Bits(16)) add_15 (
    .a({add_14_c_o[15], add_14_s[15:1]}), .b(multiplexer_16_out), .c_i(1'b0), .s(add_15_s),
    .c_o(add_15_c_o[15]));
  Multiplexer #(.Bits(16)) multiplexer_17 (
    .sel(add_1_s[14]), .in_0({16{1'b0}}), .in_1(add_2_s), .out(multiplexer_17_out));
  Add #(.Bits(16)) add_16 (
    .a({add_15_c_o[15], add_15_s[15:1]}), .b(multiplexer_17_out), .c_i(1'b0), .s(add_16_s),
    .c_o(add_16_c_o[15]));
  Multiplexer #(.Bits(16)) multiplexer_18 (
    .sel(add_1_s[15]), .in_0({16{1'b0}}), .in_1(add_2_s), .out(multiplexer_18_out));
  Add #(.Bits(16)) add_17 (
    .a({add_16_c_o[15], add_16_s[15:1]}), .b(multiplexer_18_out), .c_i(1'b0), .s(add_17_s),
    .c_o(add_17_c_o[31]));
  assign not_3_out = ~{add_17_c_o[31], add_17_s, add_16_s[0], add_15_s[0], add_14_s[0], add_13_s[0], add_12_s[0], add_11_s[0], add_10_s[0], add_9_s[0], add_8_s[0], add_7_s[0], add_6_s[0], add_5_s[0], add_4_s[0], add_3_s[0], multiplexer_3_out[0]};  // Not not_3, 32 bits wide
  Multiplexer #(.Bits(32)) multiplexer_19 (
    .sel(xor_1_out),
    .in_0({add_17_c_o[31], add_17_s, add_16_s[0], add_15_s[0], add_14_s[0], add_13_s[0], add_12_s[0], add_11_s[0], add_10_s[0], add_9_s[0], add_8_s[0], add_7_s[0], add_6_s[0], add_5_s[0], add_4_s[0], add_3_s[0], multiplexer_3_out[0]}),
    .in_1(not_3_out), .out(multiplexer_19_out));
  Add #(.Bits(32)) add_18 (.a({32{1'b0}}), .b(multiplexer_19_out), .c_i(xor_1_out), .s({P_H, P_L}));  // open: c_o

  // Notes on the sheet:
  //   P_L: Product Low
  //   P_H: Product High
  //   C: Control
endmodule
