// Digital circuit Access Stage B.dig as structural Verilog
module Access_Stage_B (
  input  [2:0] S,
  input  [8:0] P_X,
  input  [7:0] P_Y,
  input  \Φ_IO ,
  input  \Φ_PX ,
  input  [10:0] C,
  input  [15:0] D_A_2,
  input  [15:0] M_I,
  input  [11:0] M_A,
  input  M_E,
  output [2:0] S_2,
  output [8:0] P_X_2,
  output [7:0] P_Y_2,
  output [10:0] C_2,
  output [15:0] D_A,
  output [15:0] M_O,
  output [15:0] D_B
);

  wire M_3, xor_1_out;
  wire [2:0] add_1_s, add_2_s, multiplexer_2_out, multiplexer_3_out, not_1_out, not_2_out, P_X_t, P_Y_t;
  wire [7:0] multiplexer_5_out;
  wire [8:0] multiplexer_4_out;
  wire [11:0] multiplexer_1_out;
  wire [15:0] ramdualaccess_1_d1, ramdualaccess_1_d2;

  Multiplexer #(.Selector_Bits(2), .Bits(12)) multiplexer_1 (
    .sel(C[10:9]), .in_0({P_Y[6:0], P_X[8:4]}), .in_1({P_Y[6:1], P_X[8:3]}), .in_2({P_Y[7:2], P_X[8:3]}),
    .in_3({D_A_2[7:4], P_Y_t, D_A_2[3:0], P_X_t[2]}), .out(multiplexer_1_out));
  assign not_1_out = ~P_X[2:0];  // Not not_1, 3 bits wide
  assign not_2_out = ~P_Y[2:0];  // Not not_2, 3 bits wide
  Add #(.Bits(3)) add_1 (.a(3'b111), .b(not_1_out), .c_i(1'b1), .s(add_1_s));  // open: c_o
  Add #(.Bits(3)) add_2 (.a(3'b111), .b(not_2_out), .c_i(1'b1), .s(add_2_s));  // open: c_o
  and and_1 (M_3, C[9], C[10]);
  Multiplexer #(.Bits(3)) multiplexer_2 (.sel(D_A_2[13]), .in_0(P_X[2:0]), .in_1(add_1_s), .out(multiplexer_2_out));
  Multiplexer #(.Bits(3)) multiplexer_3 (.sel(xor_1_out), .in_0(P_Y[2:0]), .in_1(add_2_s), .out(multiplexer_3_out));
  Register #(.Bits(3)) register_1 (.D(S), .C(\Φ_PX ), .en(1'b1), .Q(S_2));
  Register #(.Bits(11)) register_2 (.D(C), .C(\Φ_PX ), .en(1'b1), .Q(C_2));
  Multiplexer #(.Bits(9)) multiplexer_4 (.sel(M_3), .in_0(P_X), .in_1({P_X[8:3], P_X_t}), .out(multiplexer_4_out));
  Multiplexer #(.Bits(8)) multiplexer_5 (.sel(M_3), .in_0(P_Y), .in_1({P_Y[7:3], P_Y_t}), .out(multiplexer_5_out));
  Register #(.Bits(16)) register_3 (.D(D_A_2), .C(\Φ_PX ), .en(1'b1), .Q(D_A));
  Register #(.Bits(16)) register_4 (.D(ramdualaccess_1_d1), .C(\Φ_IO ), .en(1'b1), .Q(M_O));
  RAMDualAccess #(.AddrBits(12), .isProgramMemory("true"), .Bits(16)) ramdualaccess_1 (
    .str(M_E), .C(\Φ_IO ), .ld(1'b1), .A1(M_A), .Din1(M_I), .A2(multiplexer_1_out), .D1(ramdualaccess_1_d1),
    .D2(ramdualaccess_1_d2));
  xor xor_1 (xor_1_out, D_A_2[14], D_A_2[15]);
  Multiplexer #(.Bits(3)) multiplexer_6 (
    .sel(D_A_2[15]), .in_0(multiplexer_2_out), .in_1(multiplexer_3_out), .out(P_X_t));
  Multiplexer #(.Bits(3)) multiplexer_7 (
    .sel(D_A_2[15]), .in_0(multiplexer_3_out), .in_1(multiplexer_2_out), .out(P_Y_t));
  Register #(.Bits(9)) register_5 (.D(multiplexer_4_out), .C(\Φ_PX ), .en(1'b1), .Q(P_X_2));
  Register #(.Bits(8)) register_6 (.D(multiplexer_5_out), .C(\Φ_PX ), .en(1'b1), .Q(P_Y_2));
  Register #(.Bits(16)) register_7 (.D(ramdualaccess_1_d2), .C(\Φ_PX ), .en(1'b1), .Q(D_B));

  // Other names for the same wires on the sheet: D_A_t[15:0] = D_A_2; P_X_t[8:3] = P_X[8:3]; P_Y_t[7:3] = P_Y[7:3]

  // Notes on the sheet:
  //   S: Sync Signals
  //   P_X: X Position
  //   P_Y: Y Posititon
  //   Φ_IO: IO Clock
  //   S_2: Sync Signals
  //   Φ_PX: Pixel Clock
  //   C: Control Word
  //   P_X_2: X Position
  //   P_Y_2: Y Position
  //   C_2: Control Word
  //   D_A: Data Output Part A
  //   D_A_2: Data Input Part A
  //   M_I: VRAM Data Input
  //   M_A: VRAM Address
  //   M_E: VRAM Write Enable
  //   M_O: VRAM Data Output
  //   D_B: Data Output Part B
  //   Mode Selection
  //   Character Mode
  //   Flip X
  //   Flip Y
  //   I/O
  //   VRAM Part B
  //   Rotate
endmodule
