// Digital circuit Parts.dig as structural Verilog
module Parts (
  input  Long_Mode
);

  wire and_1_out, comparator_1_eq, undriven_3, \Φ ;
  wire [0:0] and_2_out, undriven_2;
  wire [3:0] bcd_encoder_1_d_0, bcd_encoder_1_d_0_2, bcd_encoder_1_d_1, bcd_encoder_1_d_1_2;
  wire [7:0] bcd_encoder_1_d_2, bcd_encoder_1_d_3, bcd_encoder_1_d_4, undriven;
  wire [15:0] display_peripheral_1_num;

  Display_Peripheral display_peripheral_1 (
    .A_h({8{1'b1}}), .A_l(8'hfe), .\Φ (\Φ ), .NUM(display_peripheral_1_num), .M(Long_Mode));  // open: C_m, C_m_2, A, D
  BCD_Encoder bcd_encoder_1 (
    .NUM(display_peripheral_1_num), .D_0({bcd_encoder_1_d_0_2, bcd_encoder_1_d_0}),
    .D_1({bcd_encoder_1_d_1_2, bcd_encoder_1_d_1}), .D_2(bcd_encoder_1_d_2), .D_3(bcd_encoder_1_d_3),
    .D_4(bcd_encoder_1_d_4));
  Seven_Seg seven_seg_1 (
    .a(bcd_encoder_1_d_4[0]), .b(bcd_encoder_1_d_4[1]), .c(bcd_encoder_1_d_4[2]), .d(bcd_encoder_1_d_4[3]),
    .e(bcd_encoder_1_d_4[4]), .f(bcd_encoder_1_d_4[5]), .g(bcd_encoder_1_d_4[6]), .dp(bcd_encoder_1_d_4[7]));
  Seven_Seg seven_seg_2 (
    .a(bcd_encoder_1_d_3[0]), .b(bcd_encoder_1_d_3[1]), .c(bcd_encoder_1_d_3[2]), .d(bcd_encoder_1_d_3[3]),
    .e(bcd_encoder_1_d_3[4]), .f(bcd_encoder_1_d_3[5]), .g(bcd_encoder_1_d_3[6]), .dp(bcd_encoder_1_d_3[7]));
  Seven_Seg seven_seg_3 (
    .a(bcd_encoder_1_d_2[0]), .b(bcd_encoder_1_d_2[1]), .c(bcd_encoder_1_d_2[2]), .d(bcd_encoder_1_d_2[3]),
    .e(bcd_encoder_1_d_2[4]), .f(bcd_encoder_1_d_2[5]), .g(bcd_encoder_1_d_2[6]), .dp(bcd_encoder_1_d_2[7]));
  Seven_Seg seven_seg_4 (
    .a(bcd_encoder_1_d_1[0]), .b(bcd_encoder_1_d_1[1]), .c(bcd_encoder_1_d_1[2]), .d(bcd_encoder_1_d_1[3]),
    .e(bcd_encoder_1_d_1_2[0]), .f(bcd_encoder_1_d_1_2[1]), .g(bcd_encoder_1_d_1_2[2]),
    .dp(bcd_encoder_1_d_1_2[3]));
  Seven_Seg seven_seg_5 (
    .a(bcd_encoder_1_d_0[0]), .b(bcd_encoder_1_d_0[1]), .c(bcd_encoder_1_d_0[2]), .d(bcd_encoder_1_d_0[3]),
    .e(bcd_encoder_1_d_0_2[0]), .f(bcd_encoder_1_d_0_2[1]), .g(bcd_encoder_1_d_0_2[2]),
    .dp(bcd_encoder_1_d_0_2[3]));
  Comparator #(.Bits(8)) comparator_1 (.a({8{1'b1}}), .b(undriven), .eq(comparator_1_eq));  // open: gt, lt
  and and_1 (and_1_out, comparator_1_eq, undriven_2[0]);
  and and_2 (and_2_out[0], ~and_1_out, undriven_2[0]);  // And
  Telnet telnet_1 (.in(undriven_3), .C(\Φ ), .wr(and_1_out), .rd(1'b1));  // open: out, av

  // Notes on the sheet:
  //   Output Display
  //   Mapped @ FF:FE
endmodule
