// Digital circuit Smolproc.dig as structural Verilog
module Smolproc (
  input  clk
);

  wire and_1_out, comparator_1_eq, decode_stage_1_c_w, execute_stage_1_c_w_2, execute_stage_1_je,
       forwarding_unit_1_f_a, forwarding_unit_1_f_b, H, memory_stage_1_c_w, multiplexer_1_out, Q_out,
       t_ff_1_q, W_out, \Φ ;
  wire [0:0] and_2_out;
  wire [1:0] decode_stage_1_a_a, decode_stage_1_a_b, decode_stage_1_c_m, decode_stage_1_ra_a,
       decode_stage_1_ra_b, execute_stage_1_a, execute_stage_1_c_m_2, memory_stage_1_a;
  wire [6:0] decode_stage_1_c_x;
  wire [7:0] bcd_encoder_1_d_0, bcd_encoder_1_d_1, bcd_encoder_1_d_2, bcd_encoder_1_d_3, bcd_encoder_1_d_4,
       decode_stage_1_d_a, decode_stage_1_d_b, decode_stage_1_im_2, decode_stage_1_wa_2, execute_stage_1_d,
       execute_stage_1_d_a_2, execute_stage_1_ja, execute_stage_1_sp, fetch_stage_1_ma, fetch_stage_1_wa,
       fetch_stage_1_wd, forwarding_unit_1_d_a_2, forwarding_unit_1_d_b_2, memory_stage_1_d,
       memory_stage_1_pd, regfile_1_r_0, regfile_1_r_1, regfile_1_r_2, regfile_1_r_3, regfile_1_rd_a,
       regfile_1_rd_b;
  wire [15:0] counter_1_out;

  Fetch_Stage fetch_stage_1 (
    .JA(execute_stage_1_ja), .JE(execute_stage_1_je), .MA(fetch_stage_1_ma), .WA(fetch_stage_1_wa),
    .MD(memory_stage_1_pd), .WD(fetch_stage_1_wd), .\Φ (\Φ ));
  Decode_Stage decode_stage_1 (
    .WA(fetch_stage_1_wa), .IM(memory_stage_1_pd), .WD(fetch_stage_1_wd), .RA_a(decode_stage_1_ra_a),
    .RA_b(decode_stage_1_ra_b), .RD_a(regfile_1_rd_a), .RD_b(regfile_1_rd_b), .A_a(decode_stage_1_a_a),
    .D_a(decode_stage_1_d_a), .D_b(decode_stage_1_d_b), .WA_2(decode_stage_1_wa_2), .\Φ (\Φ ),
    .C_x(decode_stage_1_c_x), .C_m(decode_stage_1_c_m), .C_w(decode_stage_1_c_w), .IM_2(decode_stage_1_im_2),
    .A_b(decode_stage_1_a_b), .H(H));
  Regfile regfile_1 (
    .RD_a(regfile_1_rd_a), .RA_a(decode_stage_1_ra_a), .RA_b(decode_stage_1_ra_b), .WA(memory_stage_1_a),
    .RD_b(regfile_1_rd_b), .WD(memory_stage_1_d), .WE(memory_stage_1_c_w), .\Φ (\Φ ), .R_0(regfile_1_r_0),
    .R_1(regfile_1_r_1), .R_2(regfile_1_r_2), .R_3(regfile_1_r_3));
  // Probe on regfile_1_r_0
  // Probe on regfile_1_r_1
  // Probe on regfile_1_r_2
  // Probe on regfile_1_r_3
  Comparator #(.Bits(8)) comparator_1 (.a({8{1'b1}}), .b(execute_stage_1_d), .eq(comparator_1_eq));  // open: gt, lt
  and and_1 (and_1_out, comparator_1_eq, execute_stage_1_c_m_2[0]);
  Execute_Stage execute_stage_1 (
    .WA(decode_stage_1_wa_2), .C_w(decode_stage_1_c_w), .C_m(decode_stage_1_c_m), .C_x(decode_stage_1_c_x),
    .IM(decode_stage_1_im_2), .A_a(decode_stage_1_a_a), .D_a(forwarding_unit_1_d_a_2),
    .D_b(forwarding_unit_1_d_b_2), .C_w_2(execute_stage_1_c_w_2), .C_m_2(execute_stage_1_c_m_2), .\Φ (\Φ ),
    .A(execute_stage_1_a), .D(execute_stage_1_d), .D_a_2(execute_stage_1_d_a_2), .JA(execute_stage_1_ja),
    .JE(execute_stage_1_je), .SP(execute_stage_1_sp));
  Forwarding_Unit forwarding_unit_1 (
    .A_a(decode_stage_1_a_a), .A_b(decode_stage_1_a_b), .D_a(decode_stage_1_d_a), .D_b(decode_stage_1_d_b),
    .D_a_2(forwarding_unit_1_d_a_2), .D_B_2(forwarding_unit_1_d_b_2), .D_m(execute_stage_1_d),
    .A_m(execute_stage_1_a), .W_m(execute_stage_1_c_w_2), .D_w(memory_stage_1_d), .A_w(memory_stage_1_a),
    .W_w(memory_stage_1_c_w), .F_b(forwarding_unit_1_f_b), .F_a(forwarding_unit_1_f_a));
  // Probe on execute_stage_1_sp
  Telnet telnet_1 (.in(execute_stage_1_d_a_2), .C(\Φ ), .wr(and_1_out), .rd(1'b1));  // open: out, av
  and and_2 (and_2_out[0], ~and_1_out, execute_stage_1_c_m_2[0]);  // And
  Button W (.out(W_out));
  Memory_Stage memory_stage_1 (
    .C_w(memory_stage_1_c_w), .A(memory_stage_1_a), .D(memory_stage_1_d), .C_w_2(execute_stage_1_c_w_2),
    .C_m({execute_stage_1_c_m_2[1], and_2_out[0]}), .A_2(execute_stage_1_a), .D_2(execute_stage_1_d),
    .D_a(execute_stage_1_d_a_2), .\Φ (\Φ ), .PA(fetch_stage_1_ma), .PD(memory_stage_1_pd));
  // Probe on forwarding_unit_1_f_a
  // Probe on forwarding_unit_1_f_b
  Multiplexer multiplexer_1 (.sel(t_ff_1_q), .in_0(Q_out), .in_1(clk), .out(multiplexer_1_out));
  Button Q (.out(Q_out));
  T_FF #(.withEnable("false")) t_ff_1 (.C(W_out), .Q(t_ff_1_q));  // open: nQ
  Counter #(.Bits(16)) counter_1 (.en(1'b1), .C(\Φ ), .clr(1'b0), .out(counter_1_out));  // open: ovf
  Multiplexer multiplexer_2 (.sel(H), .in_0(multiplexer_1_out), .in_1(1'b0), .out(\Φ ));
  BCD_Encoder bcd_encoder_1 (
    .NUM(counter_1_out), .D_0(bcd_encoder_1_d_0), .D_1(bcd_encoder_1_d_1), .D_2(bcd_encoder_1_d_2),
    .D_3(bcd_encoder_1_d_3), .D_4(bcd_encoder_1_d_4));
  LED led_1 (.in(H));
  Seven_Seg seven_seg_1 (
    .a(bcd_encoder_1_d_4[0]), .b(bcd_encoder_1_d_4[1]), .c(bcd_encoder_1_d_4[2]), .d(bcd_encoder_1_d_4[3]),
    .e(bcd_encoder_1_d_4[4]), .f(bcd_encoder_1_d_4[5]), .g(bcd_encoder_1_d_4[6]), .dp(bcd_encoder_1_d_4[7]));
  Seven_Seg seven_seg_2 (
    .a(bcd_encoder_1_d_3[0]), .b(bcd_encoder_1_d_3[1]), .c(bcd_encoder_1_d_3[2]), .d(bcd_encoder_1_d_3[3]),
    .e(bcd_encoder_1_d_3[4]), .f(bcd_encoder_1_d_3[5]), .g(bcd_encoder_1_d_3[6]), .dp(bcd_encoder_1_d_3[7]));
  Seven_Seg seven_seg_3 (
    .a(bcd_encoder_1_d_2[0]), .b(bcd_encoder_1_d_2[1]), .c(bcd_encoder_1_d_2[2]), .d(bcd_encoder_1_d_2[3]),
    .e(bcd_encoder_1_d_2[4]), .f(bcd_encoder_1_d_2[5]), .g(bcd_encoder_1_d_2[6]), .dp(bcd_encoder_1_d_2[7]));
  Seven_Seg seven_seg_4 (
    .a(bcd_encoder_1_d_1[0]), .b(bcd_encoder_1_d_1[1]), .c(bcd_encoder_1_d_1[2]), .d(bcd_encoder_1_d_1[3]),
    .e(bcd_encoder_1_d_1[4]), .f(bcd_encoder_1_d_1[5]), .g(bcd_encoder_1_d_1[6]), .dp(bcd_encoder_1_d_1[7]));
  Seven_Seg seven_seg_5 (
    .a(bcd_encoder_1_d_0[0]), .b(bcd_encoder_1_d_0[1]), .c(bcd_encoder_1_d_0[2]), .d(bcd_encoder_1_d_0[3]),
    .e(bcd_encoder_1_d_0[4]), .f(bcd_encoder_1_d_0[5]), .g(bcd_encoder_1_d_0[6]), .dp(bcd_encoder_1_d_0[7]));

  // Notes on the sheet:
  //   clk: Hz: 1000
  //   Write-Back
  //   Clock Counter
endmodule
