// Digital circuit BCD Encoder.dig as structural Verilog
module BCD_Encoder (
  input  [15:0] NUM,
  output [7:0] D_0,
  output [7:0] D_1,
  output [7:0] D_2,
  output [7:0] D_3,
  output [7:0] D_4
);

  wire and_1_out, B_1, B_2, B_3, B_4, comparator_1_eq, comparator_2_eq, comparator_3_eq, comparator_4_eq,
       comparator_5_eq;
  wire [2:0] rom_1_d, rom_2_d;
  wire [2:1] rom_1_d_2;
  wire [3:0] multiplexer_1_out, multiplexer_2_out, multiplexer_3_out, multiplexer_4_out, multiplexer_5_out,
       rom_3_d, rom_4_d, rom_5_d, rom_6_d, rom_7_d, rom_8_d, rom_9_d, rom_10_d, rom_11_d, rom_12_d, rom_13_d,
       rom_14_d, rom_15_d, rom_16_d, rom_17_d, rom_18_d, rom_19_d, rom_20_d, rom_21_d, rom_22_d, rom_23_d,
       rom_24_d, rom_25_d, rom_26_d, rom_27_d, rom_28_d, rom_29_d, rom_30_d, rom_31_d, rom_32_d, rom_33_d,
       rom_34_d;

  ROM #(.AddrBits(4), .Bits(4)) rom_1 (.A({1'b0, NUM[15:13]}), .sel(1'b1), .D({rom_1_d_2[2], rom_1_d}));
  ROM #(.AddrBits(4), .Bits(4)) rom_2 (.A({rom_1_d, NUM[12]}), .sel(1'b1), .D({rom_1_d_2[1], rom_2_d}));
  ROM #(.AddrBits(4), .Bits(4)) rom_3 (.A({rom_2_d, NUM[11]}), .sel(1'b1), .D(rom_3_d));
  ROM #(.AddrBits(4), .Bits(4)) rom_4 (.A({rom_3_d[2:0], NUM[10]}), .sel(1'b1), .D(rom_4_d));
  ROM #(.AddrBits(4), .Bits(4)) rom_5 (.A({1'b0, rom_1_d_2, rom_3_d[3]}), .sel(1'b1), .D(rom_5_d));
  ROM #(.AddrBits(4), .Bits(4)) rom_6 (.A({rom_4_d[2:0], NUM[9]}), .sel(1'b1), .D(rom_6_d));
  ROM #(.AddrBits(4), .Bits(4)) rom_7 (.A({rom_5_d[2:0], rom_4_d[3]}), .sel(1'b1), .D(rom_7_d));
  ROM #(.AddrBits(4), .Bits(4)) rom_8 (.A({rom_6_d[2:0], NUM[8]}), .sel(1'b1), .D(rom_8_d));
  ROM #(.AddrBits(4), .Bits(4)) rom_9 (.A({rom_7_d[2:0], rom_6_d[3]}), .sel(1'b1), .D(rom_9_d));
  ROM #(.AddrBits(4), .Bits(4)) rom_10 (.A({rom_8_d[2:0], NUM[7]}), .sel(1'b1), .D(rom_10_d));
  ROM #(.AddrBits(4), .Bits(4)) rom_11 (.A({rom_9_d[2:0], rom_8_d[3]}), .sel(1'b1), .D(rom_11_d));
  ROM #(.AddrBits(4), .Bits(4)) rom_12 (.A({1'b0, rom_5_d[3], rom_7_d[3], rom_9_d[3]}), .sel(1'b1), .D(rom_12_d));
  ROM #(.AddrBits(4), .Bits(4)) rom_13 (.A({rom_10_d[2:0], NUM[6]}), .sel(1'b1), .D(rom_13_d));
  ROM #(.AddrBits(4), .Bits(4)) rom_14 (.A({rom_11_d[2:0], rom_10_d[3]}), .sel(1'b1), .D(rom_14_d));
  ROM #(.AddrBits(4), .Bits(4)) rom_15 (.A({rom_12_d[2:0], rom_11_d[3]}), .sel(1'b1), .D(rom_15_d));
  ROM #(.AddrBits(4), .Bits(4)) rom_16 (.A({rom_13_d[2:0], NUM[5]}), .sel(1'b1), .D(rom_16_d));
  ROM #(.AddrBits(4), .Bits(4)) rom_17 (.A({rom_14_d[2:0], rom_13_d[3]}), .sel(1'b1), .D(rom_17_d));
  ROM #(.AddrBits(4), .Bits(4)) rom_18 (.A({rom_15_d[2:0], rom_14_d[3]}), .sel(1'b1), .D(rom_18_d));
  ROM #(.AddrBits(4), .Bits(4)) rom_19 (.A({rom_16_d[2:0], NUM[4]}), .sel(1'b1), .D(rom_19_d));
  ROM #(.AddrBits(4), .Bits(4)) rom_20 (.A({rom_17_d[2:0], rom_16_d[3]}), .sel(1'b1), .D(rom_20_d));
  ROM #(.AddrBits(4), .Bits(4)) rom_21 (.A({rom_18_d[2:0], rom_17_d[3]}), .sel(1'b1), .D(rom_21_d));
  ROM #(.AddrBits(4), .Bits(4)) rom_22 (.A({1'b0, rom_12_d[3], rom_15_d[3], rom_18_d[3]}), .sel(1'b1), .D(rom_22_d));
  ROM #(.AddrBits(4), .Bits(4)) rom_23 (.A({rom_19_d[2:0], NUM[3]}), .sel(1'b1), .D(rom_23_d));
  ROM #(.AddrBits(4), .Bits(4)) rom_24 (.A({rom_20_d[2:0], rom_19_d[3]}), .sel(1'b1), .D(rom_24_d));
  ROM #(.AddrBits(4), .Bits(4)) rom_25 (.A({rom_21_d[2:0], rom_20_d[3]}), .sel(1'b1), .D(rom_25_d));
  ROM #(.AddrBits(4), .Bits(4)) rom_26 (.A({rom_22_d[2:0], rom_21_d[3]}), .sel(1'b1), .D(rom_26_d));
  ROM #(.AddrBits(4), .Bits(4)) rom_27 (.A({rom_23_d[2:0], NUM[2]}), .sel(1'b1), .D(rom_27_d));
  ROM #(.AddrBits(4), .Bits(4)) rom_28 (.A({rom_24_d[2:0], rom_23_d[3]}), .sel(1'b1), .D(rom_28_d));
  ROM #(.AddrBits(4), .Bits(4)) rom_29 (.A({rom_25_d[2:0], rom_24_d[3]}), .sel(1'b1), .D(rom_29_d));
  ROM #(.AddrBits(4), .Bits(4)) rom_30 (.A({rom_26_d[2:0], rom_25_d[3]}), .sel(1'b1), .D(rom_30_d));
  ROM #(.AddrBits(4), .Bits(4)) rom_31 (.A({rom_27_d[2:0], NUM[1]}), .sel(1'b1), .D(rom_31_d));
  ROM #(.AddrBits(4), .Bits(4)) rom_32 (.A({rom_28_d[2:0], rom_27_d[3]}), .sel(1'b1), .D(rom_32_d));
  ROM #(.AddrBits(4), .Bits(4)) rom_33 (.A({rom_29_d[2:0], rom_28_d[3]}), .sel(1'b1), .D(rom_33_d));
  ROM #(.AddrBits(4), .Bits(4)) rom_34 (.A({rom_30_d[2:0], rom_29_d[3]}), .sel(1'b1), .D(rom_34_d));
  Comparator #(.Bits(4)) comparator_1 (.a({rom_31_d[2:0], NUM[0]}), .b(4'b0000), .eq(comparator_1_eq));  // open: gt, lt
  Comparator #(.Bits(4)) comparator_2 (
    .a({rom_32_d[2:0], rom_31_d[3]}), .b(4'b0000), .eq(comparator_2_eq));  // open: gt, lt
  Comparator #(.Bits(4)) comparator_3 (
    .a({rom_33_d[2:0], rom_32_d[3]}), .b(4'b0000), .eq(comparator_3_eq));  // open: gt, lt
  Comparator #(.Bits(4)) comparator_4 (
    .a({rom_34_d[2:0], rom_33_d[3]}), .b(4'b0000), .eq(comparator_4_eq));  // open: gt, lt
  Comparator #(.Bits(4)) comparator_5 (
    .a({rom_22_d[3], rom_26_d[3], rom_30_d[3], rom_34_d[3]}), .b(4'b0000), .eq(comparator_5_eq));  // open: gt, lt
  and and_1 (and_1_out, comparator_1_eq, B_1);
  and and_2 (B_1, comparator_2_eq, B_2);
  and and_3 (B_2, comparator_3_eq, B_3);
  and and_4 (B_3, comparator_4_eq, B_4);
  and and_5 (B_4, comparator_5_eq, 1'b1);
  Multiplexer #(.Bits(4)) multiplexer_1 (
    .sel(and_1_out), .in_0({rom_31_d[2:0], NUM[0]}), .in_1(4'b0000), .out(multiplexer_1_out));
  Multiplexer #(.Bits(4)) multiplexer_2 (
    .sel(B_1), .in_0({rom_32_d[2:0], rom_31_d[3]}), .in_1(4'b1111), .out(multiplexer_2_out));
  Multiplexer #(.Bits(4)) multiplexer_3 (
    .sel(B_2), .in_0({rom_33_d[2:0], rom_32_d[3]}), .in_1(4'b1111), .out(multiplexer_3_out));
  Multiplexer #(.Bits(4)) multiplexer_4 (
    .sel(B_3), .in_0({rom_34_d[2:0], rom_33_d[3]}), .in_1(4'b1111), .out(multiplexer_4_out));
  Multiplexer #(.Bits(4)) multiplexer_5 (
    .sel(B_4), .in_0({rom_22_d[3], rom_26_d[3], rom_30_d[3], rom_34_d[3]}), .in_1(4'b1111),
    .out(multiplexer_5_out));
  ROM #(.AddrBits(4), .Bits(8)) rom_35 (.A(multiplexer_1_out), .sel(1'b1), .D(D_0));
  ROM #(.AddrBits(4), .Bits(8)) rom_36 (.A(multiplexer_2_out), .sel(1'b1), .D(D_1));
  ROM #(.AddrBits(4), .Bits(8)) rom_37 (.A(multiplexer_3_out), .sel(1'b1), .D(D_2));
  ROM #(.AddrBits(4), .Bits(8)) rom_38 (.A(multiplexer_4_out), .sel(1'b1), .D(D_3));
  ROM #(.AddrBits(4), .Bits(8)) rom_39 (.A(multiplexer_5_out), .sel(1'b1), .D(D_4));

  // Notes on the sheet:
  //   NUM: Binary Number Input
  //   D_0: Digit 0
  //   D_1: Digit 1
  //   D_2: Digit 2
  //   D_3: Digit 3
  //   D_4: Digit 4
  //   contents of rom_1 (hex, n*v repeats v):
  //   0,1,2,3,4,8,9,a,b,c
  //   contents of rom_2 (hex, n*v repeats v):
  //   0,1,2,3,4,8,9,a,b,c
  //   contents of rom_3 (hex, n*v repeats v):
  //   0,1,2,3,4,8,9,a,b,c
  //   contents of rom_4 (hex, n*v repeats v):
  //   0,1,2,3,4,8,9,a,b,c
  //   contents of rom_5 (hex, n*v repeats v):
  //   0,1,2,3,4,8,9,a,b,c
  //   contents of rom_6 (hex, n*v repeats v):
  //   0,1,2,3,4,8,9,a,b,c
  //   contents of rom_7 (hex, n*v repeats v):
  //   0,1,2,3,4,8,9,a,b,c
  //   contents of rom_8 (hex, n*v repeats v):
  //   0,1,2,3,4,8,9,a,b,c
  //   contents of rom_9 (hex, n*v repeats v):
  //   0,1,2,3,4,8,9,a,b,c
  //   contents of rom_10 (hex, n*v repeats v):
  //   0,1,2,3,4,8,9,a,b,c
  //   contents of rom_11 (hex, n*v repeats v):
  //   0,1,2,3,4,8,9,a,b,c
  //   contents of rom_12 (hex, n*v repeats v):
  //   0,1,2,3,4,8,9,a,b,c
  //   contents of rom_13 (hex, n*v repeats v):
  //   0,1,2,3,4,8,9,a,b,c
  //   contents of rom_14 (hex, n*v repeats v):
  //   0,1,2,3,4,8,9,a,b,c
  //   contents of rom_15 (hex, n*v repeats v):
  //   0,1,2,3,4,8,9,a,b,c
  //   contents of rom_16 (hex, n*v repeats v):
  //   0,1,2,3,4,8,9,a,b,c
  //   contents of rom_17 (hex, n*v repeats v):
  //   0,1,2,3,4,8,9,a,b,c
  //   contents of rom_18 (hex, n*v repeats v):
  //   0,1,2,3,4,8,9,a,b,c
  //   contents of rom_19 (hex, n*v repeats v):
  //   0,1,2,3,4,8,9,a,b,c
  //   contents of rom_20 (hex, n*v repeats v):
  //   0,1,2,3,4,8,9,a,b,c
  //   contents of rom_21 (hex, n*v repeats v):
  //   0,1,2,3,4,8,9,a,b,c
  //   contents of rom_22 (hex, n*v repeats v):
  //   0,1,2,3,4,8,9,a,b,c
  //   contents of rom_23 (hex, n*v repeats v):
  //   0,1,2,3,4,8,9,a,b,c
  //   contents of rom_24 (hex, n*v repeats v):
  //   0,1,2,3,4,8,9,a,b,c
  //   contents of rom_25 (hex, n*v repeats v):
  //   0,1,2,3,4,8,9,a,b,c
  //   contents of rom_26 (hex, n*v repeats v):
  //   0,1,2,3,4,8,9,a,b,c
  //   contents of rom_27 (hex, n*v repeats v):
  //   0,1,2,3,4,8,9,a,b,c
  //   contents of rom_28 (hex, n*v repeats v):
  //   0,1,2,3,4,8,9,a,b,c
  //   contents of rom_29 (hex, n*v repeats v):
  //   0,1,2,3,4,8,9,a,b,c
  //   contents of rom_30 (hex, n*v repeats v):
  //   0,1,2,3,4,8,9,a,b,c
  //   contents of rom_31 (hex, n*v repeats v):
  //   0,1,2,3,4,8,9,a,b,c
  //   contents of rom_32 (hex, n*v repeats v):
  //   0,1,2,3,4,8,9,a,b,c
  //   contents of rom_33 (hex, n*v repeats v):
  //   0,1,2,3,4,8,9,a,b,c
  //   contents of rom_34 (hex, n*v repeats v):
  //   0,1,2,3,4,8,9,a,b,c
  //   contents of rom_35 (hex, n*v repeats v):
  //   3f,6,5b,4f,66,6d,7d,7,7f,6f
  //   contents of rom_36 (hex, n*v repeats v):
  //   3f,6,5b,4f,66,6d,7d,7,7f,6f
  //   contents of rom_37 (hex, n*v repeats v):
  //   3f,6,5b,4f,66,6d,7d,7,7f,6f
  //   contents of rom_38 (hex, n*v repeats v):
  //   3f,6,5b,4f,66,6d,7d,7,7f,6f
  //   contents of rom_39 (hex, n*v repeats v):
  //   3f,6,5b,4f,66,6d,7d,7,7f,6f
endmodule
