// Digital circuit Decode Stage.dig as structural Verilog
module Decode_Stage (
  input  [7:0] WA,
  input  [7:0] IM,
  input  [7:0] WD,
  input  [7:0] RD_a,
  input  [7:0] RD_b,
  input  \Φ ,
  output [1:0] RA_a,
  output [1:0] RA_b,
  output [1:0] A_a,
  output [7:0] D_a,
  output [7:0] D_b,
  output [7:0] WA_2,
  output [6:0] C_x,
  output [1:0] C_m,
  output C_w,
  output [7:0] IM_2,
  output [1:0] A_b,
  output H
);

  wire [4:0] multiplexer_1_out;
  wire [10:10] register_7_q;
  wire [11:0] multiplexer_2_out, rom_1_d;

  Register #(.Bits(8)) register_1 (.D(WA), .C(\Φ ), .en(1'b1), .Q(WA_2));
  Register #(.Bits(8)) register_2 (.D(IM), .C(\Φ ), .en(1'b1), .Q(IM_2));
  Register #(.Bits(8)) register_3 (.D(RD_a), .C(\Φ ), .en(1'b1), .Q(D_a));
  Register #(.Bits(8)) register_4 (.D(RD_b), .C(\Φ ), .en(1'b1), .Q(D_b));
  nand nand_1 (multiplexer_1_out[4], WD[6], WD[7]);
  Register #(.Bits(2)) register_5 (.D(WD[1:0]), .C(\Φ ), .en(1'b1), .Q(A_a));
  Register #(.Bits(2)) register_6 (.D(WD[3:2]), .C(\Φ ), .en(1'b1), .Q(A_b));
  Multiplexer #(.Bits(4)) multiplexer_1 (
    .sel(multiplexer_1_out[4]), .in_0(WD[5:2]), .in_1(WD[7:4]), .out(multiplexer_1_out[3:0]));
  ROM #(.AddrBits(5), .Bits(12)) rom_1 (.A(multiplexer_1_out), .sel(1'b1), .D(rom_1_d));
  Multiplexer #(.Bits(12)) multiplexer_2 (
    .sel(register_7_q[10]), .in_0(rom_1_d), .in_1({12{1'b0}}), .out(multiplexer_2_out));
  Register #(.Bits(12)) register_7 (
    .D(multiplexer_2_out), .C(\Φ ), .en(1'b1), .Q({H, register_7_q[10], C_m, C_w, C_x}));

  assign RA_a = WD[1:0];
  assign RA_b = WD[3:2];

  // Notes on the sheet:
  //   WA: Program Word Address
  //   IM: Immediate
  //   WD: Program Word Data
  //   RA_a: Register Read Address Port A
  //   RA_b: Register Read Address Port A
  //   RD_a: Register Read Data Port A
  //   RD_b: Register Read Data Port B
  //   A_a: Originating Register Address Port A
  //   D_a: Originating Register Data Port A
  //   D_b: Originating Register Data Port B
  //   WA_2: Program Word Address
  //   Φ: Clock
  //   C_x: Execute Stage Control
  //   C_m: Memory Stage Control
  //   C_w: Write-Back Stage Control
  //   IM_2: Immediate
  //   A_b: Originating Register Address Port B
  //   H: Halt
  //   dmm wxxx xxxx
  //   contents of rom_1 (hex, n*v repeats v):
  //   88,89,490,494,10c,28d,f,472,c0,69,471,473,530,6b0,4b0,800,80,82
  //   ,81,83,84,85,86,87,8a,463,520,6a0
endmodule
