// Digital circuit Display Peripheral.dig as structural Verilog
module Display_Peripheral (
  input  [1:0] C_m_2,
  input  [7:0] A_h,
  input  [7:0] A_l,
  input  [7:0] A,
  input  [7:0] D,
  input  \Φ ,
  input  M,
  output [1:0] C_m,
  output [15:0] NUM
);

  wire and_1_out, and_2_out, comparator_1_eq, comparator_2_eq, nor_1_out;
  wire [7:0] register_1_q, register_2_q, register_3_q;

  Comparator #(.Bits(8)) comparator_1 (.a(A_l), .b(A), .eq(comparator_1_eq));  // open: gt, lt
  Comparator #(.Bits(8)) comparator_2 (.a(A_h), .b(A), .eq(comparator_2_eq));  // open: gt, lt
  and and_1 (and_1_out, M, C_m_2[0], comparator_1_eq);
  and and_2 (and_2_out, comparator_2_eq, C_m_2[0]);
  and and_3 (C_m[0], nor_1_out, C_m_2[0]);
  nor nor_1 (nor_1_out, and_1_out, and_2_out);
  Register #(.Bits(8)) register_1 (.D(D), .C(\Φ ), .en(and_1_out), .Q(register_1_q));
  Register #(.Bits(8)) register_2 (.D(register_1_q), .C(\Φ ), .en(and_2_out), .Q(register_2_q));
  Register #(.Bits(8)) register_3 (.D(D), .C(\Φ ), .en(and_2_out), .Q(register_3_q));
  Multiplexer #(.Bits(8)) multiplexer_1 (.sel(M), .in_0(register_3_q), .in_1(register_2_q), .out(NUM[7:0]));
  Multiplexer #(.Bits(8)) multiplexer_2 (.sel(M), .in_0({8{1'b0}}), .in_1(register_3_q), .out(NUM[15:8]));

  assign C_m[1] = C_m_2[1];

  // Notes on the sheet:
  //   A_h: High Word Address
  //   A_l: Low Word Address
  //   A: Address
  //   D: Data
  //   Φ: Clock
  //   NUM: Number
  //   M: Display Mode
endmodule
