// Digital circuit Execute Stage.dig as structural Verilog
module Execute_Stage (
  input  [7:0] WA,
  input  C_w,
  input  [1:0] C_m,
  input  [6:0] C_x,
  input  [7:0] IM,
  input  [1:0] A_a,
  input  [7:0] D_a,
  input  [7:0] D_b,
  input  \Φ ,
  output C_w_2,
  output [1:0] C_m_2,
  output [1:0] A,
  output [7:0] D,
  output [7:0] D_a_2,
  output [7:0] JA,
  output JE,
  output [7:0] SP
);

  wire and_2_out, and_3_out, F, F_a, F_s, multiplexer_4_out, multiplexer_5_out, multiplexer_8_out, nor_1_out,
       or_1_out, or_2_out;
  wire [3:0] bitcount_1_out;
  wire [7:0] add_1_s, add_3_s, and_4_out, IN_b, multiplexer_2_out, multiplexer_3_out, multiplexer_6_out,
       multiplexer_9_out, multiplexer_10_out, multiplexer_11_out, nor_2_out, not_1_out, or_3_out, OUT_a,
       OUT_b, OUT_p, OUT_s, xor_1_out;
  wire [8:0] barrelshifter_1_out;
  wire [8:8] and_5_out;

  BitCount #(.Bits(8)) bitcount_1 (.in(D_a), .out(bitcount_1_out));
  Multiplexer #(.Bits(8)) multiplexer_1 (.sel(C_x[4]), .in_0(D_b), .in_1(IM), .out(IN_b));
  Multiplexer #(.Bits(8)) multiplexer_2 (.sel(C_x[4]), .in_0(D_b), .in_1({8{1'b0}}), .out(multiplexer_2_out));
  Multiplexer #(.Selector_Bits(2), .Bits(8)) multiplexer_3 (
    .sel(C_x[3:2]), .in_0(OUT_a), .in_1(OUT_b), .in_2(OUT_s), .in_3(OUT_p), .out(multiplexer_3_out));
  or or_1 (or_1_out, bitcount_1_out[0], bitcount_1_out[1], bitcount_1_out[2], bitcount_1_out[3], 1'b0);
  Multiplexer #(.Selector_Bits(2)) multiplexer_4 (
    .sel(C_x[1:0]), .in_0(1'b0), .in_1(1'b1), .in_2(F), .in_3(or_1_out), .out(multiplexer_4_out));
  Add #(.Bits(8)) add_1 (.a(multiplexer_2_out), .b(IM), .c_i(1'b0), .s(add_1_s));  // open: c_o
  Multiplexer #(.Selector_Bits(2)) multiplexer_5 (
    .sel(C_x[3:2]), .in_0(F_a), .in_1(F), .in_2(F_s), .in_3(F), .out(multiplexer_5_out));
  nor nor_1 (nor_1_out, C_x[5], C_x[6]);
  Register register_1 (.D(multiplexer_5_out), .C(\Φ ), .en(nor_1_out), .Q(F));
  and and_1 (JE, C_x[5], C_x[6], multiplexer_4_out);
  Multiplexer #(.Selector_Bits(2), .Bits(8)) multiplexer_6 (
    .sel(C_x[6:5]), .in_0(multiplexer_3_out), .in_1(add_1_s), .in_2(WA), .in_3({8{1'b0}}),
    .out(multiplexer_6_out));
  Multiplexer #(.Bits(8)) multiplexer_7 (.sel(C_x[3]), .in_0(add_1_s), .in_1(D_a), .out(JA));
  Register #(.Bits(8)) register_2 (.D(multiplexer_6_out), .C(\Φ ), .en(1'b1), .Q(D));
  and and_2 (and_2_out, C_x[2], C_x[3]);
  or or_2 (or_2_out, ~C_x[1], C_x[0]);  // Or
  assign not_1_out = ~IN_b;  // Not not_1, 8 bits wide
  Multiplexer #(.Selector_Bits(2)) multiplexer_8 (
    .sel(C_x[1:0]), .in_0(1'b0), .in_1(1'b1), .in_2(F), .in_3(F), .out(multiplexer_8_out));
  Multiplexer #(.Bits(8)) multiplexer_9 (.sel(C_x[1]), .in_0(add_3_s), .in_1(D_a), .out(multiplexer_9_out));
  and and_3 (and_3_out, and_2_out, or_2_out);
  Multiplexer #(.Bits(8)) multiplexer_10 (.sel(C_x[0]), .in_0(IN_b), .in_1(not_1_out), .out(multiplexer_10_out));
  Register #(.Bits(8)) register_3 (.D(D_a), .C(\Φ ), .en(1'b1), .Q(D_a_2));
  Register register_4 (.D(C_w), .C(\Φ ), .en(1'b1), .Q(C_w_2));
  Register #(.Bits(2)) register_5 (.D(C_m), .C(\Φ ), .en(1'b1), .Q(C_m_2));
  Register #(.Bits(2)) register_6 (.D(A_a), .C(\Φ ), .en(1'b1), .Q(A));
  Add #(.Bits(8)) add_2 (.a(D_a), .b(multiplexer_10_out), .c_i(multiplexer_8_out), .s(OUT_a), .c_o(F_a));
  Register #(.Bits(8)) register_7 (.D(multiplexer_9_out), .C(\Φ ), .en(and_3_out), .Q(SP));
  Multiplexer #(.Bits(8)) multiplexer_11 (.sel(C_x[0]), .in_0({8{1'b1}}), .in_1(8'h1), .out(multiplexer_11_out));
  Add #(.Bits(8)) add_3 (.a(SP), .b(multiplexer_11_out), .c_i(1'b0), .s(add_3_s));  // open: c_o
  assign and_4_out = D_a & IN_b;  // And and_4, 8 bits wide
  assign nor_2_out = ~(D_a | IN_b);  // NOr nor_2, 8 bits wide
  Multiplexer #(.Bits(8)) multiplexer_12 (.sel(C_x[0]), .in_0(SP), .in_1(add_3_s), .out(OUT_p));
  and and_5 (and_5_out[8], F, C_x[0]);
  assign or_3_out = D_a | IN_b;  // Or or_3, 8 bits wide
  assign xor_1_out = D_a ^ IN_b;  // XOr xor_1, 8 bits wide
  BarrelShifter #(.Bits(9), .direction("right")) barrelshifter_1 (
    .in({and_5_out[8], D_a}), .shift(4'b0001), .out(barrelshifter_1_out));
  Multiplexer #(.Selector_Bits(2), .Bits(8)) multiplexer_13 (
    .sel(C_x[1:0]), .in_0(and_4_out), .in_1(or_3_out), .in_2(nor_2_out), .in_3(xor_1_out), .out(OUT_b));
  Multiplexer #(.Bits(8)) multiplexer_14 (.sel(C_x[1]), .in_0(barrelshifter_1_out[7:0]), .in_1(IN_b), .out(OUT_s));
  Multiplexer multiplexer_15 (.sel(C_x[1]), .in_0(D_a[0]), .in_1(F), .out(F_s));

  // Other names for the same wires on the sheet: C_0[1:0] = C_x[1:0]; IN_a[7:0] = D_a

  // Notes on the sheet:
  //   WA: Program Word Address
  //   C_w: Write-Back Stage Control
  //   C_m: Memory Stage Control
  //   C_x: Execute Stage Control
  //   IM: Immediate
  //   A_a: Originating Register Address Port A
  //   D_a: Originating Register Data Port A
  //   D_b: Originating Register Data Port B
  //   C_w_2: Write-Back Stage Control
  //   C_m_2: Memory Stage Control
  //   Φ: Clock
  //   A: Combined Data Register Address
  //   D: Combined Data Output
  //   D_a_2: Originating Register Data Port A
  //   JA: Jump Address
  //   JE: Jump Enable
  //   SP: Stack Pointer Probe
endmodule
