// Digital circuit Fetch Stage.dig as structural Verilog
module Fetch_Stage (
  input  [7:0] JA,
  input  JE,
  input  [7:0] MD,
  input  \Φ ,
  output [7:0] MA,
  output [7:0] WA,
  output [7:0] WD
);

  wire [7:0] add_1_s, multiplexer_1_out;

  Multiplexer #(.Bits(8)) multiplexer_1 (.sel(JE), .in_0(add_1_s), .in_1(JA), .out(multiplexer_1_out));
  Register #(.Bits(8)) PC (.D(multiplexer_1_out), .C(\Φ ), .en(1'b1), .Q(MA));
  Add #(.Bits(8)) add_1 (.a(MA), .b({8{1'b0}}), .c_i(1'b1), .s(add_1_s));  // open: c_o
  Register #(.Bits(8)) register_1 (.D(add_1_s), .C(\Φ ), .en(1'b1), .Q(WA));
  Register #(.Bits(8)) register_2 (.D(MD), .C(\Φ ), .en(1'b1), .Q(WD));

  // Notes on the sheet:
  //   JA: Jump Address
  //   JE: Jump Enable
  //   MA: Memory Address
  //   WA: Program Word Address
  //   MD: Memory Data
  //   WD: Program Word Data
  //   Φ: Clock
endmodule
