// Digital circuit Forwarding Unit.dig as structural Verilog
module Forwarding_Unit (
  input  [1:0] A_a,
  input  [1:0] A_b,
  input  [7:0] D_a,
  input  [7:0] D_b,
  input  [7:0] D_m,
  input  [1:0] A_m,
  input  W_m,
  input  [7:0] D_w,
  input  [1:0] A_w,
  input  W_w,
  output [7:0] D_a_2,
  output [7:0] D_B_2,
  output F_b,
  output F_a
);

  wire and_1_out, and_2_out, and_3_out, and_4_out, comparator_1_eq, comparator_2_eq, comparator_3_eq,
       comparator_4_eq, nor_1_out;
  wire [7:0] multiplexer_1_out, multiplexer_2_out;

  Comparator #(.Bits(2)) comparator_1 (.a(A_a), .b(A_w), .eq(comparator_1_eq));  // open: gt, lt
  Comparator #(.Bits(2)) comparator_2 (.a(A_a), .b(A_m), .eq(comparator_2_eq));  // open: gt, lt
  Comparator #(.Bits(2)) comparator_3 (.a(A_b), .b(A_m), .eq(comparator_3_eq));  // open: gt, lt
  Comparator #(.Bits(2)) comparator_4 (.a(A_b), .b(A_w), .eq(comparator_4_eq));  // open: gt, lt
  and and_1 (and_1_out, W_w, comparator_1_eq);
  and and_2 (and_2_out, W_m, comparator_2_eq);
  and and_3 (and_3_out, comparator_3_eq, W_m);
  and and_4 (and_4_out, comparator_4_eq, W_w);
  or or_1 (F_a, and_1_out, and_2_out);
  nor nor_1 (nor_1_out, and_3_out, and_4_out);
  Multiplexer #(.Bits(8)) multiplexer_1 (.sel(and_2_out), .in_0(D_w), .in_1(D_m), .out(multiplexer_1_out));
  Multiplexer #(.Bits(8)) multiplexer_2 (.sel(and_3_out), .in_0(D_w), .in_1(D_m), .out(multiplexer_2_out));
  Multiplexer #(.Bits(8)) multiplexer_3 (.sel(F_a), .in_0(D_a), .in_1(multiplexer_1_out), .out(D_a_2));
  Multiplexer #(.Bits(8)) multiplexer_4 (.sel(nor_1_out), .in_0(multiplexer_2_out), .in_1(D_b), .out(D_B_2));
  not not_1 (F_b, nor_1_out);

  // Notes on the sheet:
  //   A_a: Read Register Address Port A
  //   A_b: Read Register Address Port B
  //   D_a: Read Register Data Port A
  //   D_b: Read Register Data Port B
  //   D_a_2: Fixed Read Register Data Port A
  //   D_B_2: Fixed Read Register Data Port B
  //   D_m: Register Data On Memory Stage
  //   A_m: Register Address On Memory Stage
  //   W_m: Register Write-Back Enable On Memory Stage
  //   D_w: Register Data On Write-Back Stage
  //   A_w: Register Address On Write-Back Stage
  //   W_w: Register Write-Back Enable On Write-Back Stage
  //   F_b: Forward B Enable Probe
  //   F_a: Forward A Enable Probe
endmodule
