// Digital circuit Memory Stage.dig as structural Verilog
module Memory_Stage (
  input  C_w_2,
  input  [1:0] C_m,
  input  [1:0] A_2,
  input  [7:0] D_2,
  input  [7:0] D_a,
  input  \Φ ,
  input  [7:0] PA,
  output C_w,
  output [1:0] A,
  output [7:0] D,
  output [7:0] PD
);

  wire [7:0] multiplexer_1_out, ramdualaccess_1_d1;

  Register register_1 (.D(C_w_2), .C(\Φ ), .en(1'b1), .Q(C_w));
  Register #(.Bits(2)) register_2 (.D(A_2), .C(\Φ ), .en(1'b1), .Q(A));
  RAMDualAccess #(.AddrBits(8), .isProgramMemory("true"), .Bits(8)) ramdualaccess_1 (
    .str(C_m[0]), .C(\Φ ), .ld(1'b1), .A1(D_2), .Din1(D_a), .A2(PA), .D1(ramdualaccess_1_d1), .D2(PD));
  Multiplexer #(.Bits(8)) multiplexer_1 (.sel(C_m[1]), .in_0(D_2), .in_1(ramdualaccess_1_d1), .out(multiplexer_1_out));
  Register #(.Bits(8)) register_3 (.D(multiplexer_1_out), .C(\Φ ), .en(1'b1), .Q(D));

  // Notes on the sheet:
  //   C_w: Write-Back Stage Control
  //   A: Combined Data Register Address
  //   D: Combined Data Output
  //   C_w_2: Write-Back Stage Control
  //   C_m: Memory Stage Control
  //   A_2: Combined Data Register Address
  //   D_2: Combined Data Input
  //   D_a: Originating Register Data Port A
  //   Φ: Clock
  //   PA: Program Address
  //   PD: Program Data
endmodule
