// Digital circuit Regfile.dig as structural Verilog
module Regfile (
  input  [1:0] RA_a,
  input  [1:0] RA_b,
  input  [1:0] WA,
  input  [7:0] WD,
  input  WE,
  input  \Φ ,
  output [7:0] RD_a,
  output [7:0] RD_b,
  output [7:0] R_0,
  output [7:0] R_1,
  output [7:0] R_2,
  output [7:0] R_3
);

  wire and_1_out, and_2_out, comparator_1_eq, comparator_2_eq, demultiplexer_1_out_0, demultiplexer_1_out_1,
       demultiplexer_1_out_2, demultiplexer_1_out_3;
  wire [7:0] multiplexer_1_out, multiplexer_2_out;

  Demultiplexer #(.Selector_Bits(2)) demultiplexer_1 (
    .sel(WA), .in(WE), .out_0(demultiplexer_1_out_0), .out_1(demultiplexer_1_out_1),
    .out_2(demultiplexer_1_out_2), .out_3(demultiplexer_1_out_3));
  Register #(.Bits(8)) register_1 (.D(WD), .C(\Φ ), .en(demultiplexer_1_out_0), .Q(R_0));
  Register #(.Bits(8)) register_2 (.D(WD), .C(\Φ ), .en(demultiplexer_1_out_1), .Q(R_1));
  Register #(.Bits(8)) register_3 (.D(WD), .C(\Φ ), .en(demultiplexer_1_out_2), .Q(R_2));
  Register #(.Bits(8)) register_4 (.D(WD), .C(\Φ ), .en(demultiplexer_1_out_3), .Q(R_3));
  Multiplexer #(.Selector_Bits(2), .Bits(8)) multiplexer_1 (
    .sel(RA_b), .in_0(R_0), .in_1(R_1), .in_2(R_2), .in_3(R_3), .out(multiplexer_1_out));
  Multiplexer #(.Selector_Bits(2), .Bits(8)) multiplexer_2 (
    .sel(RA_a), .in_0(R_0), .in_1(R_1), .in_2(R_2), .in_3(R_3), .out(multiplexer_2_out));
  Comparator #(.Bits(2)) comparator_1 (.a(RA_b), .b(WA), .eq(comparator_1_eq));  // open: gt, lt
  Comparator #(.Bits(2)) comparator_2 (.a(RA_a), .b(WA), .eq(comparator_2_eq));  // open: gt, lt
  Multiplexer #(.Bits(8)) multiplexer_3 (.sel(and_2_out), .in_0(multiplexer_2_out), .in_1(WD), .out(RD_a));
  Multiplexer #(.Bits(8)) multiplexer_4 (.sel(and_1_out), .in_0(multiplexer_1_out), .in_1(WD), .out(RD_b));
  and and_1 (and_1_out, WE, comparator_1_eq);
  and and_2 (and_2_out, comparator_2_eq, WE);

  // Notes on the sheet:
  //   RD_a: Read Data Port A
  //   RA_a: Read Address Port A
  //   RA_b: Read Address Port B
  //   WA: Write Address
  //   RD_b: Read Data Port B
  //   WD: Write Data
  //   WE: Write Enable
  //   Φ: Clock
  //   R_0: Register 1 Probe
  //   R_1: Register 1 Probe
  //   R_2: Register 2 Probe
  //   R_3: Register 3 Probe
endmodule
